// Logisim project RISK_V22_l341.circ as structural Verilog: 67 circuits, main circuit main
module main (
  input  RESET,
  input  [31:0] in_2,
  input  in_3
);

  wire ALU_G, ALU_OP_0, ALU_OP_1, ALU_SRC, and_4_out, Branch, button_1_out, CLK, comparator_1_eq, CPU_BUSY,
       CPU_CLK_SRC, CU_RST, decoder_1_out0, decoder_1_out1, decoder_1_out2, hlt, MEM_LOAD, MEM_STORE,
       nIMM_RTB_G, not_2_out, not_3_out, not_4_out, not_8_out, not_9_out, nPC_RTB_G, nREG_RTB_G, or_1_out,
       PC_SRC_0, PC_SRC_1, PCE, RF_LOAD, RF_STORE, RST, RTB_SEL_0, RTB_SEL_1, SH_LATCH, SH_LOAD, SH_RTB_EN,
       shifter_v20_1_cpu_busy, TAKE_BRANCH;
  wire [2:0] control_unit_v20_1_out_6, IMM_GEN_CTR_0_3;
  wire [7:0] rom_1_p2, rom_1_p3, rom_1_p4, rom_1_p5;
  wire [18:0] instruction_memory_v1_1_out_6;
  wire [23:13] control_unit_v20_1_ins;
  wire [31:0] ALU, controlled_buffer_1_out, counter_1_q, counter_2_q, data_memory_v9_1_out_7,
       imm_generator_v4_1_out, INS, LTCH, multiplexer_1_out, OUT, PREP, PULS, REG, register_1_q,
       register_file_v20_1_rb_1;

  Pull_Resistor pull_resistor_1 (.node(hlt));
  Button button_1 (.out(button_1_out));
  // NOT_Gate not_1 is placed but not wired
  Clock clock_1 (.out(CPU_CLK_SRC));
  and and_1 (CLK, CPU_CLK_SRC, not_2_out);
  not not_2 (not_2_out, hlt);
  or or_1 (or_1_out, button_1_out, RESET);
  Comparator #(.width(32)) comparator_1 (.a(in_2), .b(PULS), .eq(comparator_1_eq));  // open: gt, lt
  and and_2 (hlt, comparator_1_eq, in_3);
  not not_3 (not_3_out, CLK);
  D_Flip_Flop d_ff_1 (.clk(not_3_out), .D(or_1_out), .Q(RST));  // open: Qn, preset, reset
  assign controlled_buffer_1_out = nPC_RTB_G ? OUT : 32'bz;  // Controlled_Buffer controlled_buffer_1
  D_Flip_Flop d_ff_2 (.clk(CLK), .D(RST), .Q(CU_RST));  // open: Qn, preset, reset
  Program_Counter_v20 program_counter_v20_1 (
    .X(LTCH), .OUT(PREP), .SRC1(PC_SRC_1), .CLK(CLK), .T_BRCH(TAKE_BRANCH), .SRC0(PC_SRC_0), .PCE(PCE),
    .BRCH(Branch), .RST(RST), .Y(imm_generator_v4_1_out), .OUT_in(controlled_buffer_1_out));
  not not_4 (not_4_out, nPC_RTB_G);
  assign OUT = not_4_out ? PREP : 32'bz;  // Controlled_Buffer controlled_buffer_2
  // Probe on PULS
  // Probe on INS
  // Probe on PREP
  // Probe on LTCH
  // Probe on REG
  // Probe on ALU
  // Probe on OUT
  LED led_1 (.in(CLK));
  Instruction_memory_v1 instruction_memory_v1_1 (
    .out_6(instruction_memory_v1_1_out_6), .out_7(INS), .in_2(rom_1_p2), .in_3(rom_1_p3), .in_4(rom_1_p4),
    .in_5(rom_1_p5), .in({LTCH[31:2], 2'b00}));
  // ROM #(.addrWidth(19), .line("quad")) rom_1: pin names not known; wires that end beside it: instruction_memory_v1_1_out_6, rom_1_p2, rom_1_p3, rom_1_p4, rom_1_p5
  Imm_generator_v4 imm_generator_v4_1 (.Out(imm_generator_v4_1_out), .Sel(IMM_GEN_CTR_0_3), .Ins(INS));
  Counter #(.max('hffffffff), .width(32)) counter_1 (
    .Q(counter_1_q), .clk(CLK), .clr(RST));  // open: load, D, count, carry
  Counter #(.max('hffffffff), .trigger("falling"), .width(32)) counter_2 (
    .Q(counter_2_q), .clk(CLK), .clr(RST));  // open: load, D, count, carry
  // Probe on imm_generator_v4_1_out
  Adder #(.width(32)) adder_1 (.a(counter_1_q), .b(counter_2_q), .out(PULS));  // open: cin, cout
  Decoder #(.select(2)) decoder_1 (
    .out0(decoder_1_out0), .out1(decoder_1_out1), .out2(decoder_1_out2), .sel({RTB_SEL_1, RTB_SEL_0}),
    .en(SH_RTB_EN));  // open: out3
  Control_unit_v20 control_unit_v20_1 (
    .INS({control_unit_v20_1_ins[23:21], IMM_GEN_CTR_0_3[2], MEM_LOAD, RF_LOAD, SH_LATCH, SH_LOAD, control_unit_v20_1_ins[15], ALU_SRC, control_unit_v20_1_ins[13], PCE, ALU_G, RF_STORE, IMM_GEN_CTR_0_3[1:0], PC_SRC_1, TAKE_BRANCH, ALU_OP_1, RTB_SEL_1, PC_SRC_0, RTB_SEL_0, MEM_STORE, ALU_OP_0}),
    .out_6(control_unit_v20_1_out_6), .CLK(CLK), .CPU_BUSY(CPU_BUSY), .RST(CU_RST), .OP_CODE(INS[6:0]));
  not not_5 (nREG_RTB_G, decoder_1_out0);
  not not_6 (nIMM_RTB_G, decoder_1_out1);
  not not_7 (nPC_RTB_G, decoder_1_out2);
  // Probe on control_unit_v20_1_out_6
  Register_file_v20 register_file_v20_1 (
    .RB_0(REG), .RB_1(register_file_v20_1_rb_1), .Store(RF_STORE), .Clock(CLK), .Load(RF_LOAD),
    .read_register_1(INS[19:15]), .read_register_2(INS[24:20]), .write_data(OUT), .write_register(INS[11:7]));
  Multiplexer #(.enable("false"), .width(32)) multiplexer_1 (
    .in0(register_file_v20_1_rb_1), .in1(imm_generator_v4_1_out), .out(multiplexer_1_out), .sel(ALU_SRC));
  ALU_v20 alu_v20_1 (
    .Branch(Branch), .out_6(ALU), .Y(multiplexer_1_out), .I(INS[30]), .Funct3(INS[14:12]), .X(REG),
    .ALU_op({ALU_OP_1, ALU_OP_0}));
  Shifter_v20 shifter_v20_1 (
    .Out(OUT), .OUT_EN(SH_RTB_EN), .CPU_BUSY(shifter_v20_1_cpu_busy), .I(INS[30]), .Funct3(INS[14:12]),
    .RS2(multiplexer_1_out[4:0]), .CLK(CLK), .SH_LOAD(SH_LATCH), .in_6(SH_LOAD), .RF_STORE(RF_STORE),
    .Data_IN(REG), .PCE(PCE), .RST(RST));
  LED led_2 (.in(shifter_v20_1_cpu_busy));
  and and_3 (CPU_BUSY, ~RF_STORE, shifter_v20_1_cpu_busy);  // AND_Gate
  Data_memory_v9 data_memory_v9_1 (
    .out_7(data_memory_v9_1_out_7), .Load(MEM_LOAD), .Store(MEM_STORE), .Clock(CLK), .Funct3(INS[14:12]),
    .Data(register_file_v20_1_rb_1), .Adress(ALU));  // open: out_9, Exception
  Register #(.width(32)) register_1 (
    .D(data_memory_v9_1_out_7), .en(1'b1), .Q(register_1_q), .clk(and_4_out));  // open: clr
  and and_4 (and_4_out, CLK, ~RF_STORE);  // AND_Gate
  assign data_memory_v9_1_out_7 = ALU_G ? ALU : 32'bz;  // Controlled_Buffer controlled_buffer_3
  Pull_Resistor pull_resistor_2 (.node(data_memory_v9_1_out_7));
  assign OUT = not_8_out ? register_1_q : 32'bz;  // Controlled_Buffer controlled_buffer_4
  not not_8 (not_8_out, nREG_RTB_G);
  not not_9 (not_9_out, nIMM_RTB_G);
  assign OUT = not_9_out ? imm_generator_v4_1_out : 32'bz;  // Controlled_Buffer controlled_buffer_5
  // NOT_Gate not_10 is placed but not wired

  // Notes on the sheet:
  //   Simulation
  //   CLOCK
  //   Halt at pulse
  //   Program Counter
  //   Diagnostics
  //   Pulse Count
  //   Instruction
  //   Prepared
  //   Latched
  //   REG
  //   ALU
  //   Out
  //   Instruction Memory
  //   contents of rom_1 (hex, n*v repeats v):
  //   0 8 1 37 ff c1 1 13 0 c0 0 ef 0 40 0 6f 0 0 0 6f fe 1 1 13 0 11 2e 23 0 81 2c 23 2 1 4 13 80 0 7 b7
  //   0 30 7 13 0 e7 83 23 80 0 7 b7 0 40 7 13 0 e7 83 a3 0 10 5 13 16 40 0 ef 10 40 0 ef 0 40 7 93 fe f4
  //   26 23 2 0 0 6f fe c4 26 3 3 20 5 93 6 40 5 13 4c c0 0 ef fe c4 27 83 0 27 87 93 fe f4 26 23 fe c4 27
  //   3 2 70 7 93 fc e7 de e3 0 0 0 6f fd 1 1 13 2 81 26 23 3 1 4 13 fc a4 2e 23 0 5 87 93 fc f4 d a3 fd
  //   c4 27 3 40 0 7 b7 0 f7 7 b3 fe f4 26 23 fe c4 27 83 fd b4 47 3 0 e7 80 23 0 0 0 13 2 c1 24 3 3 1 1
  //   13 0 0 80 67 fd 1 1 13 2 81 26 23 3 1 4 13 fc a4 2e 23 fc b4 2c 23 fd c4 27 3 40 0 7 b7 0 f7 7 b3 fe
  //   f4 26 23 fe c4 27 83 fd 84 27 3 0 e7 a0 23 0 0 0 13 2 c1 24 3 3 1 1 13 0 0 80 67 fe 1 1 13 0 81 2e
  //   23 2 1 4 13 fe 4 26 23 1 0 0 6f fe c4 27 83 0 17 87 93 fe f4 26 23 fe c4 27 3 0 0 27 b7 70 f7 87 93
  //   fe e7 d4 e3 0 0 0 13 0 0 0 13 1 c1 24 3 2 1 1 13 0 0 80 67 fe 1 1 13 0 11 2e 23 0 81 2c 23 2 1 4 13
  //   fe 4 26 23 2 0 0 6f fe c4 27 83 0 0 5 93 0 7 85 13 f5 9f f0 ef fe c4 27 83 0 47 87 93 fe f4 26 23 fe
  //   c4 27 3 0 0 17 b7 35 57 87 93 fc e7 dc e3 0 0 0 13 0 0 0 13 1 c1 20 83 1 81 24 3 2 1 1 13 0 0 80 67
  //   fe 1 1 13 0 81 2e 23 2 1 4 13 0 5 7 93 fe f4 7 a3 fe f4 47 83 0 7 88 63 fe f4 47 3 0 10 7 93 0 f7 18
  //   63 80 0 7 b7 fe f4 47 3 0 e7 80 a3 0 0 0 13 1 c1 24 3 2 1 1 13 0 0 80 67 fd 1 1 13 2 81 26 23 3 1 4
  //   13 fc a4 2e 23 fc b4 2c 23 fd c4 27 83 41 f7 d7 13 1 f7 77 13 0 f7 7 b3 40 57 d7 93 fe f4 26 23 fe
  //   c4 27 83 0 27 97 13 40 0 7 b7 0 f7 7 33 fd 84 27 83 0 37 97 93 0 27 97 93 0 f7 7 b3 fe f4 24 23 fe
  //   84 27 83 0 7 a7 83 fe f4 22 23 fd c4 27 3 41 f7 57 93 1 b7 d7 93 0 f7 7 33 1 f7 77 13 40 f7 7 b3 0 7
  //   87 13 0 10 7 93 0 e7 97 b3 fe 44 27 3 0 f7 67 b3 fe f4 22 23 fe 84 27 83 fe 44 27 3 0 e7 a0 23 0 0 0
  //   13 2 c1 24 3 3 1 1 13 0 0 80 67 fd 1 1 13 2 81 26 23 3 1 4 13 fc a4 2e 23 fc b4 2c 23 fd c4 27 83 41
  //   f7 d7 13 1 f7 77 13 0 f7 7 b3 40 57 d7 93 fe f4 26 23 fe c4 27 83 0 27 97 13 40 0 7 b7 0 f7 7 33 fd
  //   84 27 83 0 37 97 93 0 27 97 93 0 f7 7 b3 fe f4 24 23 fe 84 27 83 0 7 a7 83 fe f4 22 23 fd c4 27 3 41
  //   f7 57 93 1 b7 d7 93 0 f7 7 33 1 f7 77 13 40 f7 7 b3 0 7 87 13 0 10 7 93 0 e7 97 b3 ff f7 c7 93 fe 44
  //   27 3 0 f7 77 b3 fe f4 22 23 fe 84 27 83 fe 44 27 3 0 e7 a0 23 0 0 0 13 2 c1 24 3 3 1 1 13 0 0 80 67
  //   fd 1 1 13 2 81 26 23 3 1 4 13 fc a4 2e 23 fc b4 2c 23 fc c4 2a 23 fd c4 27 83 fe f4 24 23 fe 84 27 3
  //   40 0 7 b7 0 f7 7 33 fd 84 27 83 0 87 97 93 0 f7 7 b3 fe f4 22 23 fe 4 26 23 3 c0 0 6f fe c4 27 83 0
  //   57 97 13 fe 44 27 83 0 f7 7 b3 fe f4 20 23 fe c4 27 83 fd 44 27 3 0 f7 7 b3 0 7 c7 3 fe 4 27 83 0 e7
  //   80 23 fe c4 27 83 0 17 87 93 fe f4 26 23 fe c4 27 3 0 70 7 93 fc e7 d0 e3 0 0 0 13 0 0 0 13 2 c1 24
  //   3 3 1 1 13 0 0 80 67 fe 1 1 13 0 11 2e 23 0 81 2c 23 2 1 4 13 fe a4 26 23 fe b4 24 23 fe c4 22 23 fe
  //   d4 20 23 fe c4 27 3 fe 44 27 83 0 f7 6 b3 fe 84 27 3 fe 4 27 83 0 f7 7 b3 0 7 85 93 0 6 85 13 dd 1f
  //   f0 ef fe c4 27 3 fe 44 27 83 40 f7 6 b3 fe 84 27 3 fe 4 27 83 0 f7 7 b3 0 7 85 93 0 6 85 13 da df f0
  //   ef fe c4 27 3 fe 44 27 83 0 f7 6 b3 fe 84 27 3 fe 4 27 83 40 f7 7 b3 0 7 85 93 0 6 85 13 d8 9f f0 ef
  //   fe c4 27 3 fe 44 27 83 40 f7 6 b3 fe 84 27 3 fe 4 27 83 40 f7 7 b3 0 7 85 93 0 6 85 13 d6 5f f0 ef
  //   fe c4 27 3 fe 4 27 83 0 f7 6 b3 fe 84 27 3 fe 44 27 83 0 f7 7 b3 0 7 85 93 0 6 85 13 d4 1f f0 ef fe
  //   c4 27 3 fe 4 27 83 40 f7 6 b3 fe 84 27 3 fe 44 27 83 0 f7 7 b3 0 7 85 93 0 6 85 13 d1 df f0 ef fe c4
  //   27 3 fe 4 27 83 0 f7 6 b3 fe 84 27 3 fe 44 27 83 40 f7 7 b3 0 7 85 93 0 6 85 13 cf 9f f0 ef fe c4 27
  //   3 fe 4 27 83 40 f7 6 b3 fe 84 27 3 fe 44 27 83 40 f7 7 b3 0 7 85 93 0 6 85 13 cd 5f f0 ef 0 0 0 13 1
  //   c1 20 83 1 81 24 3 2 1 1 13 0 0 80 67 fd 1 1 13 2 11 26 23 2 81 24 23 3 1 4 13 fc a4 2e 23 fc b4 2c
  //   23 fc c4 2a 23 fe 4 26 23 fd 44 27 83 fe f4 24 23 fd 44 27 83 0 17 97 93 0 30 7 13 40 f7 7 b3 fe f4
  //   22 23 fe 84 26 83 fe c4 26 3 fd 84 25 83 fd c4 25 3 e6 1f f0 ef 7 40 0 6f fe c4 27 83 0 17 87 93 fe
  //   f4 26 23 fe 44 27 83 2 f0 5a 63 fe 84 27 83 ff f7 87 93 fe f4 24 23 fe c4 27 3 fe 84 27 83 40 f7 7
  //   b3 0 27 97 13 fe 44 27 83 0 f7 7 b3 0 a7 87 93 fe f4 22 23 1 c0 0 6f fe c4 27 83 0 27 97 1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
  //   STORED PROGRAM
  //   Utilities
  //   Control Unit
  //   uCounter
  //   Shifter
  //   Imm Gen Contol [2]
  //   ALU_OP_0 (ALU operation code 0)
  //   ALU_OP_1 (ALU operation code 1)
  //   TAKE_BRANCH
  //   RF_STORE (Register file store)
  //   PCE (Program counter enable)
  //   RESERVED_0 (Not used)
  //   ALU_SRC (ALU source select )
  //   RESERVED_1 (Not used)
  //   SH_LOAD (Shifter load)
  //   SH_LATCH (Shifter latch)
  //   RF_LOAD (Register file load)
  //   MEM_STORE (Store to data memory/RAM)
  //   RTB_SEL_0 (RTB - return bus select 0)
  //   PC_SRC_0 (Program counter source select 0)
  //   RTB_SEL_1 (RTB - return bus select 1)
  //   PC_SRC_1 (Program counter source select 1)
  //   IMM_GEN_CTR_0 (Immediate generator control 0)
  //   IMM_GEN_CTR_1 (Immediate generator control 1)
  //   ALU_G (ALU gate - enables data memory bypass)
  //   MEM_LOAD (Load from data memory/RAM)
  //   IMM_GEN_CTR_2 (Immediate generator control 2)
  //   Data memory bypass
  //   RTB 
  //   (Return BUS - writeback)
endmodule

module CPU_v18 (
  input  [31:0] in_1,
  input  in_2,
  input  [30:0] in_3,
  input  in_4,
  input  in_5,
  input  in_6,
  input  in_7,
  input  in_8,
  output [31:0] inst_adr
);

  wire a_err, ALU_Control, ALU_Control_1, and_2_out, and_3_out, and_4_out, and_8_out, branch, button_2_out,
       button_3_out, CLK, comparator_1_eq, comparator_2_eq, comparator_3_eq, comparator_4_eq,
       comparator_5_eq, comparator_6_eq, controlled_buffer_2_out, Counter_reset, CPU_Busy, d_err, d_ff_1_qn,
       d_ff_3_q, GPU_c, gpu_v5_1_p3, gpu_v5_1_p4, hlt, i, Im_err, Inter, k, Main_Clock, Master_Reset,
       Memory_load, Memory_store, nor_1_out, not_1_out, not_2_out, or_1_out, or_2_out, or_3_out, or_4_out,
       or_6_out, or_7_out, or_9_out, or_10_out, PC_Source, PC_Source_1, PLS, Program_counter_enable,
       Register_file_load, Register_file_store, s_err, Shifter_latch, Shifter_load, shifter_v6_1_out_9,
       shifter_v6_1_out_10, Store_to_register_0, Store_to_register_imm_0, Store_to_register_imm_1,
       Take_branch, uCounter_reset, XL, XX;
  wire [1:0] ALU_Source;
  wire [2:0] alu_control_v3_1_aluop, counter_7_q, Imm_Gen_Control;
  wire [4:0] Rd, Rs1, Rs2;
  wire [6:0] rom_2_data;
  wire [7:0] counter_1_q, counter_2_q, counter_3_q, counter_4_q, rom_1_p2, rom_1_p3, rom_1_p4, rom_1_p5;
  wire [7:5] E2_data;
  wire [18:0] rom_1_p1;
  wire [30:0] divider_1_out;
  wire [31:0] alu, controlled_buffer_1_out, controlled_buffer_3_out, controlled_buffer_4_out,
       controlled_buffer_5_out, controlled_buffer_6_out, controlled_buffer_7_out, controlled_buffer_8_out,
       controlled_buffer_9_out, counter_5_q, counter_6_q, data_memory_v9_1_out_7, imm_generator_v4_1_out,
       ins, multiplexer_2_out, out, pc_adder_v2_1_out_5, prep, pull_resistor_7_node, PulseC, \reg ,
       register_1_q, register_file_v6_1_read_register_1_2, register_file_v6_1_read_register_2_2;

  // Probe on PulseC
  // Probe on ins
  // Probe on prep
  // Probe on inst_adr
  // Probe on \reg 
  // Probe on alu
  // Probe on out
  LED led_1 (.in(CLK));
  Button button_1 (.out(Master_Reset));
  LED led_2 (.in(PLS));
  Comparator #(.width(32)) comparator_1 (.a(in_1), .b(PulseC), .eq(comparator_1_eq));  // open: gt, lt
  and and_1 (hlt, comparator_1_eq, in_2);
  Button button_2 (.out(button_2_out));
  and and_2 (and_2_out, ~Take_branch, PC_Source);  // AND_Gate
  or or_1 (or_1_out, and_2_out, and_3_out);
  and and_3 (and_3_out, branch, Take_branch);
  or or_2 (or_2_out, and_3_out, Master_Reset, Program_counter_enable);
  Counter counter_1 (.Q(counter_1_q), .clk(Im_err), .clr(Master_Reset));  // open: load, D, count, carry
  Comparator comparator_2 (.a(counter_1_q), .b({8{1'b0}}), .eq(comparator_2_eq));  // open: gt, lt
  Counter counter_2 (.Q(counter_2_q), .clk(a_err), .clr(Master_Reset));  // open: load, D, count, carry
  Comparator comparator_3 (.a(counter_2_q), .b({8{1'b0}}), .eq(comparator_3_eq));  // open: gt, lt
  Comparator comparator_4 (.a({8{1'b0}}), .b(counter_3_q), .eq(comparator_4_eq));  // open: gt, lt
  Counter counter_3 (.Q(counter_3_q), .clk(s_err), .clr(Master_Reset));  // open: load, D, count, carry
  Comparator comparator_5 (.a({8{1'b0}}), .b(counter_4_q), .eq(comparator_5_eq));  // open: gt, lt
  Counter counter_4 (.Q(counter_4_q), .clk(d_err), .clr(Master_Reset));  // open: load, D, count, carry
  Program_Counter_v1 program_counter_v1_1 (
    .out(inst_adr), .Enable(or_2_out), .Clock(CLK), .in(prep), .Clear(button_2_out));
  // Probe on counter_1_q
  // Probe on counter_2_q
  // Probe on counter_3_q
  // Probe on counter_4_q
  nand nand_1 (k, comparator_2_eq, comparator_3_eq, comparator_4_eq, comparator_5_eq);
  Counter #(.max('hffffffff), .width(32)) counter_5 (
    .Q(counter_5_q), .clk(CLK), .clr(Master_Reset));  // open: load, D, count, carry
  Adder #(.width(32)) adder_1 (.a(counter_5_q), .b(counter_6_q), .out(PulseC));  // open: cin, cout
  Counter #(.max('hffffffff), .trigger("falling"), .width(32)) counter_6 (
    .Q(counter_6_q), .clk(CLK), .clr(Master_Reset));  // open: load, D, count, carry
  // ROM #(.addrWidth(19), .line("quad")) rom_1: pin names not known; wires that end beside it: rom_1_p1, rom_1_p2, rom_1_p3, rom_1_p4, rom_1_p5
  Instruction_memory_v1 instruction_memory_v1_1 (
    .out_6(rom_1_p1), .out_7(ins), .in_2(rom_1_p2), .in_3(rom_1_p3), .in_4(rom_1_p4), .in_5(rom_1_p5),
    .in(inst_adr));
  assign controlled_buffer_1_out = in_7 ? PulseC : 32'bz;  // Controlled_Buffer controlled_buffer_1
  assign controlled_buffer_2_out = in_8 ? CLK : 1'bz;  // Controlled_Buffer controlled_buffer_2
  assign controlled_buffer_3_out = in_7 ? ins : 32'bz;  // Controlled_Buffer controlled_buffer_3
  assign controlled_buffer_4_out = in_7 ? prep : 32'bz;  // Controlled_Buffer controlled_buffer_4
  assign controlled_buffer_5_out = in_7 ? inst_adr : 32'bz;  // Controlled_Buffer controlled_buffer_5
  assign controlled_buffer_6_out = in_7 ? alu : 32'bz;  // Controlled_Buffer controlled_buffer_6
  assign controlled_buffer_7_out = in_7 ? out : 32'bz;  // Controlled_Buffer controlled_buffer_7
  assign controlled_buffer_8_out = in_7 ? \reg  : 32'bz;  // Controlled_Buffer controlled_buffer_8
  PC_Adder_v2 pc_adder_v2_1 (
    .out_5(pc_adder_v2_1_out_5), .Y(imm_generator_v4_1_out), .X(inst_adr), .Mode(or_1_out), .Rst(Master_Reset));
  Pull_Resistor pull_resistor_1 (.node(controlled_buffer_2_out));
  RAM #(.addrWidth(24), .dataWidth(32)) ram_1 (
    .addr(controlled_buffer_1_out[23:0]), .we(1'b1), .clk(controlled_buffer_2_out),
    .din(controlled_buffer_3_out));  // open: dout
  RAM #(.addrWidth(24), .dataWidth(32)) ram_2 (
    .addr(controlled_buffer_1_out[23:0]), .we(1'b1), .clk(controlled_buffer_2_out),
    .din(controlled_buffer_4_out));  // open: dout
  RAM #(.addrWidth(24), .dataWidth(32)) ram_3 (
    .addr(controlled_buffer_1_out[23:0]), .we(1'b1), .clk(controlled_buffer_2_out),
    .din(controlled_buffer_5_out));  // open: dout
  RAM #(.addrWidth(24), .dataWidth(32)) ram_4 (
    .addr(controlled_buffer_1_out[23:0]), .we(1'b1), .clk(controlled_buffer_2_out),
    .din(controlled_buffer_6_out));  // open: dout
  RAM #(.addrWidth(24), .dataWidth(32)) ram_5 (
    .addr(controlled_buffer_1_out[23:0]), .we(1'b1), .clk(controlled_buffer_2_out),
    .din(controlled_buffer_7_out));  // open: dout
  RAM #(.addrWidth(24), .dataWidth(32)) ram_6 (
    .addr(controlled_buffer_1_out[23:0]), .we(1'b1), .clk(controlled_buffer_2_out),
    .din(controlled_buffer_8_out));  // open: dout
  Multiplexer #(.enable("false"), .width(32)) multiplexer_1 (
    .in0(pc_adder_v2_1_out_5), .in1(out), .out(prep), .sel(PC_Source_1));
  // Probe on divider_1_out
  Divider #(.width(31)) divider_1 (.a(inst_adr[31:1]), .b(31'h2), .out(divider_1_out));  // open: upper, rem
  // Probe on controlled_buffer_1_out[23:0]
  Comparator #(.width(31)) comparator_6 (.a(divider_1_out), .b(in_3), .eq(comparator_6_eq));  // open: gt, lt
  assign {controlled_buffer_9_out[31:25], Rs2, Rs1, controlled_buffer_9_out[14:12], Rd, controlled_buffer_9_out[6:0]} = in_6 ? ins : 32'bz;  // Controlled_Buffer controlled_buffer_9
  Pull_Resistor pull_resistor_2 (.node({controlled_buffer_9_out[31:25], Rs2, Rs1, controlled_buffer_9_out[14:12], Rd, controlled_buffer_9_out[6:0]}));
  Imm_generator_v4 imm_generator_v4_1 (.Out(imm_generator_v4_1_out), .Sel(Imm_Gen_Control), .Ins(ins));
  Clock clock_1 (.out(PLS));
  or or_3 (or_3_out, PLS, button_3_out);
  Button button_3 (.out(button_3_out));
  and and_4 (and_4_out, or_4_out, ~hlt);  // AND_Gate
  or or_4 (or_4_out, ~in_4, ~comparator_6_eq);  // OR_Gate
  // OR_Gate or_5 is placed but not wired
  // Probe on ins
  and and_5 (Main_Clock, or_3_out, and_4_out);
  Pull_Resistor pull_resistor_3 (.node(hlt));
  ROM #(.addrWidth(11), .dataWidth(7)) rom_2 (
    .addr({controlled_buffer_9_out[30], controlled_buffer_9_out[14:12], controlled_buffer_9_out[6:0]}),
    .data(rom_2_data));
  RAM #(.addrWidth(24), .dataWidth(32), .trigger("falling")) ram_7 (
    .addr(controlled_buffer_1_out[23:0]), .we(1'b1), .clk(controlled_buffer_2_out),
    .din(controlled_buffer_3_out));  // open: dout
  RAM #(.addrWidth(24), .dataWidth(32), .trigger("falling")) ram_8 (
    .addr(controlled_buffer_1_out[23:0]), .we(1'b1), .clk(controlled_buffer_2_out),
    .din(controlled_buffer_4_out));  // open: dout
  RAM #(.addrWidth(24), .dataWidth(32), .trigger("falling")) ram_9 (
    .addr(controlled_buffer_1_out[23:0]), .we(1'b1), .clk(controlled_buffer_2_out),
    .din(controlled_buffer_5_out));  // open: dout
  RAM #(.addrWidth(24), .dataWidth(32), .trigger("falling")) ram_10 (
    .addr(controlled_buffer_1_out[23:0]), .we(1'b1), .clk(controlled_buffer_2_out),
    .din(controlled_buffer_6_out));  // open: dout
  RAM #(.addrWidth(24), .dataWidth(32), .trigger("falling")) ram_11 (
    .addr(controlled_buffer_1_out[23:0]), .we(1'b1), .clk(controlled_buffer_2_out),
    .din(controlled_buffer_7_out));  // open: dout
  RAM #(.addrWidth(24), .dataWidth(32), .trigger("falling")) ram_12 (
    .addr(controlled_buffer_1_out[23:0]), .we(1'b1), .clk(controlled_buffer_2_out),
    .din(controlled_buffer_8_out));  // open: dout
  D_Flip_Flop d_ff_1 (.Qn(d_ff_1_qn), .preset(CLK), .reset(Master_Reset));  // open: clk, D, Q
  // Probe on imm_generator_v4_1_out
  LED led_3 (.in(k));
  LED led_4 (.in(k));
  Button button_4 (.out(uCounter_reset));
  or or_6 (or_6_out, d_ff_1_qn, CLK);
  not not_1 (not_1_out, CLK);
  D_Flip_Flop d_ff_2 ();  // open: clk, D, Q, Qn, preset, reset
  LED led_5 (.in(k));
  LED led_6 (.in(k));
  LED led_7 (.in(k));
  LED led_8 (.in(k));
  nor nor_1 (nor_1_out, CPU_Busy, or_6_out);
  or or_7 (or_7_out, Master_Reset, uCounter_reset);
  or or_8 (XX, or_7_out, d_ff_3_q);
  D_Flip_Flop d_ff_3 (
    .clk(or_6_out), .D(Program_counter_enable), .Q(d_ff_3_q), .reset(Master_Reset));  // open: Qn, preset
  // Probe on ins[6:0]
  // Probe on ins[6:0]
  // Probe on ins[11:7]
  // Probe on ins[14:12]
  // Probe on ins[19:15]
  // Probe on ins[24:20]
  // Probe on ins[31:25]
  LED led_9 (.in(k));
  LED led_10 (.in(k));
  Debugging_unit_v1 debugging_unit_v1_1 (.out_5(Inter), .in_1(rom_2_data), .in_2(Rd), .in_3(Rs1), .in_4(Rs2));
  Counter #(.max('h7), .width(3)) counter_7 (
    .Q(counter_7_q), .clk(nor_1_out), .clr(XX));  // open: load, D, count, carry
  assign CLK = not_2_out ? Main_Clock : 1'bz;  // Controlled_Buffer controlled_buffer_10
  Pull_Resistor pull_resistor_4 (.node(CLK));
  ROM #(.addrWidth(10)) E0 (
    .addr({ins[6:0], counter_7_q}),
    .data({PC_Source_1, Take_branch, ALU_Control_1, Store_to_register_imm_1, PC_Source, Store_to_register_imm_0, Memory_store, ALU_Control}));
  ROM #(.addrWidth(10)) E1 (
    .addr({ins[6:0], counter_7_q}),
    .data({ALU_Source, Counter_reset, Program_counter_enable, Store_to_register_0, Register_file_store, Imm_Gen_Control[1:0]}));
  ROM #(.addrWidth(10)) E2 (
    .addr({ins[6:0], counter_7_q}),
    .data({E2_data, Imm_Gen_Control[2], Memory_load, Register_file_load, Shifter_latch, Shifter_load}));
  assign GPU_c = in_5 ? Main_Clock : 1'bz;  // Controlled_Buffer controlled_buffer_11
  Pull_Resistor pull_resistor_5 (.node(GPU_c));
  not not_2 (not_2_out, in_5);
  or or_9 (or_9_out, Register_file_store, Register_file_load);
  // Probe on register_file_v6_1_read_register_1_2
  Register_file_v6 register_file_v6_1 (
    .Read_register_2_2(register_file_v6_1_read_register_2_2),
    .Read_register_1_2(register_file_v6_1_read_register_1_2), .write_data(out), .write_register(ins[11:7]),
    .Store(Register_file_store), .Clock(CLK), .Load(Register_file_load), .read_register_1(ins[19:15]),
    .read_register_2(ins[24:20]));
  Pull_Resistor pull_resistor_6 (.node(\reg ));
  assign \reg  = or_9_out ? register_file_v6_1_read_register_1_2 : 32'bz;  // Controlled_Buffer controlled_buffer_12
  Pull_Resistor pull_resistor_7 (.node(pull_resistor_7_node));
  assign pull_resistor_7_node = or_9_out ? register_file_v6_1_read_register_2_2 : 32'bz;  // Controlled_Buffer controlled_buffer_13
  Pull_Resistor pull_resistor_8 (.node({PC_Source_1, Take_branch, ALU_Control_1, Store_to_register_imm_1, PC_Source, Store_to_register_imm_0, Memory_store, ALU_Control}));
  Pull_Resistor pull_resistor_9 (.node({ALU_Source, Counter_reset, Program_counter_enable, Store_to_register_0, Register_file_store, Imm_Gen_Control[1:0]}));
  Pull_Resistor pull_resistor_10 (.node({E2_data, Imm_Gen_Control[2], Memory_load, Register_file_load, Shifter_latch, Shifter_load}));
  or or_10 (or_10_out, Program_counter_enable, Master_Reset);
  // Probe on pull_resistor_7_node
  // Probe on \reg 
  // Probe on multiplexer_2_out
  // Probe on multiplexer_2_out
  Multiplexer #(.enable("false"), .select(2), .width(32)) multiplexer_2 (
    .in0(pull_resistor_7_node), .in1(imm_generator_v4_1_out), .in2(inst_adr), .out(multiplexer_2_out),
    .sel(ALU_Source));  // open: in3
  ALU_v8 alu_v8_1 (
    .Branch(branch), .out_6(alu), .out_7(a_err), .in_5(CLK), .Y(multiplexer_2_out), .X(\reg ),
    .Funct3(alu_control_v3_1_aluop), .I(i));
  ALU_Control_v3 alu_control_v3_1 (
    .Instruction(ins), .ALUOp_in({ALU_Control_1, ALU_Control}), .ALUOp(alu_control_v3_1_aluop), .i(i));
  // Probe on alu
  // AND_Gate and_6 has open pins: in0=XX, in1=Memory_store, out=open
  ROM #(.addrWidth(10)) E0_2 ();  // open: addr, data
  ROM #(.addrWidth(10)) E1_2 ();  // open: addr, data
  ROM #(.addrWidth(10)) E2_2 ();  // open: addr, data
  shifter_v6 shifter_v6_1 (
    .out_12(s_err), .Out(out), .out_9(shifter_v6_1_out_9), .out_10(shifter_v6_1_out_10), .CLK(CLK),
    .SH_LOAD(Shifter_latch), .in_7(or_10_out), .Input(\reg ), .I(ins[30]), .Funct3(ins[14:12]),
    .RS2(multiplexer_2_out[4:0]), .in_5(Shifter_load));
  // Probe on alu
  and and_7 (CPU_Busy, ~Register_file_store, shifter_v6_1_out_9);  // AND_Gate
  LED led_11 (.in(d_err));
  LED led_12 (.in(CPU_Busy));
  // NOT_Gate not_3 has open pins: in=shifter_v6_1_out_10, out=open
  // Probe on data_memory_v9_1_out_7
  Data_memory_v9 data_memory_v9_1 (
    .out_7(data_memory_v9_1_out_7), .out_9(XL), .Exception(d_err), .Load(Memory_load), .Store(Memory_store),
    .Clock(CLK), .Funct3(ins[14:12]), .Data(pull_resistor_7_node), .Adress(alu));
  assign data_memory_v9_1_out_7 = Store_to_register_0 ? alu : 32'bz;  // Controlled_Buffer controlled_buffer_14
  Pull_Resistor pull_resistor_11 (.node(data_memory_v9_1_out_7));
  Register #(.width(32)) register_1 (
    .D(data_memory_v9_1_out_7), .en(1'b1), .Q(register_1_q), .clk(and_8_out));  // open: clr
  and and_8 (and_8_out, CLK, ~Register_file_store);  // AND_Gate
  // Probe on out
  Multiplexer #(.disabled("Z"), .select(2), .width(32)) multiplexer_3 (
    .in0(register_1_q), .in1(imm_generator_v4_1_out), .in2(prep), .out(out),
    .sel({Store_to_register_imm_1, Store_to_register_imm_0}), .en(shifter_v6_1_out_10));  // open: in3
  // RGB_Video #(.height(256), .scale(3), .width(256)) rgb_video_1: pin names not known
  // GPU_v5 gpu_v5_1: pin names not known; wires that end beside it: GPU_c, Master_Reset, gpu_v5_1_p3, gpu_v5_1_p4
  ROM #(.addrWidth(10)) E2_3 ();  // open: addr, data
  // NOT_Gate not_4 is placed but not wired

  // Other names for the same wires on the sheet: SH_I = ins[30]; a[31:0] = inst_adr; CPU_c = CLK; GPU_BYP = in_5

  // Notes on the sheet:
  //   Pulse Count
  //   Instruction
  //   Prepared
  //   Latched
  //   REG
  //   ALU
  //   Out
  //   Immediate errors
  //   ALU errors
  //   Shifter errors
  //   contents of rom_1 (hex, n*v repeats v):
  //   0 2 1 37 ff c1 1 13 17 c0 0 6f fd 1 1 13 2 11 26 23 2 81 24 23 3 1 4 13 fc a4 2e 23 fd c4 27 83 0 7
  //   88 63 fd c4 27 3 0 10 7 93 0 f7 16 63 fd c4 27 83 4 c0 0 6f 0 10 7 93 fe f4 26 23 0 10 7 93 fe f4 24
  //   23 2 40 0 6f fe c4 27 83 0 17 87 93 fe f4 26 23 fe c4 25 83 fe c4 25 3 35 40 0 ef 0 5 7 93 fe f4 24
  //   23 fe 84 27 3 fd c4 27 83 fc e7 dc e3 fe c4 27 83 ff f7 87 93 0 7 85 13 2 c1 20 83 2 81 24 3 3 1 1
  //   13 0 0 80 67 fd 1 1 13 2 11 26 23 2 81 24 23 3 1 4 13 fc a4 2e 23 fc b4 2c 23 fd c4 27 83 fe f4 22
  //   23 fd 84 27 83 fe f4 20 23 fe 44 27 83 fe f4 26 23 0 10 7 93 fe f4 24 23 2 40 0 6f fe 44 25 83 fe c4
  //   25 3 2d c0 0 ef 0 5 7 93 fe f4 26 23 fe 84 27 83 0 17 87 93 fe f4 24 23 fe 84 27 3 fe 4 27 83 fc f7
  //   4c e3 fe c4 27 83 0 7 85 13 2 c1 20 83 2 81 24 3 3 1 1 13 0 0 80 67 fe 1 1 13 0 11 2e 23 0 81 2c 23
  //   2 1 4 13 fe a4 26 23 fe b4 24 23 fe 84 25 83 fe c4 25 3 28 0 0 ef 0 5 7 93 0 7 85 13 1 c1 20 83 1 81
  //   24 3 2 1 1 13 0 0 80 67 fe 1 1 13 0 81 2e 23 2 1 4 13 fe a4 26 23 fe b4 24 23 fe c4 27 3 fe 84 27 83
  //   0 f7 7 b3 0 7 85 13 1 c1 24 3 2 1 1 13 0 0 80 67 fc 1 1 13 2 11 2e 23 2 81 2c 23 2 91 2a 23 4 1 4 13
  //   a b0 5 93 0 0 5 13 16 40 0 ef 0 a0 0 93 1 40 4 93 0 4 85 93 0 0 85 13 20 40 0 ef 0 5 7 93 fe f4 26
  //   23 fe c4 27 83 0 90 5 93 0 7 85 13 29 40 0 ef 0 5 7 93 fe f4 24 23 0 4 85 93 fe 84 25 3 1d 80 0 ef 0
  //   5 7 93 fe f4 24 23 fe 84 27 83 0 97 87 93 fe f4 24 23 fe 84 25 3 e1 1f f0 ef fe a4 26 23 fe f4 84 93
  //   fe c4 27 83 0 27 87 93 fe f4 26 23 0 4 85 93 fe c4 25 3 e7 df f0 ef fe a4 26 23 fe c4 27 83 0 17 87
  //   93 fe f4 26 23 fe c4 27 83 0 a0 5 93 0 7 85 13 1a 0 0 ef 0 5 7 93 fe f4 26 23 fe c4 25 83 0 0 5 13 b
  //   40 0 ef fc 4 20 23 fc 4 22 23 fc 4 24 23 fc 4 26 23 fc 4 28 23 fc 4 2a 23 fc 4 2c 23 fc 4 2e 23 fe 4
  //   20 23 fe 4 22 23 fe c4 27 83 fc f4 20 23 fe c4 27 83 0 a7 87 93 fc f4 22 23 fc 4 27 3 fc 44 27 83 0
  //   f7 7 b3 fc f4 24 23 1 30 5 93 0 10 5 13 5 c0 0 ef fc 84 27 83 0 7 85 93 0 0 5 13 4 c0 0 ef 0 0 0 6f
  //   ff 1 1 13 0 11 26 23 80 0 3 37 0 0 2 93 0 55 8 63 0 10 2 93 0 55 a 63 1 c0 0 6f 0 43 3 13 0 3 5 3 1
  //   0 0 6f 0 53 3 13 0 3 5 3 0 40 0 6f 0 c1 20 83 1 1 1 13 0 0 80 67 ff 1 1 13 0 11 26 23 80 0 2 b7 0 0
  //   3 93 0 55 3 b3 0 b3 80 23 0 c1 20 83 1 1 1 13 0 0 80 67 ff 1 1 13 0 11 26 23 0 0 2 93 0 a2 83 33 0
  //   b3 20 23 0 c1 20 83 1 1 1 13 0 0 80 67 ff 1 1 13 0 11 26 23 40 0 2 b7 0 a2 83 33 0 b3 20 23 0 c1 20
  //   83 1 1 1 13 0 0 80 67 ff 1 1 13 0 11 26 23 0 10 2 b7 c0 2 82 93 40 0 3 37 40 55 5e 13 0 2e 1e 93 0
  //   5e 83 b3 0 3 a3 83 1 f5 7f 13 0 10 e 13 1 ee 1e 33 1 c3 ef 33 0 6e 8e 33 1 ee 20 23 0 5e 8e 33 1 ee
  //   20 23 0 c1 20 83 1 1 1 13 0 0 80 67 0 5 6 13 0 0 5 13 0 15 f6 93 0 6 84 63 0 c5 5 33 0 15 d5 93 0 16
  //   16 13 fe 5 96 e3 0 0 80 67 6 5 40 63 6 5 c6 63 0 5 86 13 0 5 5 93 ff f0 5 13 2 6 c 63 0 10 6 93 0 b6
  //   7a 63 0 c0 58 63 0 16 16 13 0 16 96 93 fe b6 6a e3 0 0 5 13 0 c5 e6 63 40 c5 85 b3 0 d5 65 33 0 16
  //   d6 93 0 16 56 13 fe 6 96 e3 0 0 80 67 0 0 82 93 fb 5f f0 ef 0 5 85 13 0 2 80 67 40 a0 5 33 0 5 d8 63
  //   40 b0 5 b3 f9 df f0 6f 40 b0 5 b3 0 0 82 93 f9 1f f0 ef 40 a0 5 33 0 2 80 67 0 0 82 93 0 5 ca 63 0 5
  //   4c 63 f7 9f f0 ef 0 5 85 13 0 2 80 67 40 b0 5 b3 fe 5 58 e3 40 a0 5 33 f6 1f f0 ef 40 b0 5 33 0 2 80
  //   67
  //   Unaligned memory adr
  //   Odstranit
  //   Control
  //   instruction_BUS
  //   contents of rom_2 (hex, n*v repeats v):
  //   19*0 1b 15*0 29 15*0 1 0 0 0 7b 43*0 6f 0 0 0 7f 7*0 7d 35*0 5d 111*0 15 31*0 2d 319*0 73 47*0 63
  //   79*0 77 79*0 b 47*0 77 47*0 67 79*0 79 47*0 1d 31*0 3 175*0 71 31*0 15 31*0 2d 319*0 73 255*0 6b
  //   139*0 7d
  //   op-code 6:0
  //   B_11:7
  //   B_14:12
  //   B_19:15
  //   B_24:20
  //   B_31:25
  //   Enable
  //   CPU
  //   contents of E0 (hex, n*v repeats v):
  //   24*0 1 127*0 21 21 21 29*0 18 18 94*0 3 159*0 4 4 350*0 8 48 48 29*0 10 10 20 a0 a0 59*0 10 10 8 8
  //   contents of E1 (hex, n*v repeats v):
  //   24*0 40 4 10 125*0 40 48 44 10 28*0 3 7 10 93*0 41 10 126*0 8 8 4 10 10 27*0 3 7 10 349*0 2 12 2
  //   30*0 4 48 48 58 60*0 4 10
  //   contents of E2 (hex, n*v repeats v):
  //   7*0 80 7*0 80 7*0 80 c 14*0 80 7*0 80 7*0 80 7*0 80 7*0 80 7*0 80 7*0 80 7*0 80 7*0 80 7*0 80 7*0 80
  //   7*0 80 7*0 80 7*0 80 7*0 80 6 5 13*0 80 7*0 80 7*0 80 15*0 80 7*0 80 7*0 80 7*0 80 7*0 80 7*0 80 7*0
  //   80 7*0 80 7*0 80 7*0 80 7*0 80 4 14*0 80 7*0 80 7*0 80 7*0 80 7*0 80 7*0 80 7*0 80 7*0 80 7*0 80 7*0
  //   80 7*0 80 7*0 80 7*0 80 7*0 80 7*0 80 6 5 13*0 80 7*0 80 7*0 80 15*0 80 7*0 80 7*0 80 7*0 80 7*0 80
  //   7*0 80 7*0 80 7*0 80 7*0 80 7*0 80 7*0 80 7*0 80 7*0 80 7*0 80 7*0 80 7*0 80 7*0 80 7*0 80 7*0 80
  //   7*0 80 7*0 80 7*0 80 7*0 80 7*0 80 7*0 80 7*0 80 7*0 80 7*0 80 7*0 80 7*0 80 7*0 80 7*0 80 7*0 80
  //   7*0 80 7*0 80 7*0 80 7*0 80 7*0 80 7*0 80 7*0 80 7*0 80 7*0 80 7*0 80 4 4 4 12*0 80 7*0 80 7*0 80 0
  //   0 4 4 4 10*0 80 7*0 80 7*0 80 7*0 80 7*0 80 7*0 80 7*0 80 0 0 10 10
  //   GPU
  //   Imm Gen Contol [2]
  //   contents of E0_2 (hex, n*v repeats v):
  //   24*0 1 127*0 21 21 21 29*0 18 95*0 3 159*0 4 351*0 48 48 30*0 10 20 a0 a0 60*0 10 8 8
  //   contents of E1_2 (hex, n*v repeats v):
  //   24*0 40 4 10 125*0 40 48 44 10 28*0 7 10 94*0 41 10 126*0 8 8 4 10 10 27*0 7 10 350*0 12 3 30*0 4 48
  //   48 58 60*0 4 10 10
  //   contents of E2_2 (hex, n*v repeats v):
  //   24*0 c 127*0 6 5 1 125*0 4 127*0 6 5 1 381*0 4 32*0 4 4 4 61*0 10 10
  //   Exception
  //   contents of E2_3 (hex, n*v repeats v):
  //   24*0 c 127*0 6 5 126*0 4 127*0 6 5 382*0 4 32*0 4 4 4 61*0 10
endmodule

module Register_file_v1 (
  input  [4:0] in_1,
  input  [31:0] Write_data,
  input  [4:0] Write_reg,
  input  Load,
  input  Store,
  input  Clock,
  input  Read_r1,
  input  Read_r2,
  input  [4:0] Write_reg_2,
  output [31:0] src1,
  output [31:0] src2
);

  wire not_1_out;
  wire [4:0] controlled_buffer_1_out, controlled_buffer_2_out;
  wire [31:0] controlled_buffer_5_out, ram_2_data;

  assign controlled_buffer_1_out = not_1_out ? Write_reg : 5'bz;  // Controlled_Buffer controlled_buffer_1
  assign controlled_buffer_2_out = not_1_out ? Write_reg_2 : 5'bz;  // Controlled_Buffer controlled_buffer_2
  assign controlled_buffer_1_out = Store ? in_1 : 5'bz;  // Controlled_Buffer controlled_buffer_3
  not not_1 (not_1_out, Store);
  assign controlled_buffer_2_out = Store ? in_1 : 5'bz;  // Controlled_Buffer controlled_buffer_4
  RAM #(.addrWidth(5), .dataWidth(32), .databus("bidir"), .\type ("nonvolatile")) ram_1 (
    .sel(Load), .ld(Load), .clr(Clock));  // open: addr, data
  RAM #(.addrWidth(5), .dataWidth(32), .databus("bidir"), .\type ("nonvolatile")) ram_2 (
    .addr(controlled_buffer_2_out), .data(ram_2_data));  // open: we, oe, clk
  assign controlled_buffer_5_out = Store ? Write_data : 32'bz;  // Controlled_Buffer controlled_buffer_5
  assign ram_2_data = Store ? Write_data : 32'bz;  // Controlled_Buffer controlled_buffer_6
  assign src1 = Read_r1 ? controlled_buffer_5_out : 32'bz;  // Controlled_Buffer controlled_buffer_7
  assign src2 = Read_r2 ? ram_2_data : 32'bz;  // Controlled_Buffer controlled_buffer_8
endmodule

module Register_file_v2 (
  input  [31:0] Write_data,
  input  [31:0] BUS1,
  input  [31:0] BUS2,
  input  [4:0] Read_reg1,
  input  [4:0] Write_reg,
  input  Write,
  input  Clock,
  input  reg1_out,
  input  reg2_out,
  input  [4:0] Read_reg2
);

  wire not_1_out;
  wire [4:0] multiplexer_1_out, multiplexer_2_out;
  wire [15:0] bit_extender_1_out, bit_extender_2_out, ram_1_data, ram_2_data, ram_3_data, ram_4_data;

  Multiplexer #(.enable("false"), .width(5)) multiplexer_1 (
    .in0(Read_reg2), .in1(Write_reg), .out(multiplexer_1_out), .sel(Clock));
  Multiplexer #(.enable("false"), .width(5)) multiplexer_2 (
    .in0(Read_reg1), .in1(Write_reg), .out(multiplexer_2_out), .sel(Clock));
  not not_1 (not_1_out, Clock);
  RAM #(.addrWidth(16), .dataWidth(16), .databus("bidir")) ram_1 (
    .addr(bit_extender_1_out), .data(ram_1_data));  // open: we, oe, clk
  assign bit_extender_1_out = {{11{1'b0}}, multiplexer_2_out};  // Bit_Extender bit_extender_1
  RAM #(.addrWidth(16), .dataWidth(16), .databus("bidir")) ram_2 (
    .addr(bit_extender_1_out), .data(ram_2_data));  // open: we, oe, clk
  RAM #(.addrWidth(16), .dataWidth(16), .databus("bidir")) ram_3 (
    .addr(bit_extender_2_out), .data(ram_3_data));  // open: we, oe, clk
  assign bit_extender_2_out = {{11{1'b0}}, multiplexer_1_out};  // Bit_Extender bit_extender_2
  RAM #(.addrWidth(16), .dataWidth(16), .databus("bidir")) ram_4 (
    .addr(bit_extender_2_out), .data(ram_4_data));  // open: we, oe, clk
  assign {ram_2_data, ram_1_data} = Clock ? Write_data : 32'bz;  // Controlled_Buffer controlled_buffer_1
  assign {ram_4_data, ram_3_data} = Clock ? Write_data : 32'bz;  // Controlled_Buffer controlled_buffer_2
  assign BUS1 = reg1_out ? {ram_2_data, ram_1_data} : 32'bz;  // Controlled_Buffer controlled_buffer_3
  assign BUS2 = reg2_out ? {ram_4_data, ram_3_data} : 32'bz;  // Controlled_Buffer controlled_buffer_4

  assign Write = Clock;
endmodule

module Register_file_v3 (
  input  [4:0] read_register_1,
  input  Clock,
  input  [31:0] Write_data,
  input  [4:0] write_register,
  input  [4:0] read_register_2,
  input  Store,
  output [31:0] Read_register_1_2,
  output [31:0] Read_register_2_2
);

  wire and_1_out, and_2_out;
  wire [4:0] multiplexer_1_out, multiplexer_2_out, not_1_out;
  wire [31:0] ram_1_dout, ram_2_dout;

  Multiplexer #(.enable("false"), .width(5)) multiplexer_1 (
    .in0(read_register_1), .in1(write_register), .out(multiplexer_1_out), .sel(and_1_out));
  Multiplexer #(.enable("false"), .width(5)) multiplexer_2 (
    .in0(read_register_2), .in1(write_register), .out(multiplexer_2_out), .sel(and_1_out));
  assign not_1_out = ~write_register;  // NOT_Gate not_1, 5 bits wide
  and and_1 (and_1_out, Store, ~and_2_out);  // AND_Gate
  and and_2 (and_2_out, not_1_out[0], not_1_out[1], not_1_out[2], not_1_out[3], not_1_out[4]);
  RAM #(.addrWidth(5), .dataWidth(32)) ram_1 (
    .addr(multiplexer_1_out), .we(and_1_out), .clk(Clock), .din(Write_data), .dout(ram_1_dout));
  RAM #(.addrWidth(5), .dataWidth(32)) ram_2 (
    .addr(multiplexer_2_out), .we(and_1_out), .clk(Clock), .din(Write_data), .dout(ram_2_dout));
  Multiplexer #(.enable("false"), .width(32)) multiplexer_3 (
    .in0(ram_1_dout), .in1(Write_data), .out(Read_register_1_2), .sel(and_1_out));
  Pull_Resistor pull_resistor_1 (.node(and_1_out));
  Multiplexer #(.enable("false"), .width(32)) multiplexer_4 (
    .in0(ram_2_dout), .in1(Write_data), .out(Read_register_2_2), .sel(and_1_out));

  // Other names for the same wires on the sheet: clk = Clock; str = Store
endmodule

module Register_file_v4 (
  input  [4:0] read_register_1,
  input  [4:0] read_register_2,
  input  [31:0] Write_data,
  input  [4:0] write_register,
  input  Store,
  input  Clock,
  input  Load,
  output [31:0] Read_register_1_2,
  output [31:0] Read_register_2_2
);

  wire and_2_out, and_3_out, and_4_out, is_zero;
  wire [4:0] multiplexer_1_out, multiplexer_2_out, multiplexer_3_out, multiplexer_4_out, not_1_out;
  wire [15:0] ram_1_data, ram_2_data, ram_3_data, ram_4_data;
  wire [31:0] ram_5_dout, ram_6_dout;

  assign not_1_out = ~write_register;  // NOT_Gate not_1, 5 bits wide
  and and_1 (is_zero, not_1_out[0], not_1_out[1], not_1_out[2], not_1_out[3], not_1_out[4]);
  // NOT_Gate not_2 is placed but not wired
  and and_2 (and_2_out, Store, ~is_zero);  // AND_Gate
  and and_3 (and_3_out, Store, ~is_zero);  // AND_Gate
  Multiplexer #(.enable("false"), .width(5)) multiplexer_1 (
    .in0(read_register_1), .in1(write_register), .out(multiplexer_1_out), .sel(and_2_out));
  Multiplexer #(.enable("false"), .width(5)) multiplexer_2 (
    .in0(read_register_2), .in1(write_register), .out(multiplexer_2_out), .sel(and_3_out));
  Multiplexer #(.enable("false"), .width(5)) multiplexer_3 (
    .in0(read_register_1), .in1(write_register), .out(multiplexer_3_out), .sel(and_4_out));
  Multiplexer #(.enable("false"), .width(5)) multiplexer_4 (
    .in0(read_register_2), .in1(write_register), .out(multiplexer_4_out), .sel(and_4_out));
  RAM #(.addrWidth(5), .dataWidth(16), .databus("bidir")) ram_1 (
    .addr(multiplexer_1_out), .data(ram_1_data));  // open: we, oe, clk
  RAM #(.addrWidth(5), .dataWidth(16), .databus("bidir")) ram_2 (
    .addr(multiplexer_1_out), .data(ram_2_data));  // open: we, oe, clk
  RAM #(.addrWidth(5), .dataWidth(16), .databus("bidir")) ram_3 (
    .addr(multiplexer_2_out), .data(ram_3_data));  // open: we, oe, clk
  RAM #(.addrWidth(5), .dataWidth(16), .databus("bidir")) ram_4 (
    .addr(multiplexer_2_out), .data(ram_4_data));  // open: we, oe, clk
  and and_4 (and_4_out, Store, ~is_zero);  // AND_Gate
  RAM #(.addrWidth(5), .dataWidth(32)) ram_5 (
    .addr(multiplexer_3_out), .we(and_4_out), .clk(Clock), .din(Write_data), .dout(ram_5_dout));
  RAM #(.addrWidth(5), .dataWidth(32)) ram_6 (
    .addr(multiplexer_4_out), .we(and_4_out), .clk(Clock), .din(Write_data), .dout(ram_6_dout));
  assign {ram_2_data, ram_1_data} = and_2_out ? Write_data : 32'bz;  // Controlled_Buffer controlled_buffer_1
  assign {ram_4_data, ram_3_data} = and_3_out ? Write_data : 32'bz;  // Controlled_Buffer controlled_buffer_2
  // Probe on ram_5_dout
  // Probe on ram_6_dout
  assign Read_register_1_2 = Load ? {ram_2_data, ram_1_data} : 32'bz;  // Controlled_Buffer controlled_buffer_3
  Pull_Resistor #(.pull(1)) pull_resistor_1 (.node({ram_2_data, ram_1_data}));
  assign Read_register_2_2 = Load ? {ram_4_data, ram_3_data} : 32'bz;  // Controlled_Buffer controlled_buffer_4
  Pull_Resistor #(.pull(1)) pull_resistor_2 (.node({ram_4_data, ram_3_data}));
  Pull_Resistor #(.pull(1)) pull_resistor_3 (.node(Read_register_1_2));
  Pull_Resistor #(.pull(1)) pull_resistor_4 (.node(Read_register_2_2));
  // NOT_Gate not_3 is placed but not wired

  // Other names for the same wires on the sheet: clk = Clock; Read_reg1[4:0] = read_register_1;
  //   Read_reg2[4:0] = read_register_2; str = Store; Write_reg[4:0] = write_register
endmodule

module Register_file_v5 (
  input  [4:0] read_register_1,
  input  [4:0] read_register_2,
  input  [31:0] write_data,
  input  [4:0] write_register,
  input  Store,
  input  Clock,
  input  Load,
  output [31:0] Read_register_1_2,
  output [31:0] Read_register_2_2
);

  wire and_1_out, and_2_out, and_3_out, and_4_out, and_5_out, and_6_out, and_7_out, and_8_out, and_9_out,
       and_10_out, and_11_out, and_12_out, and_13_out, buffer_1_out, is_zero, is_zero_r1, is_zero_r2,
       not_1_out, not_2_out, not_3_out, not_4_out, not_5_out, not_6_out, not_7_out, not_8_out;
  wire [4:0] controlled_buffer_1_out, controlled_buffer_7_out, multiplexer_1_out;
  wire [15:0] ram_1_data, ram_2_data, ram_3_data, ram_4_data;
  wire [31:0] controlled_buffer_5_out;

  or or_1 (is_zero_r1, read_register_1[0], read_register_1[1], read_register_1[2], read_register_1[3], read_register_1[4]);
  or or_2 (is_zero_r2, read_register_2[0], read_register_2[1], read_register_2[2], read_register_2[3], read_register_2[4]);
  or or_3 (is_zero, write_register[0], write_register[1], write_register[2], write_register[3], write_register[4]);
  assign controlled_buffer_1_out = not_1_out ? read_register_1 : 5'bz;  // Controlled_Buffer controlled_buffer_1
  not not_1 (not_1_out, and_4_out);
  assign controlled_buffer_1_out = and_1_out ? write_register : 5'bz;  // Controlled_Buffer controlled_buffer_2
  and and_1 (and_1_out, and_4_out, and_4_out);
  and and_2 (and_2_out, and_4_out, Clock);
  and and_3 (and_3_out, Load, is_zero_r1);
  and and_4 (and_4_out, Store, is_zero);
  Multiplexer #(.enable("false"), .width(5)) multiplexer_1 (
    .in0(read_register_2), .in1(write_register), .out(multiplexer_1_out), .sel(and_7_out));
  and and_5 (and_5_out, and_7_out, Clock);
  and and_6 (and_6_out, Load, is_zero_r2);
  and and_7 (and_7_out, Store, is_zero);
  not not_2 (not_2_out, and_2_out);
  not not_3 (not_3_out, not_2_out);
  not not_4 (not_4_out, and_5_out);
  not not_5 (not_5_out, not_4_out);
  and and_8 (and_8_out, not_3_out, and_2_out);
  and and_9 (and_9_out, not_5_out, and_5_out);
  RAM #(.addrWidth(5), .dataWidth(16), .databus("bidir")) ram_1 (
    .addr(controlled_buffer_1_out), .data(ram_1_data));  // open: we, oe, clk
  RAM #(.addrWidth(5), .dataWidth(16), .databus("bidir")) ram_2 (
    .addr(controlled_buffer_1_out), .data(ram_2_data));  // open: we, oe, clk
  RAM #(.addrWidth(5), .dataWidth(16), .databus("bidir")) ram_3 (
    .addr(multiplexer_1_out), .data(ram_3_data));  // open: we, oe, clk
  RAM #(.addrWidth(5), .dataWidth(16), .databus("bidir")) ram_4 (
    .addr(multiplexer_1_out), .data(ram_4_data));  // open: we, oe, clk
  assign {ram_2_data, ram_1_data} = and_4_out ? write_data : 32'bz;  // Controlled_Buffer controlled_buffer_3
  assign {ram_4_data, ram_3_data} = and_7_out ? write_data : 32'bz;  // Controlled_Buffer controlled_buffer_4
  assign controlled_buffer_5_out = and_3_out ? {ram_2_data, ram_1_data} : 32'bz;  // Controlled_Buffer controlled_buffer_5
  Pull_Resistor pull_resistor_1 (.node(controlled_buffer_5_out));
  assign Read_register_2_2 = and_6_out ? {ram_4_data, ram_3_data} : 32'bz;  // Controlled_Buffer controlled_buffer_6
  Pull_Resistor pull_resistor_2 (.node(Read_register_2_2));
  and and_10 (and_10_out, Store, is_zero);
  and and_11 (and_11_out, Load, is_zero_r1);
  assign controlled_buffer_7_out = not_6_out ? read_register_1 : 5'bz;  // Controlled_Buffer controlled_buffer_7
  not not_6 (not_6_out, and_10_out);
  assign controlled_buffer_7_out = buffer_1_out ? write_register : 5'bz;  // Controlled_Buffer controlled_buffer_8
  buf buffer_1 (buffer_1_out, and_10_out);
  and and_12 (and_12_out, and_10_out, Clock);
  not not_7 (not_7_out, and_12_out);
  not not_8 (not_8_out, not_7_out);
  RAM #(.addrWidth(5), .dataWidth(16), .databus("bidir")) ram_5 (
    .addr(controlled_buffer_7_out), .data(Read_register_1_2[15:0]));  // open: we, oe, clk
  and and_13 (and_13_out, not_8_out, and_12_out);
  RAM #(.addrWidth(5), .dataWidth(16), .databus("bidir")) ram_6 (
    .addr(controlled_buffer_7_out), .data(Read_register_1_2[31:16]));  // open: we, oe, clk
  assign Read_register_1_2 = and_12_out ? write_data : 32'bz;  // Controlled_Buffer controlled_buffer_9
  Pull_Resistor pull_resistor_3 (.node(Read_register_1_2));

  // Other names for the same wires on the sheet: clk = Clock; Read_reg1[4:0] = read_register_1;
  //   Read_reg2[4:0] = read_register_2; str = Store; Write_reg[4:0] = write_register
endmodule

module Register_file_v6 (
  input  [4:0] read_register_1,
  input  [4:0] read_register_2,
  input  [31:0] write_data,
  input  [4:0] write_register,
  input  Store,
  input  Clock,
  input  Load,
  output [31:0] Read_register_1_2,
  output [31:0] Read_register_2_2
);

  wire and_1_out, and_2_out, and_3_out, and_4_out, and_5_out, and_6_out, buffer_1_out, buffer_2_out, is_zero,
       is_zero_r1, is_zero_r2, not_1_out, not_2_out, not_3_out, not_4_out, not_5_out, not_6_out, not_7_out,
       not_8_out, not_9_out, not_10_out, not_11_out, not_12_out, not_13_out, not_14_out, not_15_out,
       not_16_out, not_17_out, not_18_out;
  wire [4:0] controlled_buffer_1_out, controlled_buffer_3_out;

  or or_1 (is_zero_r1, read_register_1[0], read_register_1[1], read_register_1[2], read_register_1[3], read_register_1[4]);
  or or_2 (is_zero_r2, read_register_2[0], read_register_2[1], read_register_2[2], read_register_2[3], read_register_2[4]);
  or or_3 (is_zero, write_register[0], write_register[1], write_register[2], write_register[3], write_register[4]);
  and and_1 (and_1_out, Store, is_zero);
  and and_2 (and_2_out, Load, is_zero_r1);
  and and_3 (and_3_out, Store, is_zero);
  and and_4 (and_4_out, Load, is_zero_r2);
  assign controlled_buffer_1_out = not_1_out ? read_register_1 : 5'bz;  // Controlled_Buffer controlled_buffer_1
  not not_1 (not_1_out, and_1_out);
  assign controlled_buffer_1_out = buffer_1_out ? write_register : 5'bz;  // Controlled_Buffer controlled_buffer_2
  buf buffer_1 (buffer_1_out, and_1_out);
  and and_5 (and_5_out, and_1_out, Clock);
  not not_2 (not_2_out, and_1_out);
  not not_3 (not_3_out, not_2_out);
  assign controlled_buffer_3_out = not_4_out ? read_register_2 : 5'bz;  // Controlled_Buffer controlled_buffer_3
  not not_4 (not_4_out, and_3_out);
  assign controlled_buffer_3_out = buffer_2_out ? write_register : 5'bz;  // Controlled_Buffer controlled_buffer_4
  buf buffer_2 (buffer_2_out, and_3_out);
  and and_6 (and_6_out, and_3_out, Clock);
  not not_5 (not_5_out, and_3_out);
  not not_6 (not_6_out, not_5_out);
  not not_7 (not_7_out, and_5_out);
  not not_8 (not_8_out, not_7_out);
  not not_9 (not_9_out, not_8_out);
  not not_10 (not_10_out, not_9_out);
  not not_11 (not_11_out, not_3_out);
  not not_12 (not_12_out, not_11_out);
  not not_13 (not_13_out, and_6_out);
  not not_14 (not_14_out, not_13_out);
  not not_15 (not_15_out, not_14_out);
  not not_16 (not_16_out, not_15_out);
  not not_17 (not_17_out, not_6_out);
  not not_18 (not_18_out, not_17_out);
  RAM #(.addrWidth(5), .dataWidth(16), .databus("bidir")) ram_1 (
    .addr(controlled_buffer_1_out), .data(Read_register_1_2[15:0]));  // open: we, oe, clk
  RAM #(.addrWidth(5), .dataWidth(16), .databus("bidir")) ram_2 (
    .addr(controlled_buffer_1_out), .data(Read_register_1_2[31:16]));  // open: we, oe, clk
  RAM #(.addrWidth(5), .dataWidth(16), .databus("bidir")) ram_3 (
    .addr(controlled_buffer_3_out), .data(Read_register_2_2[15:0]));  // open: we, oe, clk
  RAM #(.addrWidth(5), .dataWidth(16), .databus("bidir")) ram_4 (
    .addr(controlled_buffer_3_out), .data(Read_register_2_2[31:16]));  // open: we, oe, clk
  assign Read_register_1_2 = not_12_out ? write_data : 32'bz;  // Controlled_Buffer controlled_buffer_5
  assign Read_register_2_2 = not_18_out ? write_data : 32'bz;  // Controlled_Buffer controlled_buffer_6

  // Other names for the same wires on the sheet: clk = Clock; Read_reg1[4:0] = read_register_1;
  //   Read_reg2[4:0] = read_register_2; str = Store; Write_reg[4:0] = write_register
endmodule

module Register_file_v20 (
  input  Store,
  input  Clock,
  input  Load,
  input  [4:0] read_register_1,
  input  [4:0] read_register_2,
  input  [31:0] write_data,
  input  [4:0] write_register,
  output [31:0] RB_0,
  output [31:0] RB_1
);

  wire and_1_out, and_2_out, and_3_out, and_4_out, and_5_out, and_6_out, buffer_1_out, buffer_2_out, is_zero,
       is_zero_r1, is_zero_r2, not_1_out, not_2_out, not_3_out, not_4_out, not_5_out, not_6_out, not_7_out,
       not_8_out, not_9_out, not_10_out, not_11_out, not_12_out, not_13_out, not_14_out, not_15_out,
       not_16_out, not_17_out, not_18_out;
  wire [4:0] controlled_buffer_1_out, controlled_buffer_3_out;

  and and_1 (and_1_out, Store, is_zero);
  and and_2 (and_2_out, Load, is_zero_r1);
  and and_3 (and_3_out, Store, is_zero);
  and and_4 (and_4_out, Load, is_zero_r2);
  assign controlled_buffer_1_out = not_1_out ? read_register_1 : 5'bz;  // Controlled_Buffer controlled_buffer_1
  not not_1 (not_1_out, and_1_out);
  assign controlled_buffer_1_out = buffer_1_out ? write_register : 5'bz;  // Controlled_Buffer controlled_buffer_2
  buf buffer_1 (buffer_1_out, and_1_out);
  and and_5 (and_5_out, and_1_out, Clock);
  not not_2 (not_2_out, and_5_out);
  not not_3 (not_3_out, not_2_out);
  not not_4 (not_4_out, not_3_out);
  not not_5 (not_5_out, not_4_out);
  assign controlled_buffer_3_out = not_6_out ? read_register_2 : 5'bz;  // Controlled_Buffer controlled_buffer_3
  not not_6 (not_6_out, and_3_out);
  assign controlled_buffer_3_out = buffer_2_out ? write_register : 5'bz;  // Controlled_Buffer controlled_buffer_4
  buf buffer_2 (buffer_2_out, and_3_out);
  and and_6 (and_6_out, and_3_out, Clock);
  not not_7 (not_7_out, and_6_out);
  not not_8 (not_8_out, not_7_out);
  not not_9 (not_9_out, not_8_out);
  not not_10 (not_10_out, not_9_out);
  RAM #(.addrWidth(5), .dataWidth(16), .databus("bidir")) ram_1 (
    .addr(controlled_buffer_1_out), .data(RB_0[15:0]));  // open: we, oe, clk
  RAM #(.addrWidth(5), .dataWidth(16), .databus("bidir")) ram_2 (
    .addr(controlled_buffer_1_out), .data(RB_0[31:16]));  // open: we, oe, clk
  RAM #(.addrWidth(5), .dataWidth(16), .databus("bidir")) ram_3 (
    .addr(controlled_buffer_3_out), .data(RB_1[15:0]));  // open: we, oe, clk
  RAM #(.addrWidth(5), .dataWidth(16), .databus("bidir")) ram_4 (
    .addr(controlled_buffer_3_out), .data(RB_1[31:16]));  // open: we, oe, clk
  not not_11 (not_11_out, and_1_out);
  not not_12 (not_12_out, not_11_out);
  not not_13 (not_13_out, and_3_out);
  not not_14 (not_14_out, not_13_out);
  assign RB_0 = not_16_out ? write_data : 32'bz;  // Controlled_Buffer controlled_buffer_5
  Pull_Resistor pull_resistor_1 (.node(RB_0));
  not not_15 (not_15_out, not_12_out);
  not not_16 (not_16_out, not_15_out);
  Pull_Resistor pull_resistor_2 (.node(RB_1));
  assign RB_1 = not_18_out ? write_data : 32'bz;  // Controlled_Buffer controlled_buffer_6
  not not_17 (not_17_out, not_14_out);
  not not_18 (not_18_out, not_17_out);
  or or_1 (is_zero_r1, read_register_1[0], read_register_1[1], read_register_1[2], read_register_1[3], read_register_1[4]);
  or or_2 (is_zero_r2, read_register_2[0], read_register_2[1], read_register_2[2], read_register_2[3], read_register_2[4]);
  or or_3 (is_zero, write_register[0], write_register[1], write_register[2], write_register[3], write_register[4]);

  // Other names for the same wires on the sheet: clk = Clock; Read_reg1[4:0] = read_register_1;
  //   Read_reg2[4:0] = read_register_2; Register_bank_0[31:0] = RB_0; Register_bank_1[31:0] = RB_1; str = Store;
  //   Write_reg[4:0] = write_register

  // Notes on the sheet:
  //   Inputs
  //   Register Bank 0
  //   Register Bank 1
  //   REGISTER FILE
  //   Outputs
  //   Logic
endmodule

module ALU_v1 (
  input  [31:0] src1,
  input  [31:0] src2,
  input  control,
  output [31:0] \output 
);

  Adder #(.width(32)) adder_1 (.a(src1), .b(src2), .out(\output ));  // open: cin, cout
endmodule

module ALU_v2 (
  input  I,
  input  [31:0] SRC_1,
  input  [31:0] SRC_2,
  input  [2:0] Funct3,
  output [31:0] out_5
);

  wire [31:0] adder_1_out, and_1_out, multiplexer_1_out, or_1_out, subtractor_1_out, xor_1_out;

  Adder #(.width(32)) adder_1 (.a(SRC_1), .b(SRC_2), .out(adder_1_out));  // open: cin, cout
  Subtractor #(.width(32)) subtractor_1 (.a(SRC_1), .b(SRC_2), .out(subtractor_1_out));  // open: bin, bout
  assign or_1_out = SRC_1 | SRC_2;  // OR_Gate or_1, 32 bits wide
  assign and_1_out = SRC_1 & SRC_2;  // AND_Gate and_1, 32 bits wide
  assign xor_1_out = SRC_1 ^ SRC_2;  // XOR_Gate xor_1, 32 bits wide
  Multiplexer #(.enable("false"), .width(32)) multiplexer_1 (
    .in0(adder_1_out), .in1(subtractor_1_out), .out(multiplexer_1_out), .sel(I));
  Multiplexer #(.enable("false"), .select(3), .width(32)) multiplexer_2 (
    .in0(multiplexer_1_out), .in4(xor_1_out), .in6(or_1_out), .in7(and_1_out), .out(out_5), .sel(Funct3));  // open: in1, in2, in3, in5
endmodule

module ALU_v3 (
  input  I,
  input  [31:0] SRC_1,
  input  [31:0] SRC_2,
  input  [2:0] Funct3,
  output Zero,
  output [31:0] out_6,
  output Branch
);

  wire comparator_1_lt, comparator_2_lt, comparator_3_eq, comparator_3_gt, comparator_3_lt, comparator_4_eq,
       comparator_4_gt, comparator_4_lt, not_1_out, or_2_out, or_3_out;
  wire [31:0] adder_1_out, and_1_out, bit_extender_1_out, bit_extender_2_out, multiplexer_1_out,
       multiplexer_2_out, or_1_out, shifter_1_out, shifter_2_out, shifter_3_out, subtractor_1_out, xor_1_out;

  Adder #(.width(32)) adder_1 (.a(SRC_1), .b(SRC_2), .out(adder_1_out));  // open: cin, cout
  Subtractor #(.width(32)) subtractor_1 (.a(SRC_1), .b(SRC_2), .out(subtractor_1_out));  // open: bin, bout
  Comparator #(.width(32)) comparator_1 (.a(SRC_1), .b(SRC_2), .lt(comparator_1_lt));  // open: gt, eq
  Comparator #(.mode("unsigned"), .width(32)) comparator_2 (
    .a(SRC_1), .b(SRC_2), .lt(comparator_2_lt));  // open: gt, eq
  assign xor_1_out = SRC_1 ^ SRC_2;  // XOR_Gate xor_1, 32 bits wide
  assign or_1_out = SRC_1 | SRC_2;  // OR_Gate or_1, 32 bits wide
  assign and_1_out = SRC_1 & SRC_2;  // AND_Gate and_1, 32 bits wide
  Comparator #(.width(32)) comparator_3 (
    .a(SRC_1), .b(SRC_2), .gt(comparator_3_gt), .eq(comparator_3_eq), .lt(comparator_3_lt));
  Comparator #(.mode("unsigned"), .width(32)) comparator_4 (
    .a(SRC_1), .b(SRC_2), .gt(comparator_4_gt), .eq(comparator_4_eq), .lt(comparator_4_lt));
  Multiplexer #(.enable("false"), .width(32)) multiplexer_1 (
    .in0(adder_1_out), .in1(subtractor_1_out), .out(multiplexer_1_out), .sel(I));
  Shifter #(.width(32)) shifter_1 (.in(SRC_1), .\dist (SRC_2[4:0]), .out(shifter_1_out));
  assign bit_extender_1_out = {{31{1'b0}}, comparator_1_lt};  // Bit_Extender bit_extender_1
  assign bit_extender_2_out = {{31{1'b0}}, comparator_2_lt};  // Bit_Extender bit_extender_2
  Shifter #(.shift("lr"), .width(32)) shifter_2 (.in(SRC_1), .\dist (SRC_2[4:0]), .out(shifter_2_out));
  Shifter #(.shift("ar"), .width(32)) shifter_3 (.in(SRC_1), .\dist (SRC_2[4:0]), .out(shifter_3_out));
  or or_2 (or_2_out, comparator_4_gt, comparator_4_eq);
  Multiplexer #(.enable("false"), .width(32)) multiplexer_2 (
    .in0(shifter_2_out), .in1(shifter_3_out), .out(multiplexer_2_out), .sel(I));
  not not_1 (not_1_out, comparator_3_eq);
  or or_3 (or_3_out, comparator_3_eq, comparator_3_gt);
  // Probe on multiplexer_1_out
  Multiplexer #(.enable("false"), .select(3)) multiplexer_3 (
    .in0(comparator_3_eq), .in1(not_1_out), .in2(1'b0), .in3(1'b0), .in4(comparator_3_lt), .in5(or_3_out),
    .in6(comparator_4_lt), .in7(or_2_out), .out(Branch), .sel(Funct3));
  Multiplexer #(.enable("false"), .select(3), .width(32)) multiplexer_4 (
    .in0(multiplexer_1_out), .in1(shifter_1_out), .in2(bit_extender_1_out), .in3(bit_extender_2_out),
    .in4(xor_1_out), .in5(multiplexer_2_out), .in6(or_1_out), .in7(and_1_out), .out(out_6), .sel(Funct3));
  Comparator #(.width(32)) comparator_5 (.a({32{1'b0}}), .b(out_6), .eq(Zero));  // open: gt, lt

  // Notes on the sheet:
  //   add
  //   sub
  //   SLL
  //   SLT
  //   SLTU
  //   XOR
  //   SRL
  //   SRA
  //   OR
  //   AND
endmodule

module ALU_v4 (
  input  I,
  input  [31:0] SRC_1,
  input  [31:0] SRC_2,
  input  [2:0] Funct3,
  input  [2:0] Funct3_2,
  output Zero,
  output [31:0] out_7,
  output Branch
);

  wire comparator_1_lt, comparator_2_lt, comparator_3_eq, comparator_3_gt, comparator_3_lt, comparator_4_eq,
       comparator_4_gt, comparator_4_lt, not_1_out, or_2_out, or_3_out;
  wire [31:0] adder_1_out, and_1_out, bit_extender_1_out, bit_extender_2_out, multiplexer_1_out,
       multiplexer_2_out, or_1_out, shifter_1_out, shifter_2_out, shifter_3_out, subtractor_1_out, xor_1_out;

  Adder #(.width(32)) adder_1 (.a(SRC_1), .b(SRC_2), .out(adder_1_out));  // open: cin, cout
  Subtractor #(.width(32)) subtractor_1 (.a(SRC_1), .b(SRC_2), .out(subtractor_1_out));  // open: bin, bout
  Comparator #(.width(32)) comparator_1 (.a(SRC_1), .b(SRC_2), .lt(comparator_1_lt));  // open: gt, eq
  Comparator #(.mode("unsigned"), .width(32)) comparator_2 (
    .a(SRC_1), .b(SRC_2), .lt(comparator_2_lt));  // open: gt, eq
  assign xor_1_out = SRC_1 ^ SRC_2;  // XOR_Gate xor_1, 32 bits wide
  assign or_1_out = SRC_1 | SRC_2;  // OR_Gate or_1, 32 bits wide
  assign and_1_out = SRC_1 & SRC_2;  // AND_Gate and_1, 32 bits wide
  Comparator #(.width(32)) comparator_3 (
    .a(SRC_1), .b(SRC_2), .gt(comparator_3_gt), .eq(comparator_3_eq), .lt(comparator_3_lt));
  Comparator #(.mode("unsigned"), .width(32)) comparator_4 (
    .a(SRC_1), .b(SRC_2), .gt(comparator_4_gt), .eq(comparator_4_eq), .lt(comparator_4_lt));
  Multiplexer #(.enable("false"), .width(32)) multiplexer_1 (
    .in0(adder_1_out), .in1(subtractor_1_out), .out(multiplexer_1_out), .sel(I));
  Shifter #(.width(32)) shifter_1 (.in(SRC_1), .\dist (SRC_2[4:0]), .out(shifter_1_out));
  assign bit_extender_1_out = {{31{1'b0}}, comparator_1_lt};  // Bit_Extender bit_extender_1
  assign bit_extender_2_out = {{31{1'b0}}, comparator_2_lt};  // Bit_Extender bit_extender_2
  Shifter #(.shift("lr"), .width(32)) shifter_2 (.in(SRC_1), .\dist (SRC_2[4:0]), .out(shifter_2_out));
  Shifter #(.shift("ar"), .width(32)) shifter_3 (.in(SRC_1), .\dist (SRC_2[4:0]), .out(shifter_3_out));
  or or_2 (or_2_out, comparator_4_gt, comparator_4_eq);
  Multiplexer #(.enable("false"), .width(32)) multiplexer_2 (
    .in0(shifter_2_out), .in1(shifter_3_out), .out(multiplexer_2_out), .sel(I));
  not not_1 (not_1_out, comparator_3_eq);
  Multiplexer #(.enable("false"), .select(3)) multiplexer_3 (
    .in0(comparator_3_eq), .in1(not_1_out), .in4(comparator_3_lt), .in5(or_3_out), .in6(comparator_4_lt),
    .in7(or_2_out), .out(Branch), .sel(Funct3_2));  // open: in2, in3
  or or_3 (or_3_out, comparator_3_eq, comparator_3_gt);
  Multiplexer #(.enable("false"), .select(3), .width(32)) multiplexer_4 (
    .in0(multiplexer_1_out), .in1(shifter_1_out), .in2(bit_extender_1_out), .in3(bit_extender_2_out),
    .in4(xor_1_out), .in5(multiplexer_2_out), .in6(or_1_out), .in7(and_1_out), .out(out_7), .sel(Funct3));
  Comparator #(.width(32)) comparator_5 (.a({32{1'b0}}), .b(out_7), .eq(Zero));  // open: gt, lt

  // Notes on the sheet:
  //   add
  //   sub
  //   SLL
  //   SLT
  //   SLTU
  //   XOR
  //   SRL
  //   SRA
  //   OR
  //   AND
endmodule

module ALU_v5_experimental (
  input  Cin,
  input  [8:0] X,
  input  [8:0] Y,
  input  [2:0] Funct3
);

  wire [7:0] rom_4_data;
  wire [7:3] rom_1_data, rom_2_data, rom_3_data;
  wire [8:0] rom_1_data_2;

  ROM #(.addrWidth(10)) rom_1 (.addr({Funct3, Y[2:0], X[2:0], Cin}), .data({rom_1_data, rom_1_data_2[2:0]}));
  ROM #(.addrWidth(10)) rom_2 (.addr({Funct3, Y[5:3], X[5:3], rom_4_data[0]}), .data({rom_2_data, rom_1_data_2[5:3]}));
  ROM #(.addrWidth(10)) rom_3 (.addr({Funct3, Y[8:6], X[8:6], rom_4_data[1]}), .data({rom_3_data, rom_1_data_2[8:6]}));
  LED led_1 (.in(rom_1_data[3]));
  LED led_2 (.in(rom_1_data[4]));
  LED led_3 (.in(rom_2_data[3]));
  LED led_4 (.in(rom_2_data[4]));
  LED led_5 (.in(rom_3_data[3]));
  LED led_6 (.in(rom_3_data[4]));
  // Probe on rom_1_data_2[2:0]
  // Probe on rom_1_data_2[5:3]
  // Probe on rom_1_data_2[8:6]
  ROM #(.addrWidth(7)) rom_4 (.addr({rom_3_data[4:3], rom_2_data[4:3], rom_1_data[4:3], Cin}), .data(rom_4_data));
  // Probe on rom_1_data_2

  // Notes on the sheet:
  //   contents of rom_1 (hex, n*v repeats v):
  //   0 1 1 2 2 3 3 4 4 5 5 6 6 7 17 10 1 2 2 3 3 4 4 5 5 6 6 7 17 10 18 19 2 3 3 4 4 5 5 6 6 7 17 10 18
  //   19 19 1a 3 4 4 5 5 6 6 7 17 10 18 19 19 1a 1a 1b 4 5 5 6 6 7 17 10 18 19 19 1a 1a 1b 1b 1c 5 6 6 7
  //   17 10 18 19 19 1a 1a 1b 1b 1c 1c 1d 6 7 17 10 18 19 19 1a 1a 1b 1b 1c 1c 1d 1d 1e 17 10 18 19 19 1a
  //   1a 1b 1b 1c 1c 1d 1d 1e 1e 1f
  //   contents of rom_2 (hex, n*v repeats v):
  //   0 1 1 2 2 3 3 4 4 5 5 6 6 7 17 10 1 2 2 3 3 4 4 5 5 6 6 7 17 10 18 19 2 3 3 4 4 5 5 6 6 7 17 10 18
  //   19 19 1a 3 4 4 5 5 6 6 7 17 10 18 19 19 1a 1a 1b 4 5 5 6 6 7 17 10 18 19 19 1a 1a 1b 1b 1c 5 6 6 7
  //   17 10 18 19 19 1a 1a 1b 1b 1c 1c 1d 6 7 17 10 18 19 19 1a 1a 1b 1b 1c 1c 1d 1d 1e 17 10 18 19 19 1a
  //   1a 1b 1b 1c 1c 1d 1d 1e 1e 1f
  //   contents of rom_3 (hex, n*v repeats v):
  //   0 1 1 2 2 3 3 4 4 5 5 6 6 7 17 10 1 2 2 3 3 4 4 5 5 6 6 7 17 10 18 19 2 3 3 4 4 5 5 6 6 7 17 10 18
  //   19 19 1a 3 4 4 5 5 6 6 7 17 10 18 19 19 1a 1a 1b 4 5 5 6 6 7 17 10 18 19 19 1a 1a 1b 1b 1c 5 6 6 7
  //   17 10 18 19 19 1a 1a 1b 1b 1c 1c 1d 6 7 17 10 18 19 19 1a 1a 1b 1b 1c 1c 1d 1d 1e 17 10 18 19 19 1a
  //   1a 1b 1b 1c 1c 1d 1d 1e 1e 1f
  //   G
  //   P
  //   G
  //   P
  //   G
  //   P
  //   contents of rom_4 (hex, n*v repeats v):
  //   0 0 1 1 0 1 1 1 2 2 3 3 2 3 3 3 0 0 3 3 0 3 3 3 2 2 3 3 2 3 3 3 4 4 5 5 4 5 5 5 6 6 7 7 6 7 7 7 4 4
  //   7 7 4 7 7 7 6 6 7 7 6 7 7 7 0 0 1 1 0 1 1 1 6 6 7 7 6 7 7 7 0 0 7 7 0 7 7 7 6 6 7 7 6 7 7 7 4 4 5 5
  //   4 5 5 5 6 6 7 7 6 7 7 7 4 4 7 7 4 7 7 7 6 6 7 7 6 7 7 7
endmodule

module ALU_v6 (
  input  [31:0] Y,
  input  [31:0] X,
  input  [2:0] Funct3,
  input  i,
  output Branch,
  output [31:0] Out
);

  wire comparator_1_eq, comparator_1_gt, comparator_1_lt, comparator_2_eq, comparator_2_gt, comparator_2_lt,
       controlled_buffer_1_out, decoder_1_out2, decoder_1_out3, not_1_out, or_1_out, or_2_out, or_3_out;
  wire [0:0] rom_1_data_2;
  wire [7:0] pull_resistor_1_node;
  wire [7:6] rom_1_data, rom_2_data, rom_3_data, rom_4_data, rom_5_data, rom_6_data, rom_7_data, rom_8_data;
  wire [16:1] rom_1_data_3;
  wire [31:0] alu_v3_1_out_6;

  ROM #(.addrWidth(13)) rom_1 (
    .addr({i, Funct3, X[3:0], Y[3:0], 1'b0}),
    .data({rom_1_data, rom_1_data_3[2:1], Out[3:1], rom_1_data_2[0]}));
  Pull_Resistor pull_resistor_1 (.node(pull_resistor_1_node[0]));
  ROM #(.addrWidth(13)) rom_2 (
    .addr({i, Funct3, X[7:4], Y[7:4], pull_resistor_1_node[0]}),
    .data({rom_2_data, rom_1_data_3[4:3], Out[7:4]}));
  Pull_Resistor pull_resistor_2 (.node(pull_resistor_1_node[1]));
  ROM #(.addrWidth(13)) rom_3 (
    .addr({i, Funct3, X[11:8], Y[11:8], pull_resistor_1_node[1]}),
    .data({rom_3_data, rom_1_data_3[6:5], Out[11:8]}));
  Pull_Resistor pull_resistor_3 (.node(pull_resistor_1_node[2]));
  ROM #(.addrWidth(13)) rom_4 (
    .addr({i, Funct3, X[15:12], Y[15:12], pull_resistor_1_node[2]}),
    .data({rom_4_data, rom_1_data_3[8:7], Out[15:12]}));
  Pull_Resistor pull_resistor_4 (.node(pull_resistor_1_node[3]));
  ROM #(.addrWidth(13)) rom_5 (
    .addr({i, Funct3, X[19:16], Y[19:16], pull_resistor_1_node[3]}),
    .data({rom_5_data, rom_1_data_3[10:9], Out[19:16]}));
  Pull_Resistor pull_resistor_5 (.node(pull_resistor_1_node[4]));
  ROM #(.addrWidth(13)) rom_6 (
    .addr({i, Funct3, X[23:20], Y[23:20], pull_resistor_1_node[4]}),
    .data({rom_6_data, rom_1_data_3[12:11], Out[23:20]}));
  Pull_Resistor pull_resistor_6 (.node(pull_resistor_1_node[5]));
  ROM #(.addrWidth(13)) rom_7 (
    .addr({i, Funct3, X[27:24], Y[27:24], pull_resistor_1_node[5]}),
    .data({rom_7_data, rom_1_data_3[14:13], Out[27:24]}));
  Pull_Resistor pull_resistor_7 (.node(pull_resistor_1_node[6]));
  ROM #(.addrWidth(13)) rom_8 (
    .addr({i, Funct3, X[31:28], Y[31:28], pull_resistor_1_node[6]}),
    .data({rom_8_data, rom_1_data_3[16:15], Out[31:28]}));
  Comparator #(.width(32)) comparator_1 (
    .a(X), .b(Y), .gt(comparator_1_gt), .eq(comparator_1_eq), .lt(comparator_1_lt));
  or or_1 (or_1_out, comparator_2_gt, comparator_2_eq);
  Comparator #(.mode("unsigned"), .width(32)) comparator_2 (
    .a(X), .b(Y), .gt(comparator_2_gt), .eq(comparator_2_eq), .lt(comparator_2_lt));
  // Probe on {Out[3:1], rom_1_data_2[0]}
  LED led_1 (.in(rom_1_data_3[1]));
  // Probe on Out[7:4]
  LED led_2 (.in(rom_1_data_3[3]));
  // Probe on Out[11:8]
  LED led_3 (.in(rom_1_data_3[5]));
  // Probe on Out[15:12]
  LED led_4 (.in(rom_1_data_3[7]));
  // Probe on Out[19:16]
  LED led_5 (.in(rom_1_data_3[9]));
  // Probe on Out[23:20]
  LED led_6 (.in(rom_1_data_3[11]));
  // Probe on Out[27:24]
  LED led_7 (.in(rom_1_data_3[13]));
  // Probe on Out[31:28]
  LED led_8 (.in(rom_1_data_3[15]));
  not not_1 (not_1_out, comparator_1_eq);
  or or_2 (or_2_out, comparator_1_eq, comparator_1_gt);
  LED led_9 (.in(rom_1_data_3[2]));
  LED led_10 (.in(rom_1_data_3[4]));
  LED led_11 (.in(rom_1_data_3[6]));
  LED led_12 (.in(rom_1_data_3[8]));
  LED led_13 (.in(rom_1_data_3[10]));
  LED led_14 (.in(rom_1_data_3[12]));
  LED led_15 (.in(rom_1_data_3[14]));
  LED led_16 (.in(rom_1_data_3[16]));
  Multiplexer #(.enable("false"), .select(3)) multiplexer_1 (
    .in0(comparator_1_eq), .in1(not_1_out), .in2(comparator_1_lt), .in3(comparator_1_lt),
    .in4(comparator_1_lt), .in5(or_2_out), .in6(comparator_2_lt), .in7(or_1_out), .out(Branch), .sel(Funct3));
  ALU_v3 alu_v3_1 (.out_6(alu_v3_1_out_6), .SRC_1(X), .SRC_2(Y), .I(i), .Funct3(Funct3));  // open: Branch, Zero
  ROM #(.addrWidth(17)) rom_9 (.addr({rom_1_data_3, 1'b0}), .data(pull_resistor_1_node));
  LED Carry (.in(pull_resistor_1_node[7]));
  or or_3 (or_3_out, decoder_1_out2, decoder_1_out3);
  assign controlled_buffer_1_out = or_3_out ? pull_resistor_1_node[7] : 1'bz;  // Controlled_Buffer controlled_buffer_1
  Pull_Resistor pull_resistor_8 (.node(controlled_buffer_1_out));
  or or_4 (Out[0], controlled_buffer_1_out, rom_1_data_2[0]);
  Decoder #(.enable("false"), .select(3)) decoder_1 (
    .out2(decoder_1_out2), .out3(decoder_1_out3), .sel(Funct3));  // open: out0, out1, out4, out5, out6, out7
  // Probe on Out
  // OR_Gate or_5 is placed but not wired

  // Other names for the same wires on the sheet: f[2:0] = Funct3

  // Notes on the sheet:
  //   contents of rom_1 (hex, n*v repeats v):
  //   compressed eJzVWUl26zgM3NcpuNbKkif5OIkT3/8IHwAJBijacTwsuh/pyLQeppJIVjGbMktbpG2l7bAre2kH
  //   aUdpK9ZykvYh7VPaGefyJe1b2qUs0jcI1tL2CNbSTgjW0r6QrMtW+oxgr9ER7DU6gr1GB9lbXxA8
  //   aAYIHjQDBA+aAQYP1rdPYDD4sL57CovBi/X9s5iwH+uHp7EZPFk/voDR4Mv6+hJWgzfrpxcxG/xZ
  //   /3gZu8Gj9c83YDj4tH5+C5aDV+tfb8J08Gv9+23YDp6tX7Cft5M6nyREbctJv+/l1+Uo33DUb3v9
  //   7aTftvptnvWrGZn9rDaY1Wg+2q9qNZvVrGazmS1qNqsZFjWzSItamdGiRmazqM22Pn/Lzq4hTwx5
  //   lit54mqe5WqeuJpnuZInhjxLyhOaYdhlkFbpomtHWj2QZpPMJ7W1aqWJD6it+tD1UHxAbdWHzm3x
  //   AbVVH2KrPuD7U8sDvia3PODrTMsDLa7ParS4peWBFre0PNDilpYHWtzS8hjqZTy4XsaD62U8uF7G
  //   g+tlPLhexoPrZTy43ojHbvpt37vUHH7hEFYLei01BnqtNQd0LGqO6Fj13c0xrSt0r7XGRceiMwd/
  //   ZhYX/dnWuOi11rjoWNS46FgN9TIP4HoZD66X8eB6GQ+ul/HgehkPrpfx4HojHvv5MPU3HYnhlQMS
  //   mykfSDuzxNTIu2mWj9hN4n2SLCd9oz6xm77keukouX9H0f07yu7fn4L7X8X3Kn7XSRARf/p2R+7H
  //   Y327w0wdxi1P/ORb8/Sr58V5+tjz4jx9LIAe9c+4RtxbQ/h+QzJkmMYIyJl9yMjs7913RP3qawuv
  //   NX8dE5JgZD0u5/GX8VYdyJ9NX9F8Nj8yVvvdtPAVPg6rPsLq++fxKn7WadevnIe/qz7H7t3/yU9+
  //   mQ4h7zp2+7Ayp7lw736d/IdpRUDK9hse+7vq+w2PR2RX+Xz4ddhPecxzYRh3ZOXOdB7y9H3TkeM8
  //   /V31OUZI4iffs3y+u/+055U9klYsJ6Q9M8wFIcBCg7cX5cPKWiuDrWy2cubKnyvjrey3cuzKtytD
  //   rmy5cvLKzyuj3tiTsRiwGGWIYey5MukUw9h2Zd4phrHzytRn5w0IVcQICFXECAhVxAgIVTgvQa8g
  //   +seAUvWPAaXqHxGlHe3073oGbddEZFSvY3/ovCBxtZcwbxwQYZ9/Eevf2cPjGDdGgsRWn8b2o3Ot
  //   xH+fwrTxYQTO9CSWjzGw2xg2NoekXB7G7rvz06SBHsKsaQcEfvkgVqTZ/+Na+P9ytvDaHuXMKOky
  //   eRP8ebpWTrpO3iTnZryXu3b2PZj3cudzvge7Kki6TOaJv9muCpKuE7btOofrZTy4XsaD62U8uF7G
  //   g+tlPLhexoPrZTy43oiHafabJ8OXkvjVlVP3dP6A/my7lkznF+jvRl/J0vkD+rPtWjqdX6C/G11L
  //   81qUzidwprVoM6xVXC+flHO9jAfXy3hwvYwH18t4cL2MB9f7yNpsmv1XXq9vaTrrHzSwaXaQZi9B
  //   s/dZ0DR70sCu1d0/a+Cm2RE0ezpT4DGfKYxnDJ5n0uwImv2qVvfxLa3u467Z766Z9+6zRmdkfQ0I
  //   yCXNe+8+afbhzODRMWt01vDPaHUfd83+lFbvyo40Ol9Z4z46bsoSQbPnMwPX4m2O3bvPGp01PJ8Z
  //   8Fy4d79r9pta3ce3tLqPx1OQpNmH/ZTHPBeGcdbsQ54BOdvHOU9/V32Ojcgmzf7a/zDwD355EDU=
  //   contents of rom_2 (hex, n*v repeats v):
  //   compressed eJzVWUl26zgM3NcpuNbKkif5OIkT3/8IHwAJBijacTwsuh/pyLQeppJIVjGbMktbpG2l7bAre2kH
  //   aUdpK9ZykvYh7VPaGefyJe1b2qUs0jcI1tL2CNbSTgjW0r6QrMtW+oxgr9ER7DU6gr1GB9lbXxA8
  //   aAYIHjQDBA+aAQYP1rdPYDD4sL57CovBi/X9s5iwH+uHp7EZPFk/voDR4Mv6+hJWgzfrpxcxG/xZ
  //   /3gZu8Gj9c83YDj4tH5+C5aDV+tfb8J08Gv9+23YDp6tX7Cft5M6nyREbctJv+/l1+Uo33DUb3v9
  //   7aTftvptnvWrGZn9rDaY1Wg+2q9qNZvVrGazmS1qNqsZFjWzSItamdGiRmazqM22Pn/Lzq4hTwx5
  //   lit54mqe5WqeuJpnuZInhjxLyhOaYdhlkFbpomtHWj2QZpPMJ7W1aqWJD6it+tD1UHxAbdWHzm3x
  //   AbVVH2KrPuD7U8sDvia3PODrTMsDLa7ParS4peWBFre0PNDilpYHWtzS8hjqZTy4XsaD62U8uF7G
  //   g+tlPLhexoPrZTy43ojHbvpt37vUHH7hEFYLei01BnqtNQd0LGqO6Fj13c0xrSt0r7XGRceiMwd/
  //   ZhYX/dnWuOi11rjoWNS46FgN9TIP4HoZD66X8eB6GQ+ul/HgehkPrpfx4HojHvv5MPU3HYnhlQMS
  //   mykfSDuzxNTIu2mWj9hN4n2SLCd9oz6xm77keukouX9H0f07yu7fn4L7X8X3Kn7XSRARf/p2R+7H
  //   Y327w0wdxi1P/ORb8/Sr58V5+tjz4jx9LIAe9c+4RtxbQ/h+QzJkmMYIyJl9yMjs7913RP3qawuv
  //   NX8dE5JgZD0u5/GX8VYdyJ9NX9F8Nj8yVvvdtPAVPg6rPsLq++fxKn7WadevnIe/qz7H7t3/yU9+
  //   mQ4h7zp2+7Ayp7lw736d/IdpRUDK9hse+7vq+w2PR2RX+Xz4ddhPecxzYRh3ZOXOdB7y9H3TkeM8
  //   /V31OUZI4iffs3y+u/+055U9klYsJ6Q9M8wFIcBCg7cX5cPKWiuDrWy2cubKnyvjrey3cuzKtytD
  //   rmy5cvLKzyuj3tiTsRiwGGWIYey5MukUw9h2Zd4phrHzytRn5w0IVcQICFXECAhVxAgIVTgvQa8g
  //   +seAUvWPAaXqHxGlHe3073oGbddEZFSvY3/ovCBxtZcwbxwQYZ9/Eevf2cPjGDdGgsRWn8b2o3Ot
  //   xH+fwrTxYQTO9CSWjzGw2xg2NoekXB7G7rvz06SBHsKsaQcEfvkgVqTZ/+Na+P9ytvDaHuXMKOky
  //   eRP8ebpWTrpO3iTnZryXu3b2PZj3cudzvge7Kki6TOaJv9muCpKuE7btOofrZTy4XsaD62U8uF7G
  //   g+tlPLhexoPrZTy43oiHafabJ8OXkvjVlVP3dP6A/my7lkznF+jvRl/J0vkD+rPtWjqdX6C/G11L
  //   81qUzidwprVoM6xVXC+flHO9jAfXy3hwvYwH18t4cL2MB9f7yNpsmv1XXq9vaTrrHzSwaXaQZi9B
  //   s/dZ0DR70sCu1d0/a+Cm2RE0ezpT4DGfKYxnDJ5n0uwImv2qVvfxLa3u467Z766Z9+6zRmdkfQ0I
  //   yCXNe+8+afbhzODRMWt01vDPaHUfd83+lFbvyo40Ol9Z4z46bsoSQbPnMwPX4m2O3bvPGp01PJ8Z
  //   8Fy4d79r9pta3ce3tLqPx1OQpNmH/ZTHPBeGcdbsQ54BOdvHOU9/V32Ojcgmzf7a/zDwD355EDU=
  //   contents of rom_3 (hex, n*v repeats v):
  //   compressed eJzVWUl26zgM3NcpuNbKkif5OIkT3/8IHwAJBijacTwsuh/pyLQeppJIVjGbMktbpG2l7bAre2kH
  //   aUdpK9ZykvYh7VPaGefyJe1b2qUs0jcI1tL2CNbSTgjW0r6QrMtW+oxgr9ER7DU6gr1GB9lbXxA8
  //   aAYIHjQDBA+aAQYP1rdPYDD4sL57CovBi/X9s5iwH+uHp7EZPFk/voDR4Mv6+hJWgzfrpxcxG/xZ
  //   /3gZu8Gj9c83YDj4tH5+C5aDV+tfb8J08Gv9+23YDp6tX7Cft5M6nyREbctJv+/l1+Uo33DUb3v9
  //   7aTftvptnvWrGZn9rDaY1Wg+2q9qNZvVrGazmS1qNqsZFjWzSItamdGiRmazqM22Pn/Lzq4hTwx5
  //   lit54mqe5WqeuJpnuZInhjxLyhOaYdhlkFbpomtHWj2QZpPMJ7W1aqWJD6it+tD1UHxAbdWHzm3x
  //   AbVVH2KrPuD7U8sDvia3PODrTMsDLa7ParS4peWBFre0PNDilpYHWtzS8hjqZTy4XsaD62U8uF7G
  //   g+tlPLhexoPrZTy43ojHbvpt37vUHH7hEFYLei01BnqtNQd0LGqO6Fj13c0xrSt0r7XGRceiMwd/
  //   ZhYX/dnWuOi11rjoWNS46FgN9TIP4HoZD66X8eB6GQ+ul/HgehkPrpfx4HojHvv5MPU3HYnhlQMS
  //   mykfSDuzxNTIu2mWj9hN4n2SLCd9oz6xm77keukouX9H0f07yu7fn4L7X8X3Kn7XSRARf/p2R+7H
  //   Y327w0wdxi1P/ORb8/Sr58V5+tjz4jx9LIAe9c+4RtxbQ/h+QzJkmMYIyJl9yMjs7913RP3qawuv
  //   NX8dE5JgZD0u5/GX8VYdyJ9NX9F8Nj8yVvvdtPAVPg6rPsLq++fxKn7WadevnIe/qz7H7t3/yU9+
  //   mQ4h7zp2+7Ayp7lw736d/IdpRUDK9hse+7vq+w2PR2RX+Xz4ddhPecxzYRh3ZOXOdB7y9H3TkeM8
  //   /V31OUZI4iffs3y+u/+055U9klYsJ6Q9M8wFIcBCg7cX5cPKWiuDrWy2cubKnyvjrey3cuzKtytD
  //   rmy5cvLKzyuj3tiTsRiwGGWIYey5MukUw9h2Zd4phrHzytRn5w0IVcQICFXECAhVxAgIVTgvQa8g
  //   +seAUvWPAaXqHxGlHe3073oGbddEZFSvY3/ovCBxtZcwbxwQYZ9/Eevf2cPjGDdGgsRWn8b2o3Ot
  //   xH+fwrTxYQTO9CSWjzGw2xg2NoekXB7G7rvz06SBHsKsaQcEfvkgVqTZ/+Na+P9ytvDaHuXMKOky
  //   eRP8ebpWTrpO3iTnZryXu3b2PZj3cudzvge7Kki6TOaJv9muCpKuE7btOofrZTy4XsaD62U8uF7G
  //   g+tlPLhexoPrZTy43oiHafabJ8OXkvjVlVP3dP6A/my7lkznF+jvRl/J0vkD+rPtWjqdX6C/G11L
  //   81qUzidwprVoM6xVXC+flHO9jAfXy3hwvYwH18t4cL2MB9f7yNpsmv1XXq9vaTrrHzSwaXaQZi9B
  //   s/dZ0DR70sCu1d0/a+Cm2RE0ezpT4DGfKYxnDJ5n0uwImv2qVvfxLa3u467Z766Z9+6zRmdkfQ0I
  //   yCXNe+8+afbhzODRMWt01vDPaHUfd83+lFbvyo40Ol9Z4z46bsoSQbPnMwPX4m2O3bvPGp01PJ8Z
  //   8Fy4d79r9pta3ce3tLqPx1OQpNmH/ZTHPBeGcdbsQ54BOdvHOU9/V32Ojcgmzf7a/zDwD355EDU=
  //   contents of rom_4 (hex, n*v repeats v):
  //   compressed eJzVWUl26zgM3NcpuNbKkif5OIkT3/8IHwAJBijacTwsuh/pyLQeppJIVjGbMktbpG2l7bAre2kH
  //   aUdpK9ZykvYh7VPaGefyJe1b2qUs0jcI1tL2CNbSTgjW0r6QrMtW+oxgr9ER7DU6gr1GB9lbXxA8
  //   aAYIHjQDBA+aAQYP1rdPYDD4sL57CovBi/X9s5iwH+uHp7EZPFk/voDR4Mv6+hJWgzfrpxcxG/xZ
  //   /3gZu8Gj9c83YDj4tH5+C5aDV+tfb8J08Gv9+23YDp6tX7Cft5M6nyREbctJv+/l1+Uo33DUb3v9
  //   7aTftvptnvWrGZn9rDaY1Wg+2q9qNZvVrGazmS1qNqsZFjWzSItamdGiRmazqM22Pn/Lzq4hTwx5
  //   lit54mqe5WqeuJpnuZInhjxLyhOaYdhlkFbpomtHWj2QZpPMJ7W1aqWJD6it+tD1UHxAbdWHzm3x
  //   AbVVH2KrPuD7U8sDvia3PODrTMsDLa7ParS4peWBFre0PNDilpYHWtzS8hjqZTy4XsaD62U8uF7G
  //   g+tlPLhexoPrZTy43ojHbvpt37vUHH7hEFYLei01BnqtNQd0LGqO6Fj13c0xrSt0r7XGRceiMwd/
  //   ZhYX/dnWuOi11rjoWNS46FgN9TIP4HoZD66X8eB6GQ+ul/HgehkPrpfx4HojHvv5MPU3HYnhlQMS
  //   mykfSDuzxNTIu2mWj9hN4n2SLCd9oz6xm77keukouX9H0f07yu7fn4L7X8X3Kn7XSRARf/p2R+7H Y327w0wd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
  //   contents of rom_5 (hex, n*v repeats v):
  //   compressed eJzVWUl26zgM3NcpuNbKkif5OIkT3/8IHwAJBijacTwsuh/pyLQeppJIVjGbMktbpG2l7bAre2kH
  //   aUdpK9ZykvYh7VPaGefyJe1b2qUs0jcI1tL2CNbSTgjW0r6QrMtW+oxgr9ER7DU6gr1GB9lbXxA8
  //   aAYIHjQDBA+aAQYP1rdPYDD4sL57CovBi/X9s5iwH+uHp7EZPFk/voDR4Mv6+hJWgzfrpxcxG/xZ
  //   /3gZu8Gj9c83YDj4tH5+C5aDV+tfb8J08Gv9+23YDp6tX7Cft5M6nyREbc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
  //   contents of rom_6 (hex, n*v repeats v):
  //   compressed eJzVWUl26zgM3NcpuNbKkif5OIkT3/8IHwAJBijacTwsuh/pyLQeppJIVjGbMktbpG2l7bAre2kH
  //   aUdpK9ZykvYh7VPaGefyJe1b2qUs0jcI1tL2CNbSTgjW0r6QrMtW+oxgr9ER7DU6gr1GB9lbXxA8
  //   aAYIHjQDBA+aAQYP1rdPYDD4sL57CovBi/X9s5iwH+uHp7EZPFk/voDR4Mv6+hJWgzfrpxcxG/xZ
  //   /3gZu8Gj9c83YDj4tH5+C5aDV+tfb8J08Gv9+23YDp6tX7Cft5M6nyREbc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
  //   contents of rom_7 (hex, n*v repeats v):
  //   compressed eJzVWUl26zgM3NcpuNbKkif5OIkT3/8IHwAJBijacTwsuh/pyLQeppJIVjGbMktbpG2l7bAre2kH
  //   aUdpK9ZykvYh7VPaGefyJe1b2qUs0jcI1tL2CNbSTgjW0r6QrMtW+oxgr9ER7DU6gr1GB9lbXxA8
  //   aAYIHjQDBA+aAQYP1rdPYDD4sL57CovBi/X9s5iwH+uHp7EZPFk/voDR4Mv6+hJWgzfrpxcxG/xZ
  //   /3gZu8Gj9c83YDj4tH5+C5aDV+tfb8J08Gv9+23YDp6tX7Cft5M6nyREbc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
  //   contents of rom_8 (hex, n*v repeats v):
  //   compressed eJytWVl2wyAM/Ncp+PZXvGU5TtvU9z9CJYEUMcShWZ5pbWprkMYGpOkhjXxMfMx8LLSklY8jHyc+
  //   znROFz6++Pjm44d+0pWPXz62NHE7ULDmY6VgzceFgjUfV6qs08xtpGAvo1Owl9Ep2MvoBPbaJgoI
  //   4gEFBPGAAoJ4QA2CtvkFDhoMbctLXDQo2tZXOUEcbceXuWmQtJ3e4KjB0nZ+i6sGTdvlTc4aPG1f
  //   b3PXIGr7/gCHDaa2n49w2aBqu36I0wZX2+/HuG2QtW20jvNwSOM6jPz7Ip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
  //   Cin
  //   Cin
  //   Cin
  //   adder
  //   adder
  //   adder
  //   G
  //   G
  //   G
  //   G
  //   G
  //   G
  //   G
  //   G
  //   P
  //   out
  //   P
  //   out
  //   P
  //   out
  //   P
  //   out
  //   P
  //   P
  //   P
  //   P
  //   contents of rom_9 (hex, n*v repeats v):
  //   compressed eJztXWGO4ziv/K9T8AhybMfycWI7vv8RXkiOCKExEvwwnyNss5BCUKRr1FxPQVuLJdCRIg2fj34P
  //   4UEPGj8f/R5D/DxhFv/UP59PNNH8+ej3HJ70pOXz0e9FnjOb/tQ/n8cfP/9vz5nFyp//15+fKNH6
  //   +ej3Gl70ou3z0e9NnjNLf+qfz3fa6fh89PsIb3rT+fno9ynPme1/6p/Pf/78vz1nlip//l9//s/3
  //   ///9+/9f//y/PWcWb/rn9/73P3xe/AeDwMgQhgcxRoGRMeu1jEW/pp+IMQ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
  //   clu
endmodule

module ALU_v7 (
  input  [31:0] Y,
  input  [31:0] X,
  input  [2:0] Funct3,
  input  I,
  input  in_5,
  output Branch,
  output out_7,
  output [31:0] out_8
);

  wire comparator_1_eq, comparator_1_gt, comparator_1_lt, comparator_2_eq, comparator_2_gt, comparator_2_lt,
       comparator_3_eq, not_2_out, or_2_out, or_3_out;
  wire [7:0] rom_1_data;
  wire [7:5] rom_2_data, rom_3_data, rom_4_data;
  wire [7:6] rom_5_data, rom_6_data;
  wire [31:0] alu_ref_1_out_6, register_1_q, register_2_q;

  // NOT_Gate not_1 is placed but not wired
  ROM #(.addrWidth(17)) rom_1 (
    .addr({2'b00, Funct3, Y[4:0], X[4:0], I, 1'b0}), .data({rom_1_data[7:5], out_8[4:1], rom_1_data[0]}));
  ROM #(.addrWidth(17)) rom_2 (
    .addr({2'b00, Funct3, Y[9:5], X[9:5], I, rom_1_data[5]}), .data({rom_2_data, out_8[9:5]}));
  ROM #(.addrWidth(17)) rom_3 (
    .addr({2'b00, Funct3, Y[14:10], X[14:10], I, rom_2_data[5]}), .data({rom_3_data, out_8[14:10]}));
  ROM #(.addrWidth(17)) rom_4 (
    .addr({2'b00, Funct3, Y[19:15], X[19:15], I, rom_3_data[5]}), .data({rom_4_data, out_8[19:15]}));
  ROM #(.addrWidth(17)) rom_5 (
    .addr({Funct3, Y[25:20], X[25:20], I, rom_4_data[5]}), .data({rom_5_data, out_8[25:20]}));
  ROM #(.addrWidth(17)) rom_6 (
    .addr({Funct3, Y[31:26], X[31:26], I, rom_5_data[6]}), .data({rom_6_data, out_8[31:26]}));
  ALU_ref alu_ref_1 (.I(I), .SRC_1(X), .SRC_2(Y), .Funct3(Funct3), .out_6(alu_ref_1_out_6));  // open: Zero, Branch
  Comparator #(.width(32)) comparator_1 (
    .a(X), .b(Y), .gt(comparator_1_gt), .eq(comparator_1_eq), .lt(comparator_1_lt));
  Comparator #(.mode("unsigned"), .width(32)) comparator_2 (
    .a(X), .b(Y), .gt(comparator_2_gt), .eq(comparator_2_eq), .lt(comparator_2_lt));
  or or_1 (out_8[0], rom_6_data[7], rom_1_data[0]);
  or or_2 (or_2_out, comparator_2_gt, comparator_2_eq);
  // Probe on out_8
  not not_2 (not_2_out, comparator_1_eq);
  Multiplexer #(.enable("false"), .select(3)) multiplexer_1 (
    .in0(comparator_1_eq), .in1(not_2_out), .in2(1'b0), .in3(1'b0), .in4(comparator_1_lt), .in5(or_3_out),
    .in6(comparator_2_lt), .in7(or_2_out), .out(Branch), .sel(Funct3));
  or or_3 (or_3_out, comparator_1_eq, comparator_1_gt);
  // Probe on alu_ref_1_out_6
  Register #(.width(32)) register_1 (.D(alu_ref_1_out_6), .Q(register_1_q), .clk(in_5));  // open: en, clr
  Register #(.width(32)) register_2 (.D(out_8), .Q(register_2_q), .clk(in_5));  // open: en, clr
  not not_3 (out_7, comparator_3_eq);
  Comparator #(.width(32)) comparator_3 (.a(register_1_q), .b(register_2_q), .eq(comparator_3_eq));  // open: gt, lt
  // OR_Gate or_4 is placed but not wired

  // Notes on the sheet:
  //   contents of rom_1 (hex, n*v repeats v):
  //   compressed eJzF3Fty27gWQNF/jALf+rIeluXh2I4z/yFcnL0PSIGiTNZNUl3VblGPUNTiBgQp7n6px/pSz7/b
  //   xSk2y6me2TrXS2yVS31l67VeY6tc6xtbb/UWW+VW39l6rx+xVT7qJ1uf9Su2ylf9xdav+h1b5bv+
  //   Zqs940tslnZxPHolLk9eK7Fx7lfbxsWrJTZe+9W2cfVqiY23frVt3LxaYuO9X20bH14tsfHZr7aN
  //   L6+W2PjVr7aNb6+W2Pjdr/6upxevlnBrfOfvuISyBF2oBl07/hJ0gRp0jb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
  //   contents of rom_2 (hex, n*v repeats v):
  //   compressed eJzF3Fty27gWQNF/jALf+rIeluXh2I4z/yFcnL0PSIGiTNZNUl3VblGPUNTiBgQp7n6px/pSz7/b
  //   xSk2y6me2TrXS2yVS31l67VeY6tc6xtbb/UWW+VW39l6rx+xVT7qJ1uf9Su2ylf9xdav+h1b5bv+
  //   Zqs940tslnZxPHolLk9eK7Fx7lfbxsWrJTZe+9W2cfVqiY23frVt3LxaYuO9X20bH14tsfHZr7aN
  //   L6+W2PjVr7aNb6+W2Pjdr/6upxevlnBrfOfvuISyBF2oBl07/hJ0gRp0jb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
  //   contents of rom_3 (hex, n*v repeats v):
  //   compressed eJzF3Fty27gWQNF/jALf+rIeluXh2I4z/yFcnL0PSIGiTNZNUl3VblGPUNTiBgQp7n6px/pSz7/b
  //   xSk2y6me2TrXS2yVS31l67VeY6tc6xtbb/UWW+VW39l6rx+xVT7qJ1uf9Su2ylf9xdav+h1b5bv+
  //   Zqs940tslnZxPHolLk9eK7Fx7lfbxsWrJTZe+9W2cfVqiY23frVt3LxaYuO9X20bH14tsfHZr7aN
  //   L6+W2PjVr7aNb6+W2Pjdr/6upxevlnBrfOfvuISyBF2oBl07/hJ0gRp0jb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
  //   contents of rom_4 (hex, n*v repeats v):
  //   compressed eJzF3Fty27gWQNF/jALf+rIeluXh2I4z/yFcnL0PSIGiTNZNUl3VblGPUNTiBgQp7n6px/pSz7/b
  //   xSk2y6me2TrXS2yVS31l67VeY6tc6xtbb/UWW+VW39l6rx+xVT7qJ1uf9Su2ylf9xdav+h1b5bv+
  //   Zqs940tslnZxPHolLk9eK7Fx7lfbxsWrJTZe+9W2cfVqiY23frVt3LxaYuO9X20bH14tsfHZr7aN
  //   L6+W2PjVr7aNb6+W2Pjdr/6upxevlnBrfOfvuISyBF2oBl07/hJ0gRp0jb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
  //   contents of rom_5 (hex, n*v repeats v):
  //   compressed eJzt3V1620a2htF7jALXujIpWZaHYzvx/IdwuL+1iz8wKCItpOPuPs+T2IBEUzKx+FahBNKf5sP8
  //   af7y8/TbsTan4/ycref5pbaml/lztj7Pr7U1vc5fsvVlfqut6W3+mq2v87famr7N37P1ff5RW9OP
  //   +Y9s/TH/WVvTn/PPbJ2+4qfanE6/HQ526vejvak2nsfuaePF7lQbn8fuaePV7lQbX8buaePN7lQb
  //   X8fuaeOb3ak2vo/d08YPu1Nt/DF2Txt/2p1q4+fY/TkfP9mdThvHQ+/Wxt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
  //   contents of rom_6 (hex, n*v repeats v):
  //   compressed eJzt3UF220iWhtE5VoGxRiYly/JyMu30/pfQfP99QZAUKCJLqEp3V5+TaQMUTcnQxReBEEl/mQ/z
  //   l/nbr9Nvx9qcjvNztp7nl9qaXuav2fo6v9bW9Dp/y9a3+a22prf5e7a+z3/U1vTH/Ge2/px/1Nb0
  //   Y/6ZrZ/zX7U1/TX/ytbpM36pzen02+Fgp34/2ptq43nsnjZe7E618XXsnjZe7U618W3snjbe7E61
  //   8X3snjb+sDvVxp9j97Txw+5UGz/H7mnjL7tTbfwau7/m4xe702njeOjd2j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
endmodule

module ALU_v8 (
  input  [31:0] Y,
  input  [31:0] X,
  input  [2:0] Funct3,
  input  I,
  input  in_5,
  output [31:0] out_6,
  output out_7,
  output Branch
);

  wire comparator_1_eq, comparator_1_gt, comparator_1_lt, comparator_2_eq, comparator_2_gt, comparator_2_lt,
       comparator_3_eq, multiplexer_1_out, not_1_out, not_2_out, not_3_out, or_1_out, or_2_out, register_3_q,
       xnor_1_out;
  wire [7:0] rom_1_data;
  wire [7:2] rom_7_data;
  wire [7:5] rom_2_data, rom_3_data, rom_4_data, rom_5_data, rom_6_data;
  wire [31:0] alu_ref_1_out_6, register_1_q, register_2_q;

  // AND_Gate and_1 is placed but not wired
  ROM #(.addrWidth(17)) rom_1 (
    .addr({1'b0, Y[4:0], X[4:0], Funct3, 1'b1, I, 1'b0}), .data({rom_1_data[7:5], out_6[4:1], rom_1_data[0]}));
  ROM #(.addrWidth(17)) rom_2 (
    .addr({1'b0, Y[9:5], X[9:5], Funct3, rom_1_data[6], I, rom_1_data[5]}), .data({rom_2_data, out_6[9:5]}));
  ROM #(.addrWidth(17)) rom_3 (
    .addr({1'b0, Y[14:10], X[14:10], Funct3, rom_2_data[6], I, rom_2_data[5]}),
    .data({rom_3_data, out_6[14:10]}));
  ROM #(.addrWidth(17)) rom_4 (
    .addr({1'b0, Y[19:15], X[19:15], Funct3, rom_3_data[6], I, rom_3_data[5]}),
    .data({rom_4_data, out_6[19:15]}));
  ROM #(.addrWidth(17)) rom_5 (
    .addr({1'b0, Y[24:20], X[24:20], Funct3, rom_4_data[6], I, rom_4_data[5]}),
    .data({rom_5_data, out_6[24:20]}));
  ROM #(.addrWidth(17)) rom_6 (
    .addr({1'b0, Y[29:25], X[29:25], Funct3, rom_5_data[6], I, rom_5_data[5]}),
    .data({rom_6_data, out_6[29:25]}));
  ROM #(.addrWidth(17)) rom_7 (
    .addr({4'b0000, Y[31:30], 3'b000, X[31:30], Funct3, rom_6_data[6], I, rom_6_data[5]}),
    .data({rom_7_data[7], Branch, rom_7_data[5:2], out_6[31:30]}));
  Comparator #(.width(32)) comparator_1 (
    .a(X), .b(Y), .gt(comparator_1_gt), .eq(comparator_1_eq), .lt(comparator_1_lt));
  Comparator #(.mode("unsigned"), .width(32)) comparator_2 (
    .a(X), .b(Y), .gt(comparator_2_gt), .eq(comparator_2_eq), .lt(comparator_2_lt));
  or or_1 (or_1_out, comparator_2_gt, comparator_2_eq);
  not not_1 (not_1_out, comparator_1_eq);
  or or_2 (or_2_out, comparator_1_eq, comparator_1_gt);
  Multiplexer #(.enable("false"), .select(3)) multiplexer_1 (
    .in0(comparator_1_eq), .in1(not_1_out), .in2(1'b0), .in3(1'b0), .in4(comparator_1_lt), .in5(or_2_out),
    .in6(comparator_2_lt), .in7(or_1_out), .out(multiplexer_1_out), .sel(Funct3));
  ALU_ref alu_ref_1 (.I(I), .SRC_1(X), .SRC_2(Y), .Funct3(Funct3), .out_6(alu_ref_1_out_6));  // open: Zero, Branch
  or or_3 (out_6[0], rom_7_data[5], rom_1_data[0]);
  xnor xnor_1 (xnor_1_out, Branch, multiplexer_1_out);
  not not_2 (not_2_out, xnor_1_out);
  Register #(.trigger("falling"), .width(32)) register_1 (
    .D(alu_ref_1_out_6), .Q(register_1_q), .clk(in_5));  // open: en, clr
  Register #(.trigger("falling"), .width(32)) register_2 (.D(out_6), .Q(register_2_q), .clk(in_5));  // open: en, clr
  not not_3 (not_3_out, comparator_3_eq);
  Comparator #(.width(32)) comparator_3 (.a(register_1_q), .b(register_2_q), .eq(comparator_3_eq));  // open: gt, lt
  Register #(.trigger("falling"), .width(1)) register_3 (.D(not_2_out), .Q(register_3_q), .clk(in_5));  // open: en, clr
  or or_4 (out_7, not_3_out, register_3_q);

  // Notes on the sheet:
  //   contents of rom_1 (hex, n*v repeats v):
  //   compressed eJyl3dFyIjuQBNB3vqKf75OBBuzPsT3m/z/hUplVKpVQFYogYmOdu5ceqz1uziRqtT624/axne/b
  //   /rHtR/nft/vh67+P7fSxxf91mP3/jqfHS/f/Hod1aTvJH3rQr9sn/p/X/yQd8X8dLDxeccarHl8P
  //   8rV/7Yn/l4XDedvxav166F97ttdq2LfLYccrL3h1e60cZa/VcNmu8qqDfg1juNh4GR6vuOFVj68H
  //   +dq/9mp/LsPhtn3i1fo1jPdmr7WwfR0+8covvLof76e9VsPX9i2vOujXMI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
  //   contents of rom_2 (hex, n*v repeats v):
  //   compressed eJytnU1iI6uyhOe1ihrfkfVn2cux29b+l3CVEZFAZpEcDTx4R3FfFy2wBV8HoYS3/bS/7ZfHfn3b
  //   ryf77/2xXf/3/B//e+q3/Tz8Z4v/c/j/tQYH0f+u037Gez1fN3v9wP/z/X+mTvxfLrbzfsHTet3G
  //   Z8/+rMRlv24XPHnF0+3ZZ6uLPytx3W/21KbX0Icr39rF84l3PPV83ex1fPbmfy/F9r7f8bReQ3/f
  //   /VmJ+/6x3fHkB54e+3v3Z13sn/bUptfQhw/vL8XziS889Xzd7HV89tP/Xo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
  //   contents of rom_3 (hex, n*v repeats v):
  //   compressed eJytnU1iI6uyhOe1ihrfkfVn2cux29b+l3CVEZFAZpEcDTx4R3FfFy2wBV8HoYS3/bS/7ZfHfn3b
  //   ryf77/2xXf/3/B//e+q3/Tz8Z4v/c/j/tQYH0f+u037Gez1fN3v9wP/z/X+mTvxfLrbzfsHTet3G
  //   Z8/+rMRlv24XPHnF0+3ZZ6uLPytx3W/21KbX0Icr39rF84l3PPV83ex1fPbmfy/F9r7f8bReQ3/f
  //   /VmJ+/6x3fHkB54e+3v3Z13sn/bUptfQhw/vL8XziS889Xzd7HV89tP/Xo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
  //   contents of rom_4 (hex, n*v repeats v):
  //   compressed eJytnU1iI6uyhOe1ihrfkfVn2cux29b+l3CVEZFAZpEcDTx4R3FfFy2wBV8HoYS3/bS/7ZfHfn3b
  //   ryf77/2xXf/3/B//e+q3/Tz8Z4v/c/j/tQYH0f+u037Gez1fN3v9wP/z/X+mTvxfLrbzfsHTet3G
  //   Z8/+rMRlv24XPHnF0+3ZZ6uLPytx3W/21KbX0Icr39rF84l3PPV83ex1fPbmfy/F9r7f8bReQ3/f
  //   /VmJ+/6x3fHkB54e+3v3Z13sn/bUptfQhw/vL8XziS889Xzd7HV89tP/Xo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
  //   contents of rom_5 (hex, n*v repeats v):
  //   compressed eJytnU1iI6uyhOe1ihrfkfVn2cux29b+l3CVEZFAZpEcDTx4R3FfFy2wBV8HoYS3/bS/7ZfHfn3b
  //   ryf77/2xXf/3/B//e+q3/Tz8Z4v/c/j/tQYH0f+u037Gez1fN3v9wP/z/X+mTvxfLrbzfsHTet3G
  //   Z8/+rMRlv24XPHnF0+3ZZ6uLPytx3W/21KbX0Icr39rF84l3PPV83ex1fPbmfy/F9r7f8bReQ3/f
  //   /VmJ+/6x3fHkB54e+3v3Z13sn/bUptfQhw/vL8XziS889Xzd7HV89tP/Xo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
  //   contents of rom_6 (hex, n*v repeats v):
  //   compressed eJytnU1iI6uyhOe1ihrfkfVn2cux29b+l3CVEZFAZpEcDTx4R3FfFy2wBV8HoYS3/bS/7ZfHfn3b
  //   ryf77/2xXf/3/B//e+q3/Tz8Z4v/c/j/tQYH0f+u037Gez1fN3v9wP/z/X+mTvxfLrbzfsHTet3G
  //   Z8/+rMRlv24XPHnF0+3ZZ6uLPytx3W/21KbX0Icr39rF84l3PPV83ex1fPbmfy/F9r7f8bReQ3/f
  //   /VmJ+/6x3fHkB54e+3v3Z13sn/bUptfQhw/vL8XziS889Xzd7HV89tP/Xo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
  //   contents of rom_7 (hex, n*v repeats v):
  //   compressed eJytnUuW87iOhOdchcZ39MvPzOWk0/b+l9BGBAACfEgud57TXYlbZUqmJeoTAALxb1mXf8v6XE7/
  //   ltMq/zw/y+l/r//xv5f9bzmEf5T8P8O/8wGdUY+1LgeeazkU+fuFf3n5n1gr/5cZ5bAc8Wn9W/S/
  //   HuQfGHlQ48CBx3LCJ48L/+Ig8fNHNY78/Gk5Y8TrL0bgX75O285ORr1mcJIZnOrkXh/nkPNyKWcc
  //   5YIj+ZxeJz/bnNS4LFf5VNG/SzenS6Fx4X+6Ll/45LXwb/f5K77d1/+u+p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
endmodule

module ALU_v20 (
  input  [2:0] Funct3,
  input  I,
  input  [1:0] ALU_op,
  input  [31:0] Y,
  input  [31:0] X,
  output [31:0] out_6,
  output Branch
);

  wire and_2_out, or_1_out;
  wire [2:0] and_1_out, multiplexer_1_out, rom_1_data, rom_3_data, rom_4_data, rom_5_data, rom_6_data;
  wire [7:0] rom_1_data_2;
  wire [7:2] rom_7_data;
  wire [7:7] rom_2_data, rom_3_data_2, rom_4_data_2, rom_5_data_2, rom_6_data_2;

  or or_1 (or_1_out, ALU_op[0], ALU_op[1]);
  and and_1 (and_1_out[1], I, ~or_1_out);  // AND_Gate
  Multiplexer #(.enable("false"), .width(3)) multiplexer_1 (
    .in0(Funct3), .in1(3'b000), .out(multiplexer_1_out), .sel(and_2_out));
  and and_2 (and_2_out, ALU_op[0], ~ALU_op[1]);  // AND_Gate
  ROM #(.addrWidth(17)) rom_1 (
    .addr({1'b0, Y[4:0], X[4:0], multiplexer_1_out, 1'b1, and_1_out[1], 1'b0}),
    .data({rom_1_data_2[7], rom_1_data[2], rom_1_data[0], out_6[4:1], rom_1_data_2[0]}));
  ROM #(.addrWidth(17)) rom_2 (
    .addr({1'b0, Y[9:5], X[9:5], multiplexer_1_out, rom_1_data[2], and_1_out[1], rom_1_data[0]}),
    .data({rom_2_data[7], and_1_out[2], and_1_out[0], out_6[9:5]}));
  ROM #(.addrWidth(17)) rom_3 (
    .addr({1'b0, Y[14:10], X[14:10], multiplexer_1_out, and_1_out}),
    .data({rom_3_data_2[7], rom_3_data[2], rom_3_data[0], out_6[14:10]}));
  ROM #(.addrWidth(17)) rom_4 (
    .addr({1'b0, Y[19:15], X[19:15], multiplexer_1_out, rom_3_data[2], and_1_out[1], rom_3_data[0]}),
    .data({rom_4_data_2[7], rom_4_data[2], rom_4_data[0], out_6[19:15]}));
  ROM #(.addrWidth(17)) rom_5 (
    .addr({1'b0, Y[24:20], X[24:20], multiplexer_1_out, rom_4_data[2], and_1_out[1], rom_4_data[0]}),
    .data({rom_5_data_2[7], rom_5_data[2], rom_5_data[0], out_6[24:20]}));
  ROM #(.addrWidth(17)) rom_6 (
    .addr({1'b0, Y[29:25], X[29:25], multiplexer_1_out, rom_5_data[2], and_1_out[1], rom_5_data[0]}),
    .data({rom_6_data_2[7], rom_6_data[2], rom_6_data[0], out_6[29:25]}));
  ROM #(.addrWidth(17)) rom_7 (
    .addr({4'b0000, Y[31:30], 3'b000, X[31:30], multiplexer_1_out, rom_6_data[2], and_1_out[1], rom_6_data[0]}),
    .data({rom_7_data[7], Branch, rom_7_data[5:2], out_6[31:30]}));
  or or_2 (out_6[0], rom_7_data[5], rom_1_data_2[0]);

  // Notes on the sheet:
  //   Funct3
  //   i
  //   contents of rom_1 (hex, n*v repeats v):
  //   compressed eJyl3dFyIjuQBNB3vqKf75OBBuzPsT3m/z/hUplVKpVQFYogYmOdu5ceqz1uziRqtT624/axne/b
  //   /rHtR/nft/vh67+P7fSxxf91mP3/jqfHS/f/Hod1aTvJH3rQr9sn/p/X/yQd8X8dLDxeccarHl8P
  //   8rV/7Yn/l4XDedvxav166F97ttdq2LfLYccrL3h1e60cZa/VcNmu8qqDfg1juNh4GR6vuOFVj68H
  //   +dq/9mp/LsPhtn3i1fo1jPdmr7WwfR0+8covvLof76e9VsPX9i2vOujXMI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
  //   contents of rom_2 (hex, n*v repeats v):
  //   compressed eJytnU1iI6uyhOe1ihrfkfVn2cux29b+l3CVEZFAZpEcDTx4R3FfFy2wBV8HoYS3/bS/7ZfHfn3b
  //   ryf77/2xXf/3/B//e+q3/Tz8Z4v/c/j/tQYH0f+u037Gez1fN3v9wP/z/X+mTvxfLrbzfsHTet3G
  //   Z8/+rMRlv24XPHnF0+3ZZ6uLPytx3W/21KbX0Icr39rF84l3PPV83ex1fPbmfy/F9r7f8bReQ3/f
  //   /VmJ+/6x3fHkB54e+3v3Z13sn/bUptfQhw/vL8XziS889Xzd7HV89tP/Xo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
  //   contents of rom_3 (hex, n*v repeats v):
  //   compressed eJytnU1iI6uyhOe1ihrfkfVn2cux29b+l3CVEZFAZpEcDTx4R3FfFy2wBV8HoYS3/bS/7ZfHfn3b
  //   ryf77/2xXf/3/B//e+q3/Tz8Z4v/c/j/tQYH0f+u037Gez1fN3v9wP/z/X+mTvxfLrbzfsHTet3G
  //   Z8/+rMRlv24XPHnF0+3ZZ6uLPytx3W/21KbX0Icr39rF84l3PPV83ex1fPbmfy/F9r7f8bReQ3/f
  //   /VmJ+/6x3fHkB54e+3v3Z13sn/bUptfQhw/vL8XziS889Xzd7HV89tP/Xo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
  //   contents of rom_4 (hex, n*v repeats v):
  //   compressed eJytnU1iI6uyhOe1ihrfkfVn2cux29b+l3CVEZFAZpEcDTx4R3FfFy2wBV8HoYS3/bS/7ZfHfn3b
  //   ryf77/2xXf/3/B//e+q3/Tz8Z4v/c/j/tQYH0f+u037Gez1fN3v9wP/z/X+mTvxfLrbzfsHTet3G
  //   Z8/+rMRlv24XPHnF0+3ZZ6uLPytx3W/21KbX0Icr39rF84l3PPV83ex1fPbmfy/F9r7f8bReQ3/f
  //   /VmJ+/6x3fHkB54e+3v3Z13sn/bUptfQhw/vL8XziS889Xzd7HV89tP/Xo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
  //   contents of rom_5 (hex, n*v repeats v):
  //   compressed eJytnU1iI6uyhOe1ihrfkfVn2cux29b+l3CVEZFAZpEcDTx4R3FfFy2wBV8HoYS3/bS/7ZfHfn3b
  //   ryf77/2xXf/3/B//e+q3/Tz8Z4v/c/j/tQYH0f+u037Gez1fN3v9wP/z/X+mTvxfLrbzfsHTet3G
  //   Z8/+rMRlv24XPHnF0+3ZZ6uLPytx3W/21KbX0Icr39rF84l3PPV83ex1fPbmfy/F9r7f8bReQ3/f
  //   /VmJ+/6x3fHkB54e+3v3Z13sn/bUptfQhw/vL8XziS889Xzd7HV89tP/Xo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
  //   contents of rom_6 (hex, n*v repeats v):
  //   compressed eJytnU1iI6uyhOe1ihrfkfVn2cux29b+l3CVEZFAZpEcDTx4R3FfFy2wBV8HoYS3/bS/7ZfHfn3b
  //   ryf77/2xXf/3/B//e+q3/Tz8Z4v/c/j/tQYH0f+u037Gez1fN3v9wP/z/X+mTvxfLrbzfsHTet3G
  //   Z8/+rMRlv24XPHnF0+3ZZ6uLPytx3W/21KbX0Icr39rF84l3PPV83ex1fPbmfy/F9r7f8bReQ3/f
  //   /VmJ+/6x3fHkB54e+3v3Z13sn/bUptfQhw/vL8XziS889Xzd7HV89tP/Xo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
  //   contents of rom_7 (hex, n*v repeats v):
  //   compressed eJytnUuW87iOhOdchcZ39MvPzOWk0/b+l9BGBAACfEgud57TXYlbZUqmJeoTAALxb1mXf8v6XE7/
  //   ltMq/zw/y+l/r//xv5f9bzmEf5T8P8O/8wGdUY+1LgeeazkU+fuFf3n5n1gr/5cZ5bAc8Wn9W/S/
  //   HuQfGHlQ48CBx3LCJ48L/+Ig8fNHNY78/Gk5Y8TrL0bgX75O285ORr1mcJIZnOrkXh/nkPNyKWcc
  //   5YIj+ZxeJz/bnNS4LFf5VNG/SzenS6Fx4X+6Ll/45LXwb/f5K77d1/+u+p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
endmodule

module ALU_ref (
  input  I,
  input  [31:0] SRC_1,
  input  [31:0] SRC_2,
  input  [2:0] Funct3,
  output Zero,
  output [31:0] out_6,
  output Branch
);

  wire comparator_1_lt, comparator_2_lt, comparator_3_eq, comparator_3_gt, comparator_3_lt, comparator_4_eq,
       comparator_4_gt, comparator_4_lt, not_1_out, or_2_out, or_3_out;
  wire [31:0] adder_1_out, and_1_out, bit_extender_1_out, bit_extender_2_out, multiplexer_1_out, or_1_out,
       subtractor_1_out, xor_1_out;

  Adder #(.width(32)) adder_1 (.a(SRC_1), .b(SRC_2), .out(adder_1_out));  // open: cin, cout
  Subtractor #(.width(32)) subtractor_1 (.a(SRC_1), .b(SRC_2), .out(subtractor_1_out));  // open: bin, bout
  Comparator #(.width(32)) comparator_1 (.a(SRC_1), .b(SRC_2), .lt(comparator_1_lt));  // open: gt, eq
  Comparator #(.mode("unsigned"), .width(32)) comparator_2 (
    .a(SRC_1), .b(SRC_2), .lt(comparator_2_lt));  // open: gt, eq
  assign xor_1_out = SRC_1 ^ SRC_2;  // XOR_Gate xor_1, 32 bits wide
  assign or_1_out = SRC_1 | SRC_2;  // OR_Gate or_1, 32 bits wide
  assign and_1_out = SRC_1 & SRC_2;  // AND_Gate and_1, 32 bits wide
  Comparator #(.width(32)) comparator_3 (
    .a(SRC_1), .b(SRC_2), .gt(comparator_3_gt), .eq(comparator_3_eq), .lt(comparator_3_lt));
  Comparator #(.mode("unsigned"), .width(32)) comparator_4 (
    .a(SRC_1), .b(SRC_2), .gt(comparator_4_gt), .eq(comparator_4_eq), .lt(comparator_4_lt));
  Multiplexer #(.enable("false"), .width(32)) multiplexer_1 (
    .in0(adder_1_out), .in1(subtractor_1_out), .out(multiplexer_1_out), .sel(I));
  assign bit_extender_1_out = {{31{1'b0}}, comparator_1_lt};  // Bit_Extender bit_extender_1
  assign bit_extender_2_out = {{31{1'b0}}, comparator_2_lt};  // Bit_Extender bit_extender_2
  or or_2 (or_2_out, comparator_4_gt, comparator_4_eq);
  not not_1 (not_1_out, comparator_3_eq);
  or or_3 (or_3_out, comparator_3_eq, comparator_3_gt);
  // Probe on multiplexer_1_out
  Multiplexer #(.enable("false"), .select(3)) multiplexer_2 (
    .in0(comparator_3_eq), .in1(not_1_out), .in2(1'b0), .in3(1'b0), .in4(comparator_3_lt), .in5(or_3_out),
    .in6(comparator_4_lt), .in7(or_2_out), .out(Branch), .sel(Funct3));
  Multiplexer #(.enable("false"), .select(3), .width(32)) multiplexer_3 (
    .in0(multiplexer_1_out), .in1({32{1'b0}}), .in2(bit_extender_1_out), .in3(bit_extender_2_out),
    .in4(xor_1_out), .in5({32{1'b0}}), .in6(or_1_out), .in7(and_1_out), .out(out_6), .sel(Funct3));
  Comparator #(.width(32)) comparator_5 (.a({32{1'b0}}), .b(out_6), .eq(Zero));  // open: gt, lt

  // Notes on the sheet:
  //   add
  //   sub
  //   SLL
  //   SLT
  //   SLTU
  //   XOR
  //   SRL
  //   SRA
  //   OR
  //   AND
endmodule

module ALU_Control (
  input  [31:0] in_1,
  input  [1:0] in_2,
  output [2:0] Funct3,
  output i
);

  Multiplexer #(.enable("false"), .select(2), .width(3)) multiplexer_1 (
    .in0(in_1[14:12]), .in1(3'b000), .in2(3'b010), .in3(3'b011), .out(Funct3), .sel(in_2));

  assign i = in_1[30];

  // Notes on the sheet:
  //   Funct3
endmodule

module ALU_Control_v2 (
  input  [31:0] Instruction,
  input  [1:0] ALUOp_in,
  output [2:0] ALUOp,
  output out_4
);

  wire and_2_out, or_1_out;

  or or_1 (or_1_out, ALUOp_in[0], ALUOp_in[1]);
  and and_1 (out_4, Instruction[30], ~or_1_out);  // AND_Gate
  Multiplexer #(.enable("false"), .width(3)) multiplexer_1 (
    .in0(Instruction[14:12]), .in1(3'b000), .out(ALUOp), .sel(and_2_out));
  and and_2 (and_2_out, ALUOp_in[0], ~ALUOp_in[1]);  // AND_Gate

  // Notes on the sheet:
  //   Funct3
  //   i
endmodule

module ALU_Control_v3 (
  input  [31:0] Instruction,
  input  [1:0] ALUOp_in,
  output [2:0] ALUOp,
  output i
);

  wire and_2_out, not_1_out, or_1_out;

  or or_1 (or_1_out, ALUOp_in[0], ALUOp_in[1]);
  and and_1 (i, Instruction[30], ~or_1_out);  // AND_Gate
  Multiplexer #(.enable("false"), .width(3)) multiplexer_1 (
    .in0(Instruction[14:12]), .in1(3'b000), .out(ALUOp), .sel(and_2_out));
  and and_2 (and_2_out, ALUOp_in[0], ~ALUOp_in[1]);  // AND_Gate
  // AND_Gate and_3 has open pins: in1=not_1_out, out=open
  // AND_Gate and_4 has open pins: in1=not_1_out, out=open
  // AND_Gate and_5 has open pins: in1=not_1_out, out=open
  not not_1 (not_1_out, and_2_out);

  // Notes on the sheet:
  //   Funct3
endmodule

module Branch_generator_v1 (
  input  ALU_Z,
  input  [2:0] Funct3,
  input  Branch_EN,
  output Take_Branch
);

  wire and_1_out, and_2_out, and_4_out, and_5_out, and_6_out, decoder_1_out0, decoder_1_out1, decoder_1_out4,
       decoder_1_out5, decoder_1_out6, decoder_1_out7, not_1_out;

  not not_1 (not_1_out, ALU_Z);
  Decoder #(.select(3)) decoder_1 (
    .out0(decoder_1_out0), .out1(decoder_1_out1), .out4(decoder_1_out4), .out5(decoder_1_out5),
    .out6(decoder_1_out6), .out7(decoder_1_out7), .sel(Funct3), .en(Branch_EN));  // open: out2, out3
  and and_1 (and_1_out, decoder_1_out0, ALU_Z);
  and and_2 (and_2_out, decoder_1_out1, not_1_out);
  // AND_Gate and_3 has open pins: in0=decoder_1_out4, in1=ALU_Z, out=open
  and and_4 (and_4_out, decoder_1_out5, not_1_out);
  and and_5 (and_5_out, decoder_1_out6, ALU_Z);
  and and_6 (and_6_out, decoder_1_out7, not_1_out);
  or or_1 (Take_Branch, and_1_out, and_2_out, and_4_out, and_5_out, and_6_out);

  // Notes on the sheet:
  //   BEQ
  //   BNE
  //   BLT
  //   BGE
  //   BLTU
  //   BGEU
endmodule

module Program_Counter_v1 (
  input  [31:0] in,
  input  Enable,
  input  Clock,
  input  Clear,
  output [31:0] out
);

  Register #(.width(32)) register_1 (.D(in), .en(Enable), .Q(out), .clk(Clock), .clr(Clear));
endmodule
module Program_Counter_v20 (
  input  SRC1,
  input  CLK,
  input  T_BRCH,
  input  SRC0,
  input  PCE,
  input  BRCH,
  input  RST,
  input  [31:0] Y,
  input  [31:0] OUT_in,
  output [31:0] X,
  output [31:0] OUT
);

  wire and_1_out, and_2_out, and_3_out, not_1_out, not_2_out, not_3_out, or_1_out, or_2_out, PC_Clear_out;
  wire [31:0] pc_adder_v2_1_out_5;

  and and_1 (and_1_out, ~T_BRCH, SRC0);  // AND_Gate
  and and_2 (and_2_out, BRCH, T_BRCH);
  Button PC_Clear (.out(PC_Clear_out));
  or or_1 (or_1_out, and_1_out, and_2_out);
  or or_2 (or_2_out, and_2_out, RST, PCE);
  Program_Counter_v1 program_counter_v1_1 (.out(X), .Enable(or_2_out), .Clock(CLK), .in(OUT), .Clear(PC_Clear_out));
  assign OUT = not_1_out ? pc_adder_v2_1_out_5 : 32'bz;  // Controlled_Buffer controlled_buffer_1
  PC_Adder_v2 pc_adder_v2_1 (.out_5(pc_adder_v2_1_out_5), .Y(Y), .X(X), .Mode(or_1_out), .Rst(RST));
  not not_1 (not_1_out, and_3_out);
  assign OUT = not_2_out ? OUT_in : 32'bz;  // Controlled_Buffer controlled_buffer_2
  not not_2 (not_2_out, not_3_out);
  not not_3 (not_3_out, SRC1);
  and and_3 (and_3_out, SRC1, SRC1);
  // Probe on X
  // Probe on Y

  // Other names for the same wires on the sheet: branch = BRCH; PC_Source = SRC0; PC_Source_1 = SRC1;
  //   Program_counter_enable = PCE; Take_branch = T_BRCH

  // Notes on the sheet:
  //   Inputs
  //   Circuit
  //   PROGRAM COUNTER
  //   Outputs
endmodule

module Half_adder (
  input  in_1,
  input  in_2,
  output out_3,
  output out_4
);

  xor xor_1 (out_3, in_1, in_2);
  and and_1 (out_4, in_1, in_2);
endmodule

module PC_adder_v1 (
  input  [31:0] in_1
);

  wire half_adder_1_out_4, half_adder_2_out_4, half_adder_3_out_4, half_adder_4_out_4, half_adder_5_out_4,
       half_adder_6_out_4, half_adder_7_out_4, half_adder_8_out_4, half_adder_9_out_4, half_adder_10_out_4,
       half_adder_11_out_4, half_adder_12_out_4, half_adder_13_out_4, half_adder_14_out_4,
       half_adder_15_out_4, half_adder_16_out_4, half_adder_17_out_4, half_adder_18_out_4,
       half_adder_19_out_4, half_adder_20_out_4, half_adder_21_out_4, half_adder_22_out_4,
       half_adder_23_out_4, half_adder_24_out_4, half_adder_25_out_4, half_adder_26_out_4,
       half_adder_27_out_4, half_adder_28_out_4, half_adder_29_out_4;
  wire [31:2] half_adder_1_out_3;

  Half_adder half_adder_1 (.out_4(half_adder_1_out_4), .out_3(half_adder_1_out_3[2]), .in_1(in_1[2]), .in_2(1'b1));
  Half_adder half_adder_2 (
    .out_4(half_adder_2_out_4), .out_3(half_adder_1_out_3[3]), .in_1(half_adder_1_out_4), .in_2(in_1[3]));
  Half_adder half_adder_3 (
    .out_4(half_adder_3_out_4), .out_3(half_adder_1_out_3[4]), .in_1(half_adder_2_out_4), .in_2(in_1[4]));
  Half_adder half_adder_4 (
    .out_4(half_adder_4_out_4), .out_3(half_adder_1_out_3[5]), .in_1(half_adder_3_out_4), .in_2(in_1[5]));
  Half_adder half_adder_5 (
    .out_4(half_adder_5_out_4), .out_3(half_adder_1_out_3[6]), .in_1(half_adder_4_out_4), .in_2(in_1[6]));
  Half_adder half_adder_6 (
    .out_4(half_adder_6_out_4), .out_3(half_adder_1_out_3[7]), .in_1(half_adder_5_out_4), .in_2(in_1[7]));
  Half_adder half_adder_7 (
    .out_4(half_adder_7_out_4), .out_3(half_adder_1_out_3[8]), .in_1(half_adder_6_out_4), .in_2(in_1[8]));
  Half_adder half_adder_8 (
    .out_4(half_adder_8_out_4), .out_3(half_adder_1_out_3[9]), .in_1(half_adder_7_out_4), .in_2(in_1[9]));
  Half_adder half_adder_9 (
    .out_4(half_adder_9_out_4), .out_3(half_adder_1_out_3[10]), .in_1(half_adder_8_out_4), .in_2(in_1[10]));
  Half_adder half_adder_10 (
    .out_4(half_adder_10_out_4), .out_3(half_adder_1_out_3[11]), .in_1(half_adder_9_out_4), .in_2(in_1[11]));
  Half_adder half_adder_11 (
    .out_4(half_adder_11_out_4), .out_3(half_adder_1_out_3[12]), .in_1(half_adder_10_out_4), .in_2(in_1[12]));
  Half_adder half_adder_12 (
    .out_4(half_adder_12_out_4), .out_3(half_adder_1_out_3[13]), .in_1(half_adder_11_out_4), .in_2(in_1[13]));
  Half_adder half_adder_13 (
    .out_4(half_adder_13_out_4), .out_3(half_adder_1_out_3[14]), .in_1(half_adder_12_out_4), .in_2(in_1[14]));
  Half_adder half_adder_14 (
    .out_4(half_adder_14_out_4), .out_3(half_adder_1_out_3[15]), .in_1(half_adder_13_out_4), .in_2(in_1[15]));
  Half_adder half_adder_15 (
    .out_4(half_adder_15_out_4), .out_3(half_adder_1_out_3[16]), .in_1(half_adder_14_out_4), .in_2(in_1[16]));
  Half_adder half_adder_16 (
    .out_4(half_adder_16_out_4), .out_3(half_adder_1_out_3[17]), .in_1(half_adder_15_out_4), .in_2(in_1[17]));
  Half_adder half_adder_17 (
    .out_4(half_adder_17_out_4), .out_3(half_adder_1_out_3[18]), .in_1(half_adder_16_out_4), .in_2(in_1[18]));
  Half_adder half_adder_18 (
    .out_4(half_adder_18_out_4), .out_3(half_adder_1_out_3[19]), .in_1(half_adder_17_out_4), .in_2(in_1[19]));
  Half_adder half_adder_19 (
    .out_4(half_adder_19_out_4), .out_3(half_adder_1_out_3[20]), .in_1(half_adder_18_out_4), .in_2(in_1[20]));
  Half_adder half_adder_20 (
    .out_4(half_adder_20_out_4), .out_3(half_adder_1_out_3[21]), .in_1(half_adder_19_out_4), .in_2(in_1[21]));
  Half_adder half_adder_21 (
    .out_4(half_adder_21_out_4), .out_3(half_adder_1_out_3[22]), .in_1(half_adder_20_out_4), .in_2(in_1[22]));
  Half_adder half_adder_22 (
    .out_4(half_adder_22_out_4), .out_3(half_adder_1_out_3[23]), .in_1(half_adder_21_out_4), .in_2(in_1[23]));
  Half_adder half_adder_23 (
    .out_4(half_adder_23_out_4), .out_3(half_adder_1_out_3[24]), .in_1(half_adder_22_out_4), .in_2(in_1[24]));
  Half_adder half_adder_24 (
    .out_4(half_adder_24_out_4), .out_3(half_adder_1_out_3[25]), .in_1(half_adder_23_out_4), .in_2(in_1[25]));
  Half_adder half_adder_25 (
    .out_4(half_adder_25_out_4), .out_3(half_adder_1_out_3[26]), .in_1(half_adder_24_out_4), .in_2(in_1[26]));
  Half_adder half_adder_26 (
    .out_4(half_adder_26_out_4), .out_3(half_adder_1_out_3[27]), .in_1(half_adder_25_out_4), .in_2(in_1[27]));
  Half_adder half_adder_27 (
    .out_4(half_adder_27_out_4), .out_3(half_adder_1_out_3[28]), .in_1(half_adder_26_out_4), .in_2(in_1[28]));
  Half_adder half_adder_28 (
    .out_4(half_adder_28_out_4), .out_3(half_adder_1_out_3[29]), .in_1(half_adder_27_out_4), .in_2(in_1[29]));
  Half_adder half_adder_29 (
    .out_4(half_adder_29_out_4), .out_3(half_adder_1_out_3[30]), .in_1(half_adder_28_out_4), .in_2(in_1[30]));
  // Probe on {half_adder_1_out_3, in_1[1:0]}
  Half_adder half_adder_30 (
    .out_3(half_adder_1_out_3[31]), .in_1(half_adder_29_out_4), .in_2(in_1[31]));  // open: out_4
endmodule

module PC_Adder_v2 (
  input  [31:0] Y,
  input  [31:0] X,
  input  Mode,
  input  Rst,
  output [31:0] out_5
);

  wire [0:0] rom_1_data, rom_2_data, rom_3_data, rom_4_data;
  wire [7:4] rom_5_data;

  ROM #(.addrWidth(17)) rom_1 (.addr({Rst, Y[6:0], X[6:0], Mode, 1'b0}), .data({rom_1_data[0], out_5[6:0]}));
  ROM #(.addrWidth(17)) rom_2 (
    .addr({Rst, Y[13:7], X[13:7], Mode, rom_1_data[0]}), .data({rom_2_data[0], out_5[13:7]}));
  ROM #(.addrWidth(17)) rom_3 (
    .addr({Rst, Y[20:14], X[20:14], Mode, rom_2_data[0]}), .data({rom_3_data[0], out_5[20:14]}));
  ROM #(.addrWidth(17)) rom_4 (
    .addr({Rst, Y[27:21], X[27:21], Mode, rom_3_data[0]}), .data({rom_4_data[0], out_5[27:21]}));
  ROM #(.addrWidth(17)) rom_5 (
    .addr({Rst, 3'b000, Y[31:28], 3'b000, X[31:28], Mode, rom_4_data[0]}), .data({rom_5_data, out_5[31:28]}));

  // Notes on the sheet:
  //   contents of rom_1 (hex, n*v repeats v):
  //   compressed eJxk3VuS29YBRdF/joJDsN7ScCTbmv8QQux1btoNVcUMEgJsEsBdtYNXPj+/PP96fni9fn29fnx8
  //   fX57fnx+er1+f71+fnx//nh+fr374/nzmufx8/nrec3z6/n3Nc/j7+c/z2uef57/XvM8/n3+fl7z
  //   /H5++Oua6fH6tw8fntdsr3/78PGa8fH6tw+fntesr3/78LmZH69///DlafZr4qsFHtfEt6dFronv
  //   FnpcEz+eW+o18dNSj2vi13NLvSb+ttTjmvjnuaVeE/9a6nFN/H5uqd/Pj3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
  //   contents of rom_2 (hex, n*v repeats v):
  //   compressed eJxk3VmO3EajbtF3joJDUN8MR9IvzX8IJ2Ovj3V9UUBWOODsScbCtiWFPtwf7w+vn4/3p/Nzfbo/
  //   3+fn8/3l/Fxf7q/3+fl6fzs/17f7+31+vt8/zs/14/55n5+f96/zc/26f9/n5/f95/xcf+7/3efn
  //   f/ff83P9vf/d5+ff/fFDw/X658eP98bX7ZPxOpPP98bX7YvxOpOv98bX7ZvxOpPv98bX7YfxOpOf
  //   98bX7ZfxOpPf98bX7Y/xOpP/3Rtft7/G60z+3Rv/3Z8+GK/X5NPHe+Pr9s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
  //   contents of rom_3 (hex, n*v repeats v):
  //   compressed eJxk3VmO3EajbtF3joJDUN8MR9IvzX8IJ2Ovj3V9UUBWOODsScbCtiWFPtwf7w+vn4/3p/Nzfbo/
  //   3+fn8/3l/Fxf7q/3+fl6fzs/17f7+31+vt8/zs/14/55n5+f96/zc/26f9/n5/f95/xcf+7/3efn
  //   f/ff83P9vf/d5+ff/fFDw/X658eP98bX7ZPxOpPP98bX7YvxOpOv98bX7ZvxOpPv98bX7YfxOpOf
  //   98bX7ZfxOpPf98bX7Y/xOpP/3Rtft7/G60z+3Rv/3Z8+GK/X5NPHe+Pr9s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
  //   contents of rom_4 (hex, n*v repeats v):
  //   compressed eJxk3VmO3EajbtF3joJDUN8MR9IvzX8IJ2Ovj3V9UUBWOODsScbCtiWFPtwf7w+vn4/3p/Nzfbo/
  //   3+fn8/3l/Fxf7q/3+fl6fzs/17f7+31+vt8/zs/14/55n5+f96/zc/26f9/n5/f95/xcf+7/3efn
  //   f/ff83P9vf/d5+ff/fFDw/X658eP98bX7ZPxOpPP98bX7YvxOpOv98bX7ZvxOpPv98bX7YfxOpOf
  //   98bX7ZfxOpPf98bX7Y/xOpP/3Rtft7/G60z+3Rv/3Z8+GK/X5NPHe+Pr9s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
  //   contents of rom_5 (hex, n*v repeats v):
  //   compressed eJxk3VmO3EajbtF3joJDUN8MR9IvzX8IJ2Ovj3V9UUBWOODsScbCtiWFPtwf7w+vn4/3p/Nzfbo/
  //   3+fn8/3l/Fxf7q/3+fl6fzs/17f7+31+vt8/zs/14/55n5+f96/zc/26f9/n5/f95/xcf+7/3efn
  //   f/ff83P9vf/d5+ff/fFDw/X658eP98bX7ZPxOpPP98bX7YvxOpOv98bX7ZvxOpPv98bX7YfxOpOf
  //   98bX7ZfxOpPf98bX7Y/xOpP/3Rtft7/G60z+3Rv/3Z8+GK/X5NPHe+Pr9s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
endmodule

module Instruction_memory_v1 (
  input  [31:0] in,
  input  [7:0] in_2,
  input  [7:0] in_3,
  input  [7:0] in_4,
  input  [7:0] in_5,
  output [18:0] out_6,
  output [31:0] out_7
);


  assign out_6 = in[18:0];
  assign out_7 = {in_2, in_3, in_4, in_5};
endmodule

module Data_memory_v1 (
  input  [31:0] Adress,
  input  [31:0] Data,
  input  Clock,
  input  Store,
  output [31:0] out_5
);

  RAM ram_1 (.addr(Adress[9:2]), .we(Store), .clk(Clock), .din(Data[9:2]), .dout(out_5[7:0]));
  RAM ram_2 (.addr(Adress[17:10]), .we(Store), .clk(Clock), .din(Data[17:10]), .dout(out_5[15:8]));
  RAM ram_3 (.addr(Adress[25:18]), .we(Store), .clk(Clock), .din(Data[25:18]), .dout(out_5[23:16]));
  RAM #(.addrWidth(6), .dataWidth(6)) ram_4 (
    .addr(Adress[31:26]), .we(Store), .clk(Clock), .din(Data[31:26]), .dout(out_5[31:26]));
endmodule

module Data_memory_v2 (
  input  [31:0] Adress,
  input  [31:0] Data,
  input  [2:0] Funct3,
  input  Store,
  input  Clock,
  output [31:0] out_6
);

  wire B0, B1, B2, B3, decoder_1_out0, decoder_2_out0, decoder_2_out1, decoder_2_out2, decoder_2_out3, H,
       or_1_out, or_2_out, or_3_out, undriven, undriven_2, undriven_3, undriven_4, undriven_5, undriven_6, W;
  wire [7:0] controlled_buffer_1_out, controlled_buffer_2_out, controlled_buffer_4_out,
       controlled_buffer_6_out, ram_1_dout, ram_2_dout, ram_3_dout, ram_4_dout;

  Decoder #(.enable("false"), .select(2)) decoder_1 (
    .out0(decoder_1_out0), .out1(H), .out2(W), .sel(Funct3[1:0]));  // open: out3
  Decoder #(.enable("false"), .select(2)) decoder_2 (
    .out0(decoder_2_out0), .out1(decoder_2_out1), .out2(decoder_2_out2), .out3(decoder_2_out3),
    .sel(Adress[1:0]));
  // Probe on Adress
  and and_1 (B0, decoder_2_out0, decoder_1_out0);
  and and_2 (B1, decoder_1_out0, decoder_2_out1);
  and and_3 (B2, decoder_1_out0, decoder_2_out2);
  and and_4 (B3, decoder_1_out0, decoder_2_out3);
  assign controlled_buffer_1_out = or_1_out ? Data[7:0] : 8'bz;  // Controlled_Buffer controlled_buffer_1
  assign controlled_buffer_2_out = or_2_out ? Data[15:8] : 8'bz;  // Controlled_Buffer controlled_buffer_2
  or or_1 (or_1_out, B0, H, W);
  or or_2 (or_2_out, H, W);
  assign controlled_buffer_2_out = B1 ? Data[7:0] : 8'bz;  // Controlled_Buffer controlled_buffer_3
  assign controlled_buffer_4_out = B2 ? Data[7:0] : 8'bz;  // Controlled_Buffer controlled_buffer_4
  assign controlled_buffer_4_out = W ? Data[23:16] : 8'bz;  // Controlled_Buffer controlled_buffer_5
  assign controlled_buffer_6_out = W ? Data[31:24] : 8'bz;  // Controlled_Buffer controlled_buffer_6
  assign controlled_buffer_6_out = B3 ? Data[7:0] : 8'bz;  // Controlled_Buffer controlled_buffer_7
  // Probe on Adress[17:2]
  Pull_Resistor pull_resistor_1 (.node(controlled_buffer_1_out));
  Pull_Resistor pull_resistor_2 (.node(controlled_buffer_4_out));
  Pull_Resistor pull_resistor_3 (.node(controlled_buffer_6_out));
  RAM #(.addrWidth(16)) ram_1 (
    .addr(Adress[17:2]), .we(Store), .clk(Clock), .din(controlled_buffer_1_out), .dout(ram_1_dout));
  RAM #(.addrWidth(16)) ram_2 (
    .addr(Adress[17:2]), .we(Store), .clk(Clock), .din(controlled_buffer_2_out), .dout(ram_2_dout));
  Pull_Resistor pull_resistor_4 (.node(controlled_buffer_2_out));
  RAM #(.addrWidth(16)) ram_3 (
    .addr(Adress[17:2]), .we(Store), .clk(Clock), .din(controlled_buffer_4_out), .dout(ram_3_dout));
  RAM #(.addrWidth(16)) ram_4 (
    .addr(Adress[17:2]), .we(Store), .clk(Clock), .din(controlled_buffer_6_out), .dout(ram_4_dout));
  assign out_6[7:0] = or_3_out ? ram_1_dout : 8'bz;  // Controlled_Buffer controlled_buffer_8
  buf or_3 (or_3_out, B0);  // OR_Gate
  assign out_6[15:8] = undriven ? ram_2_dout : 8'bz;  // Controlled_Buffer controlled_buffer_9
  assign out_6[23:16] = undriven_2 ? ram_3_dout : 8'bz;  // Controlled_Buffer controlled_buffer_10
  assign out_6[31:24] = undriven_3 ? ram_4_dout : 8'bz;  // Controlled_Buffer controlled_buffer_11
  assign out_6[7:0] = undriven_4 ? ram_2_dout : 8'bz;  // Controlled_Buffer controlled_buffer_12
  assign out_6[7:0] = undriven_5 ? ram_3_dout : 8'bz;  // Controlled_Buffer controlled_buffer_13
  assign out_6[7:0] = undriven_6 ? ram_4_dout : 8'bz;  // Controlled_Buffer controlled_buffer_14
  Pull_Resistor pull_resistor_5 (.node(out_6[7:0]));
  Pull_Resistor pull_resistor_6 (.node(out_6[15:8]));
  Pull_Resistor pull_resistor_7 (.node(out_6[23:16]));
  Pull_Resistor pull_resistor_8 (.node(out_6[31:24]));
  // NOT_Gate not_1 is placed but not wired

  // Notes on the sheet:
  //   Byte
  //   Half
  //   Word
endmodule

module Data_memory_v3 (
  input  [31:0] Adress,
  input  [31:0] Data,
  input  [2:0] Funct3,
  input  Store,
  input  Clock,
  output [31:0] out_6
);

  wire and_1_out, and_2_out, and_3_out, and_4_out, and_5_out, and_6_out, and_7_out, and_8_out, B0, B1, B2,
       B3, decoder_1_out0, decoder_1_out1, decoder_2_out0, decoder_2_out1, decoder_2_out2, decoder_2_out3, W;
  wire [7:0] BYTE_0_dout, BYTE_1_dout, BYTE_2_dout, BYTE_3_dout, controlled_buffer_1_out,
       controlled_buffer_2_out, controlled_buffer_4_out, controlled_buffer_6_out;

  Decoder #(.enable("false"), .select(2)) decoder_1 (
    .out0(decoder_1_out0), .out1(decoder_1_out1), .out2(W), .sel(Funct3[1:0]));  // open: out3
  Decoder #(.enable("false"), .select(2)) decoder_2 (
    .out0(decoder_2_out0), .out1(decoder_2_out1), .out2(decoder_2_out2), .out3(decoder_2_out3),
    .sel(Adress[1:0]));
  and and_1 (and_1_out, decoder_2_out0, decoder_1_out0);
  and and_2 (and_2_out, decoder_1_out0, decoder_2_out1);
  and and_3 (and_3_out, decoder_1_out0, decoder_2_out2);
  and and_4 (and_4_out, decoder_1_out0, decoder_2_out3);
  and and_5 (and_5_out, decoder_1_out1, decoder_2_out0);
  and and_6 (and_6_out, decoder_1_out1, decoder_2_out1);
  and and_7 (and_7_out, decoder_1_out1, decoder_2_out2);
  and and_8 (and_8_out, decoder_1_out1, decoder_2_out3);
  or or_1 (B2, and_3_out, and_6_out, and_7_out);
  or or_2 (B0, and_1_out, W, and_5_out, and_8_out);
  or or_3 (B1, and_2_out, and_5_out, and_6_out);
  or or_4 (B3, and_4_out, and_7_out, and_8_out);
  assign controlled_buffer_1_out = B0 ? Data[7:0] : 8'bz;  // Controlled_Buffer controlled_buffer_1
  assign controlled_buffer_2_out = W ? Data[15:8] : 8'bz;  // Controlled_Buffer controlled_buffer_2
  assign controlled_buffer_2_out = B1 ? Data[7:0] : 8'bz;  // Controlled_Buffer controlled_buffer_3
  assign controlled_buffer_4_out = B2 ? Data[7:0] : 8'bz;  // Controlled_Buffer controlled_buffer_4
  assign controlled_buffer_4_out = W ? Data[23:16] : 8'bz;  // Controlled_Buffer controlled_buffer_5
  assign controlled_buffer_6_out = W ? Data[31:24] : 8'bz;  // Controlled_Buffer controlled_buffer_6
  assign controlled_buffer_6_out = B3 ? Data[7:0] : 8'bz;  // Controlled_Buffer controlled_buffer_7
  // Probe on Adress[17:2]
  Pull_Resistor pull_resistor_1 (.node(controlled_buffer_1_out));
  Pull_Resistor pull_resistor_2 (.node(controlled_buffer_2_out));
  Pull_Resistor pull_resistor_3 (.node(controlled_buffer_4_out));
  Pull_Resistor pull_resistor_4 (.node(controlled_buffer_6_out));
  RAM #(.addrWidth(16)) BYTE_0 (
    .addr(Adress[17:2]), .we(Store), .clk(Clock), .din(controlled_buffer_1_out), .dout(BYTE_0_dout));
  RAM #(.addrWidth(16)) BYTE_1 (
    .addr(Adress[17:2]), .we(Store), .clk(Clock), .din(controlled_buffer_2_out), .dout(BYTE_1_dout));
  RAM #(.addrWidth(16)) BYTE_2 (
    .addr(Adress[17:2]), .we(Store), .clk(Clock), .din(controlled_buffer_4_out), .dout(BYTE_2_dout));
  RAM #(.addrWidth(16)) BYTE_3 (
    .addr(Adress[17:2]), .we(Store), .clk(Clock), .din(controlled_buffer_6_out), .dout(BYTE_3_dout));
  assign out_6[7:0] = B0 ? BYTE_0_dout : 8'bz;  // Controlled_Buffer controlled_buffer_8
  assign out_6[15:8] = W ? BYTE_1_dout : 8'bz;  // Controlled_Buffer controlled_buffer_9
  assign out_6[23:16] = W ? BYTE_2_dout : 8'bz;  // Controlled_Buffer controlled_buffer_10
  assign out_6[31:24] = W ? BYTE_3_dout : 8'bz;  // Controlled_Buffer controlled_buffer_11
  assign out_6[7:0] = B1 ? BYTE_1_dout : 8'bz;  // Controlled_Buffer controlled_buffer_12
  assign out_6[7:0] = B2 ? BYTE_2_dout : 8'bz;  // Controlled_Buffer controlled_buffer_13
  assign out_6[7:0] = B3 ? BYTE_3_dout : 8'bz;  // Controlled_Buffer controlled_buffer_14
  Pull_Resistor pull_resistor_5 (.node(out_6[7:0]));
  Pull_Resistor pull_resistor_6 (.node(out_6[15:8]));
  Pull_Resistor pull_resistor_7 (.node(out_6[23:16]));
  Pull_Resistor pull_resistor_8 (.node(out_6[31:24]));
  // NOT_Gate not_1 is placed but not wired

  // Notes on the sheet:
  //   Byte
  //   Half
  //   Word
endmodule

module Data_memory_v4 (
  input  [31:0] Adress,
  input  [31:0] Data,
  input  [2:0] Funct3,
  input  Clock,
  input  Store,
  output [31:0] out_6
);

  wire and_1_out, and_2_out, and_3_out, and_4_out, and_5_out, and_6_out, and_7_out, and_8_out, and_10_out,
       and_11_out, and_12_out, and_13_out, and_14_out, and_15_out, and_16_out, and_17_out, and_18_out,
       and_19_out, and_20_out, and_21_out, and_22_out, B, G1, G2, G3, G5, G6, G7, G8, G9, G10, H, or_9_out,
       or_10_out, or_11_out, or_12_out, or_13_out, or_14_out, or_15_out, s0, s1, s2, s3, Sign, W;
  wire [6:0] BYTE_3_dout;
  wire [7:0] bit_extender_1_out, bit_extender_2_out, BYTE_0_dout, BYTE_1_dout, BYTE_2_dout;
  wire [14:0] memory_adder_v1_1_out, memory_adder_v1_2_out, memory_adder_v1_3_out;
  wire [31:0] controlled_buffer_1_out;

  Decoder #(.enable("false"), .select(2)) decoder_1 (.out0(B), .out1(H), .out2(W), .sel(Funct3[1:0]));  // open: out3
  Decoder #(.enable("false"), .select(2)) decoder_2 (.out0(s0), .out1(s1), .out2(s2), .out3(s3), .sel(Adress[1:0]));
  and and_1 (and_1_out, B, s0);
  and and_2 (and_2_out, B, s1);
  and and_3 (and_3_out, B, s2);
  and and_4 (and_4_out, B, s3);
  and and_5 (and_5_out, H, s0);
  and and_6 (and_6_out, H, s1);
  and and_7 (and_7_out, H, s2);
  and and_8 (and_8_out, H, s3);
  and and_9 (G3, W, s0);
  and and_10 (and_10_out, W, s1);
  and and_11 (and_11_out, W, s2);
  and and_12 (and_12_out, W, s3);
  or or_1 (G1, and_1_out, and_5_out, G3);
  or or_2 (G2, and_5_out, G3);
  or or_3 (G5, and_10_out, and_2_out, and_6_out);
  or or_4 (G6, and_11_out, and_3_out, and_7_out);
  or or_5 (G7, and_12_out, and_4_out, and_8_out);
  or or_6 (G8, and_12_out, and_8_out);
  or or_7 (G9, and_10_out, and_6_out);
  or or_8 (G10, and_11_out, and_7_out);
  assign controlled_buffer_1_out[7:0] = G1 ? Data[7:0] : 8'bz;  // Controlled_Buffer controlled_buffer_1
  assign controlled_buffer_1_out[15:8] = G2 ? Data[15:8] : 8'bz;  // Controlled_Buffer controlled_buffer_2
  assign controlled_buffer_1_out[23:16] = G3 ? Data[23:16] : 8'bz;  // Controlled_Buffer controlled_buffer_3
  assign controlled_buffer_1_out[31:24] = G3 ? Data[31:24] : 8'bz;  // Controlled_Buffer controlled_buffer_4
  assign controlled_buffer_1_out[15:8] = G5 ? Data[7:0] : 8'bz;  // Controlled_Buffer controlled_buffer_5
  assign controlled_buffer_1_out[23:16] = G6 ? Data[7:0] : 8'bz;  // Controlled_Buffer controlled_buffer_6
  assign controlled_buffer_1_out[31:24] = G7 ? Data[7:0] : 8'bz;  // Controlled_Buffer controlled_buffer_7
  assign controlled_buffer_1_out[7:0] = G8 ? Data[15:8] : 8'bz;  // Controlled_Buffer controlled_buffer_8
  assign controlled_buffer_1_out[23:16] = G9 ? Data[15:8] : 8'bz;  // Controlled_Buffer controlled_buffer_9
  assign controlled_buffer_1_out[31:24] = G10 ? Data[15:8] : 8'bz;  // Controlled_Buffer controlled_buffer_10
  assign controlled_buffer_1_out[31:24] = and_10_out ? Data[23:16] : 8'bz;  // Controlled_Buffer controlled_buffer_11
  assign controlled_buffer_1_out[7:0] = and_10_out ? Data[31:24] : 8'bz;  // Controlled_Buffer controlled_buffer_12
  or or_9 (or_9_out, G8, G1);
  or or_10 (or_10_out, G2, G5);
  or or_11 (or_11_out, G6, G3, G9);
  or or_12 (or_12_out, G3, G7, G10);
  assign controlled_buffer_1_out[7:0] = and_11_out ? Data[23:16] : 8'bz;  // Controlled_Buffer controlled_buffer_13
  assign controlled_buffer_1_out[15:8] = and_11_out ? Data[31:24] : 8'bz;  // Controlled_Buffer controlled_buffer_14
  and and_13 (and_13_out, Store, or_9_out);
  and and_14 (and_14_out, Store, or_10_out);
  and and_15 (and_15_out, Store, or_11_out);
  and and_16 (and_16_out, Store, or_12_out);
  assign controlled_buffer_1_out[15:8] = G7 ? Data[23:16] : 8'bz;  // Controlled_Buffer controlled_buffer_15
  assign controlled_buffer_1_out[23:16] = G7 ? Data[31:24] : 8'bz;  // Controlled_Buffer controlled_buffer_16
  or or_13 (or_13_out, s1, s2, s3);
  // Probe on controlled_buffer_1_out
  and and_17 (and_17_out, W, or_13_out);
  or or_14 (or_14_out, and_17_out, and_18_out);
  and and_18 (and_18_out, H, s3);
  or or_15 (or_15_out, s2, s3);
  and and_19 (and_19_out, W, or_15_out);
  Memory_adder_v1 memory_adder_v1_1 (.Out(memory_adder_v1_1_out), .In(Adress[16:2]), .plusOne(and_19_out));
  and and_20 (and_20_out, W, s3);
  Memory_adder_v1 memory_adder_v1_2 (.Out(memory_adder_v1_2_out), .In(Adress[16:2]), .plusOne(and_20_out));
  Memory_adder_v1 memory_adder_v1_3 (.Out(memory_adder_v1_3_out), .In(Adress[16:2]), .plusOne(or_14_out));
  Pull_Resistor pull_resistor_1 (.node(controlled_buffer_1_out[7:0]));
  RAM #(.addrWidth(15)) BYTE_0 (
    .addr(memory_adder_v1_3_out), .we(and_13_out), .clk(Clock), .din(controlled_buffer_1_out[7:0]),
    .dout(BYTE_0_dout));
  RAM #(.addrWidth(15)) BYTE_1 (
    .addr(memory_adder_v1_1_out), .we(and_14_out), .clk(Clock), .din(controlled_buffer_1_out[15:8]),
    .dout(BYTE_1_dout));
  Pull_Resistor pull_resistor_2 (.node(controlled_buffer_1_out[15:8]));
  RAM #(.addrWidth(15)) BYTE_2 (
    .addr(memory_adder_v1_2_out), .we(and_15_out), .clk(Clock), .din(controlled_buffer_1_out[23:16]),
    .dout(BYTE_2_dout));
  Pull_Resistor pull_resistor_3 (.node(controlled_buffer_1_out[23:16]));
  RAM #(.addrWidth(15)) BYTE_3 (
    .addr(Adress[16:2]), .we(and_16_out), .clk(Clock), .din(controlled_buffer_1_out[31:24]),
    .dout({Sign, BYTE_3_dout}));
  Pull_Resistor pull_resistor_4 (.node(controlled_buffer_1_out[31:24]));
  assign out_6[7:0] = G1 ? BYTE_0_dout : 8'bz;  // Controlled_Buffer controlled_buffer_17
  assign out_6[15:8] = G2 ? BYTE_1_dout : 8'bz;  // Controlled_Buffer controlled_buffer_18
  assign out_6[23:16] = G3 ? BYTE_2_dout : 8'bz;  // Controlled_Buffer controlled_buffer_19
  assign out_6[31:24] = G3 ? {Sign, BYTE_3_dout} : 8'bz;  // Controlled_Buffer controlled_buffer_20
  assign out_6[7:0] = G5 ? BYTE_1_dout : 8'bz;  // Controlled_Buffer controlled_buffer_21
  assign out_6[7:0] = G6 ? BYTE_2_dout : 8'bz;  // Controlled_Buffer controlled_buffer_22
  assign out_6[7:0] = G7 ? BYTE_2_dout : 8'bz;  // Controlled_Buffer controlled_buffer_23
  assign out_6[15:8] = G8 ? BYTE_0_dout : 8'bz;  // Controlled_Buffer controlled_buffer_24
  assign out_6[15:8] = G9 ? BYTE_2_dout : 8'bz;  // Controlled_Buffer controlled_buffer_25
  assign out_6[15:8] = G10 ? {Sign, BYTE_3_dout} : 8'bz;  // Controlled_Buffer controlled_buffer_26
  assign bit_extender_1_out = {{7{out_6[7]}}, out_6[7]};  // Bit_Extender bit_extender_1
  assign out_6[15:8] = and_21_out ? bit_extender_1_out : 8'bz;  // Controlled_Buffer controlled_buffer_27
  and and_21 (and_21_out, B, ~Funct3[2]);  // AND_Gate
  assign out_6[23:16] = and_21_out ? bit_extender_1_out : 8'bz;  // Controlled_Buffer controlled_buffer_28
  assign out_6[31:24] = and_21_out ? bit_extender_1_out : 8'bz;  // Controlled_Buffer controlled_buffer_29
  assign bit_extender_2_out = {{7{out_6[15]}}, out_6[15]};  // Bit_Extender bit_extender_2
  and and_22 (and_22_out, H, ~Funct3[2]);  // AND_Gate
  // Probe on bit_extender_1_out
  assign out_6[23:16] = and_22_out ? bit_extender_2_out : 8'bz;  // Controlled_Buffer controlled_buffer_30
  assign out_6[31:24] = and_22_out ? bit_extender_2_out : 8'bz;  // Controlled_Buffer controlled_buffer_31
  Pull_Resistor pull_resistor_5 (.node(out_6[7:0]));
  Pull_Resistor pull_resistor_6 (.node(out_6[15:8]));
  Pull_Resistor pull_resistor_7 (.node(out_6[23:16]));
  Pull_Resistor pull_resistor_8 (.node(out_6[31:24]));
  // NOT_Gate not_1 is placed but not wired

  // Other names for the same wires on the sheet: Funct3_2 = Funct3[2]; G4 = G3

  // Notes on the sheet:
  //   Byte
  //   Half
  //   Word
  //   For unaligned memory access
  //   Byte
  //   Half
  //   Word
endmodule

module Data_memory_v5 (
  input  [31:0] Adress,
  input  [31:0] Data,
  input  [2:0] Funct3,
  input  Clock,
  input  Store,
  output [31:0] out_6,
  output Exception
);

  wire and_6_out, and_8_out, and_9_out, and_10_out, and_11_out, and_12_out, and_13_out, and_14_out,
       and_15_out, and_16_out, and_17_out, B, B0, B1, B2, B3, G1, G2, G3, G4, G5, G6, G7, H, H0, H1,
       or_10_out, or_11_out, or_12_out, or_13_out, s0, s1, s2, s3;
  wire [7:0] bit_extender_1_out, bit_extender_2_out, BYTE_0_dout, BYTE_1_dout, BYTE_2_dout, BYTE_3_dout;
  wire [31:0] controlled_buffer_1_out;

  Decoder #(.enable("false"), .select(2)) decoder_1 (.out0(B), .out1(H), .out2(G3), .sel(Funct3[1:0]));  // open: out3
  Decoder #(.enable("false"), .select(2)) decoder_2 (.out0(s0), .out1(s1), .out2(s2), .out3(s3), .sel(Adress[1:0]));
  and and_1 (B0, B, s0);
  and and_2 (B1, B, s1);
  and and_3 (B2, B, s2);
  and and_4 (B3, B, s3);
  and and_5 (H0, H, s0);
  and and_6 (and_6_out, H, s1);
  and and_7 (H1, H, s2);
  and and_8 (and_8_out, H, s3);
  and and_9 (and_9_out, G3, s1);
  and and_10 (and_10_out, G3, s2);
  and and_11 (and_11_out, G3, s3);
  or or_1 (Exception, and_11_out, and_10_out, and_9_out, and_8_out, and_6_out);
  LED led_1 (.in(Exception));
  or or_2 (G1, G3, B0, H0);
  or or_3 (G2, G3, H0);
  buf or_4 (G4, B1);  // OR_Gate
  or or_5 (G5, B2, H1);
  buf or_6 (G6, B3);  // OR_Gate
  buf or_7 (G7, H1);  // OR_Gate
  assign controlled_buffer_1_out[7:0] = G1 ? Data[7:0] : 8'bz;  // Controlled_Buffer controlled_buffer_1
  assign controlled_buffer_1_out[15:8] = G2 ? Data[15:8] : 8'bz;  // Controlled_Buffer controlled_buffer_2
  assign controlled_buffer_1_out[23:16] = G3 ? Data[23:16] : 8'bz;  // Controlled_Buffer controlled_buffer_3
  assign controlled_buffer_1_out[31:24] = G3 ? Data[31:24] : 8'bz;  // Controlled_Buffer controlled_buffer_4
  // OR_Gate or_8 has open pins: in0=Adress[2], in1=Adress[3], in2=Adress[4], in3=Adress[5], in4=Adress[6], in5=Adress[7], in6=Adress[8], in7=Adress[9], in8=Adress[10], in9=Adress[11], in10=Adress[12], in11=Adress[13], in12=Adress[14], in13=Adress[15], in14=Adress[16], out=open
  // OR_Gate or_9 has open pins: in0=Adress[17], in1=Adress[18], in2=Adress[19], in3=Adress[20], in4=Adress[21], in5=Adress[22], in6=Adress[23], in7=Adress[25], in8=Adress[26], in9=Adress[27], in10=Adress[28], in11=Adress[29], in12=Adress[30], in13=Adress[31], out=open
  assign controlled_buffer_1_out[15:8] = G4 ? Data[7:0] : 8'bz;  // Controlled_Buffer controlled_buffer_5
  assign controlled_buffer_1_out[23:16] = G5 ? Data[7:0] : 8'bz;  // Controlled_Buffer controlled_buffer_6
  assign controlled_buffer_1_out[31:24] = G6 ? Data[7:0] : 8'bz;  // Controlled_Buffer controlled_buffer_7
  assign controlled_buffer_1_out[31:24] = G7 ? Data[15:8] : 8'bz;  // Controlled_Buffer controlled_buffer_8
  or or_10 (or_10_out, B0, H0, G3);
  or or_11 (or_11_out, B1, H0, G3);
  or or_12 (or_12_out, B2, H1, G3);
  or or_13 (or_13_out, B3, H1, G3);
  // Probe on controlled_buffer_1_out
  and and_12 (and_12_out, Store, or_10_out);
  and and_13 (and_13_out, Store, or_11_out);
  and and_14 (and_14_out, Store, or_12_out);
  and and_15 (and_15_out, Store, or_13_out);
  Pull_Resistor pull_resistor_1 (.node(controlled_buffer_1_out[7:0]));
  Pull_Resistor pull_resistor_2 (.node(controlled_buffer_1_out[31:24]));
  RAM #(.addrWidth(15)) BYTE_0 (
    .addr(Adress[16:2]), .we(and_12_out), .clk(Clock), .din(controlled_buffer_1_out[7:0]), .dout(BYTE_0_dout));
  RAM #(.addrWidth(15)) BYTE_1 (
    .addr(Adress[16:2]), .we(and_13_out), .clk(Clock), .din(controlled_buffer_1_out[15:8]), .dout(BYTE_1_dout));
  Pull_Resistor pull_resistor_3 (.node(controlled_buffer_1_out[15:8]));
  RAM #(.addrWidth(15)) BYTE_2 (
    .addr(Adress[16:2]), .we(and_14_out), .clk(Clock), .din(controlled_buffer_1_out[23:16]),
    .dout(BYTE_2_dout));
  Pull_Resistor pull_resistor_4 (.node(controlled_buffer_1_out[23:16]));
  RAM #(.addrWidth(15)) BYTE_3 (
    .addr(Adress[16:2]), .we(and_15_out), .clk(Clock), .din(controlled_buffer_1_out[31:24]),
    .dout(BYTE_3_dout));
  assign out_6[7:0] = G1 ? BYTE_0_dout : 8'bz;  // Controlled_Buffer controlled_buffer_9
  assign out_6[15:8] = G2 ? BYTE_1_dout : 8'bz;  // Controlled_Buffer controlled_buffer_10
  assign out_6[23:16] = G3 ? BYTE_2_dout : 8'bz;  // Controlled_Buffer controlled_buffer_11
  assign out_6[31:24] = G3 ? BYTE_3_dout : 8'bz;  // Controlled_Buffer controlled_buffer_12
  assign out_6[7:0] = G4 ? BYTE_1_dout : 8'bz;  // Controlled_Buffer controlled_buffer_13
  assign out_6[7:0] = G5 ? BYTE_2_dout : 8'bz;  // Controlled_Buffer controlled_buffer_14
  assign out_6[7:0] = G6 ? BYTE_3_dout : 8'bz;  // Controlled_Buffer controlled_buffer_15
  assign out_6[15:8] = G7 ? BYTE_3_dout : 8'bz;  // Controlled_Buffer controlled_buffer_16
  assign bit_extender_1_out = {{7{out_6[7]}}, out_6[7]};  // Bit_Extender bit_extender_1
  and and_16 (and_16_out, B, ~Funct3[2]);  // AND_Gate
  // Probe on out_6
  assign out_6[15:8] = and_16_out ? bit_extender_1_out : 8'bz;  // Controlled_Buffer controlled_buffer_17
  assign out_6[23:16] = and_16_out ? bit_extender_1_out : 8'bz;  // Controlled_Buffer controlled_buffer_18
  assign out_6[31:24] = and_16_out ? bit_extender_1_out : 8'bz;  // Controlled_Buffer controlled_buffer_19
  assign bit_extender_2_out = {{7{out_6[15]}}, out_6[15]};  // Bit_Extender bit_extender_2
  and and_17 (and_17_out, H, ~Funct3[2]);  // AND_Gate
  // Probe on bit_extender_1_out
  assign out_6[23:16] = and_17_out ? bit_extender_2_out : 8'bz;  // Controlled_Buffer controlled_buffer_20
  assign out_6[31:24] = and_17_out ? bit_extender_2_out : 8'bz;  // Controlled_Buffer controlled_buffer_21
  Pull_Resistor pull_resistor_5 (.node(out_6[7:0]));
  Pull_Resistor pull_resistor_6 (.node(out_6[15:8]));
  Pull_Resistor pull_resistor_7 (.node(out_6[23:16]));
  Pull_Resistor pull_resistor_8 (.node(out_6[31:24]));

  // Other names for the same wires on the sheet: Adr[31:0] = Adress; Funct3_2 = Funct3[2]; W = G3

  // Notes on the sheet:
  //   Byte
  //   Half
  //   Word
  //   Byte
  //   Half
  //   Word
endmodule

module Data_memory_v6 (
  input  [31:0] Adress,
  input  [31:0] Data,
  input  [2:0] Funct3,
  input  Clock,
  input  Store,
  input  [14:0] GPU_ADR,
  output [31:0] out_7,
  output [31:0] GPU_DATA,
  output Exception,
  output [15:0] GPU_colors
);

  wire and_6_out, and_8_out, and_9_out, and_10_out, and_11_out, and_12_out, and_13_out, and_14_out,
       and_15_out, and_16_out, and_17_out, and_18_out, and_19_out, and_20_out, and_21_out, and_22_out,
       and_23_out, and_24_out, and_26_out, and_27_out, and_28_out, and_29_out, and_30_out, and_31_out,
       and_32_out, and_33_out, and_34_out, B, B0, B1, B2, B3, decoder_3_out0, decoder_3_out1, decoder_3_out2,
       decoder_3_out3, decoder_4_out0, decoder_4_out1, G1, G2, G3, G5, G7, H, H0, or_5_out, or_6_out,
       or_7_out, or_8_out, or_9_out, or_10_out, or_11_out, or_12_out, s0, s1, s2, s3, Set_out;
  wire [7:0] bit_extender_1_out, bit_extender_2_out, BYTE_0_dout, BYTE_1_dout, BYTE_2_dout, BYTE_3_dout,
       register_1_q, register_2_q, register_3_q, register_4_q, register_6_q, register_8_q, undriven;
  wire [14:0] multiplexer_1_out;
  wire [31:0] controlled_buffer_1_out;

  Decoder #(.enable("false"), .select(2)) decoder_1 (.out0(B), .out1(H), .out2(G3), .sel(Funct3[1:0]));  // open: out3
  Decoder #(.enable("false"), .select(2)) decoder_2 (.out0(s0), .out1(s1), .out2(s2), .out3(s3), .sel(Adress[1:0]));
  and and_1 (B0, B, s0);
  and and_2 (B1, B, s1);
  and and_3 (B2, B, s2);
  and and_4 (B3, B, s3);
  and and_5 (H0, H, s0);
  and and_6 (and_6_out, H, s1);
  and and_7 (G7, H, s2);
  and and_8 (and_8_out, H, s3);
  and and_9 (and_9_out, G3, s1);
  and and_10 (and_10_out, G3, s2);
  and and_11 (and_11_out, G3, s3);
  or or_1 (Exception, and_11_out, and_10_out, and_9_out, and_8_out, and_6_out);
  LED led_1 (.in(Exception));
  or or_2 (G1, G3, B0, H0);
  or or_3 (G2, G3, H0);
  or or_4 (G5, B2, G7);
  assign controlled_buffer_1_out[7:0] = G1 ? Data[7:0] : 8'bz;  // Controlled_Buffer controlled_buffer_1
  assign controlled_buffer_1_out[15:8] = G2 ? Data[15:8] : 8'bz;  // Controlled_Buffer controlled_buffer_2
  assign controlled_buffer_1_out[23:16] = G3 ? Data[23:16] : 8'bz;  // Controlled_Buffer controlled_buffer_3
  assign controlled_buffer_1_out[31:24] = G3 ? Data[31:24] : 8'bz;  // Controlled_Buffer controlled_buffer_4
  and and_12 (and_12_out, Adress[18], Store);
  Decoder #(.select(2)) decoder_3 (
    .out0(decoder_3_out0), .out1(decoder_3_out1), .out2(decoder_3_out2), .out3(decoder_3_out3),
    .sel(Adress[1:0]), .en(and_12_out));
  Decoder #(.select(2)) decoder_4 (
    .out0(decoder_4_out0), .out1(decoder_4_out1), .sel(Adress[3:2]), .en(and_12_out));  // open: out2, out3
  assign controlled_buffer_1_out[15:8] = B1 ? Data[7:0] : 8'bz;  // Controlled_Buffer controlled_buffer_5
  assign controlled_buffer_1_out[23:16] = G5 ? Data[7:0] : 8'bz;  // Controlled_Buffer controlled_buffer_6
  assign controlled_buffer_1_out[31:24] = B3 ? Data[7:0] : 8'bz;  // Controlled_Buffer controlled_buffer_7
  assign controlled_buffer_1_out[31:24] = G7 ? Data[15:8] : 8'bz;  // Controlled_Buffer controlled_buffer_8
  or or_5 (or_5_out, B0, H0, G3);
  or or_6 (or_6_out, B1, H0, G3);
  or or_7 (or_7_out, B2, G7, G3);
  or or_8 (or_8_out, B3, G7, G3);
  // Probe on controlled_buffer_1_out
  and and_13 (and_13_out, and_17_out, or_5_out);
  and and_14 (and_14_out, and_17_out, or_6_out);
  and and_15 (and_15_out, and_17_out, or_7_out);
  and and_16 (and_16_out, and_17_out, or_8_out);
  and and_17 (and_17_out, Store, ~Adress[17]);  // AND_Gate
  or or_9 (or_9_out, B0, H0, G3);
  or or_10 (or_10_out, B1, H0, G3);
  or or_11 (or_11_out, B2, G7, G3);
  or or_12 (or_12_out, B3, G7, G3);
  and and_18 (and_18_out, Store, Adress[17]);
  Pull_Resistor pull_resistor_1 (.node(controlled_buffer_1_out[31:24]));
  Pull_Resistor pull_resistor_2 (.node(controlled_buffer_1_out[23:16]));
  Pull_Resistor pull_resistor_3 (.node(controlled_buffer_1_out[15:8]));
  Pull_Resistor pull_resistor_4 (.node(controlled_buffer_1_out[7:0]));
  and and_19 (and_19_out, and_18_out, or_9_out);
  and and_20 (and_20_out, and_18_out, or_10_out);
  and and_21 (and_21_out, and_18_out, or_11_out);
  and and_22 (and_22_out, and_18_out, or_12_out);
  and and_23 (and_23_out, decoder_4_out0, decoder_3_out3);
  and and_24 (and_24_out, decoder_4_out1, decoder_3_out3);
  // AND_Gate and_25 is placed but not wired
  Multiplexer #(.enable("false"), .width(15)) multiplexer_1 (
    .in0(GPU_ADR), .in1(Adress[16:2]), .out(multiplexer_1_out), .sel(Adress[17]));
  Register register_1 (
    .D(controlled_buffer_1_out[31:24]), .en(and_23_out), .Q(register_1_q), .clk(Clock));  // open: clr
  Register register_2 (
    .D(controlled_buffer_1_out[31:24]), .en(and_24_out), .Q(register_2_q), .clk(Clock));  // open: clr
  Register register_3 (
    .D(controlled_buffer_1_out[23:16]), .en(and_26_out), .Q(register_3_q), .clk(Clock));  // open: clr
  and and_26 (and_26_out, decoder_4_out0, decoder_3_out2);
  Register register_4 (
    .D(controlled_buffer_1_out[23:16]), .en(and_27_out), .Q(register_4_q), .clk(Clock));  // open: clr
  and and_27 (and_27_out, decoder_4_out1, decoder_3_out2);
  RAM #(.addrWidth(15)) BYTE_0 (
    .addr(Adress[16:2]), .we(and_13_out), .clk(Clock), .din(controlled_buffer_1_out[7:0]), .dout(BYTE_0_dout));
  RAM #(.addrWidth(15)) BYTE_1 (
    .addr(Adress[16:2]), .we(and_14_out), .clk(Clock), .din(controlled_buffer_1_out[15:8]), .dout(BYTE_1_dout));
  RAM #(.addrWidth(15)) BYTE_2 (
    .addr(Adress[16:2]), .we(and_15_out), .clk(Clock), .din(controlled_buffer_1_out[23:16]),
    .dout(BYTE_2_dout));
  RAM #(.addrWidth(15)) BYTE_3 (
    .addr(Adress[16:2]), .we(and_16_out), .clk(Clock), .din(controlled_buffer_1_out[31:24]),
    .dout(BYTE_3_dout));
  RAM #(.addrWidth(15)) ram_1 (
    .addr(multiplexer_1_out), .we(and_19_out), .clk(Clock), .din(controlled_buffer_1_out[7:0]),
    .dout(GPU_DATA[7:0]));
  RAM #(.addrWidth(15)) ram_2 (
    .addr(multiplexer_1_out), .we(and_20_out), .clk(Clock), .din(controlled_buffer_1_out[15:8]),
    .dout(GPU_DATA[15:8]));
  RAM #(.addrWidth(15)) ram_3 (
    .addr(multiplexer_1_out), .we(and_21_out), .clk(Clock), .din(controlled_buffer_1_out[23:16]),
    .dout(GPU_DATA[23:16]));
  RAM #(.addrWidth(15)) ram_4 (
    .addr(multiplexer_1_out), .we(and_22_out), .clk(Clock), .din(controlled_buffer_1_out[31:24]),
    .dout(GPU_DATA[31:24]));
  Register register_5 (
    .D(controlled_buffer_1_out[15:8]), .en(and_28_out), .Q(GPU_colors[15:8]), .clk(Clock));  // open: clr
  and and_28 (and_28_out, decoder_4_out0, decoder_3_out1);
  Register register_6 (.D(controlled_buffer_1_out[15:8]), .en(and_29_out), .Q(register_6_q), .clk(Clock));  // open: clr
  and and_29 (and_29_out, decoder_4_out1, decoder_3_out1);
  and and_30 (and_30_out, decoder_4_out0, decoder_3_out0);
  Register register_7 (
    .D(controlled_buffer_1_out[7:0]), .en(and_30_out), .Q(GPU_colors[7:0]), .clk(Clock));  // open: clr
  Register register_8 (.D(undriven), .Q(register_8_q), .clk(Set_out));  // open: en, clr
  Button Set (.out(Set_out));
  // Probe on register_6_q
  assign out_7[7:0] = and_31_out ? BYTE_0_dout : 8'bz;  // Controlled_Buffer controlled_buffer_9
  assign out_7[15:8] = G2 ? BYTE_1_dout : 8'bz;  // Controlled_Buffer controlled_buffer_10
  assign out_7[23:16] = G3 ? BYTE_2_dout : 8'bz;  // Controlled_Buffer controlled_buffer_11
  assign out_7[31:24] = G3 ? BYTE_3_dout : 8'bz;  // Controlled_Buffer controlled_buffer_12
  assign out_7[7:0] = and_32_out ? register_8_q : 8'bz;  // Controlled_Buffer controlled_buffer_13
  // DipSwitch dipswitch_1: pin names not known
  assign out_7[7:0] = B1 ? BYTE_1_dout : 8'bz;  // Controlled_Buffer controlled_buffer_14
  and and_31 (and_31_out, G1, ~Adress[18]);  // AND_Gate
  and and_32 (and_32_out, G1, Adress[18]);
  assign out_7[7:0] = G5 ? BYTE_2_dout : 8'bz;  // Controlled_Buffer controlled_buffer_15
  assign out_7[7:0] = B3 ? BYTE_3_dout : 8'bz;  // Controlled_Buffer controlled_buffer_16
  assign out_7[15:8] = G7 ? BYTE_3_dout : 8'bz;  // Controlled_Buffer controlled_buffer_17
  assign bit_extender_1_out = {{7{out_7[7]}}, out_7[7]};  // Bit_Extender bit_extender_1
  and and_33 (and_33_out, B, ~Funct3[2]);  // AND_Gate
  // Probe on out_7
  assign out_7[15:8] = and_33_out ? bit_extender_1_out : 8'bz;  // Controlled_Buffer controlled_buffer_18
  assign out_7[23:16] = and_33_out ? bit_extender_1_out : 8'bz;  // Controlled_Buffer controlled_buffer_19
  assign out_7[31:24] = and_33_out ? bit_extender_1_out : 8'bz;  // Controlled_Buffer controlled_buffer_20
  assign bit_extender_2_out = {{7{out_7[15]}}, out_7[15]};  // Bit_Extender bit_extender_2
  and and_34 (and_34_out, H, ~Funct3[2]);  // AND_Gate
  // Probe on bit_extender_1_out
  assign out_7[23:16] = and_34_out ? bit_extender_2_out : 8'bz;  // Controlled_Buffer controlled_buffer_21
  assign out_7[31:24] = and_34_out ? bit_extender_2_out : 8'bz;  // Controlled_Buffer controlled_buffer_22
  Pull_Resistor pull_resistor_5 (.node(out_7[7:0]));
  Pull_Resistor pull_resistor_6 (.node(out_7[15:8]));
  Pull_Resistor pull_resistor_7 (.node(out_7[23:16]));
  Pull_Resistor pull_resistor_8 (.node(out_7[31:24]));

  // Other names for the same wires on the sheet: Adr[31:0] = Adress; Store_to_VRAM = Adress[17];
  //   VRAM[14:0] = Adress[31:17]; Store_to_Special_registers = Adress[18]; clk = Clock; Funct3_2 = Funct3[2]; G4 = B1;
  //   G6 = B3; H1 = G7; W = G3

  // Notes on the sheet:
  //   Byte
  //   Half
  //   Word
  //   Byte
  //   Half
  //   Word
  //   Second
  //   Output
  //   First
  //   Input
endmodule

module Data_memory_v7 (
  input  Load,
  input  Store,
  input  Clock,
  input  [31:0] Data,
  input  [2:0] Funct3,
  input  [31:0] Adress,
  input  [14:0] GPU_ADR,
  output [31:0] out_8,
  output Exception,
  output [31:0] GPU_DATA,
  output [15:0] GPU_colors
);

  wire and_1_out, and_2_out, and_3_out, and_4_out, and_9_out, and_14_out, and_15_out, and_16_out, and_17_out,
       and_18_out, and_19_out, and_20_out, and_21_out, B, B0, B1, B2, B3, BO0, BO1, BO2, BO3, decoder_1_out0,
       decoder_1_out1, decoder_1_out2, decoder_1_out3, decoder_1_out6, decoder_1_out7, decoder_4_out2, G1,
       G2, G3, G5, G7, H, H0, H2, H3, HO0, HO1, HO2, HO3, in1_ac, in2_ac, iS4Clk, iS5Clk, not_1_out,
       not_2_out, or_4_out, or_5_out, or_6_out, or_7_out, or_9_out, or_10_out, or_11_out, or_12_out,
       or_13_out, or_14_out, or_15_out, Store_R0, Store_R1, Store_R2, Store_R3, to_SP, to_SRAM, to_VRAM, W1,
       W2, W3, WO0, WO1, WO2, WO3;
  wire [7:0] bit_extender_1_out, bit_extender_2_out, in1, in2, iS4, iS5, S2, S3, S6, S7;
  wire [14:0] multiplexer_1_out;
  wire [31:0] Memory_data;

  // Probe on GPU_colors[7:0]
  // Probe on GPU_colors[15:8]
  // Probe on S2
  // Probe on S3
  // Probe on in1
  // Probe on in2
  // Probe on S6
  // Probe on S7
  and and_1 (and_1_out, Clock, Store);
  and and_2 (and_2_out, to_SP, and_1_out);
  Decoder #(.select(4)) decoder_1 (
    .out0(decoder_1_out0), .out1(decoder_1_out1), .out2(decoder_1_out2), .out3(decoder_1_out3),
    .out6(decoder_1_out6), .out7(decoder_1_out7), .sel(Adress[3:0]), .en(and_2_out));  // open: out4, out5, out8, out9, out10, out11, out12, out13, out14, out15
  and and_3 (and_3_out, to_SP, Load);
  Decoder #(.select(4)) decoder_2 (
    .out4(in1_ac), .out5(in2_ac), .sel(Adress[3:0]), .en(and_3_out));  // open: out0, out1, out2, out3, out6, out7, out8, out9, out10, out11, out12, out13, out14, out15
  or or_1 (Exception, W3, W2, W1, H3, G7);
  LED led_1 (.in(Exception));
  Button button_1 (.out(iS4Clk));
  // DipSwitch dipswitch_1: pin names not known
  Button button_2 (.out(iS5Clk));
  // DipSwitch dipswitch_2: pin names not known
  Register SReg_3 (.D(Memory_data[31:24]), .en(1'b1), .Q(S3), .clk(decoder_1_out3), .clr(1'b0));
  Register SReg_7 (.D(Memory_data[31:24]), .en(1'b1), .Q(S7), .clk(decoder_1_out7));  // open: clr
  Register SReg_2 (.D(Memory_data[23:16]), .en(1'b1), .Q(S2), .clk(decoder_1_out2), .clr(1'b0));
  Register SReg_6 (.D(Memory_data[23:16]), .en(1'b1), .Q(S6), .clk(decoder_1_out6));  // open: clr
  or or_2 (G1, G3, B0, H0);
  or or_3 (G2, G3, H0);
  Register SReg_1 (.D(Memory_data[15:8]), .en(1'b1), .Q(GPU_colors[15:8]), .clk(decoder_1_out1), .clr(1'b0));
  Register SReg_5 (.D(iS5), .en(1'b1), .Q(in2), .clk(iS5Clk));  // open: clr
  assign Memory_data[7:0] = G1 ? Data[7:0] : 8'bz;  // Controlled_Buffer controlled_buffer_1
  buf or_4 (or_4_out, G1);  // OR_Gate
  or or_5 (or_5_out, G2, B1);
  or or_6 (or_6_out, G3, G5);
  or or_7 (or_7_out, G3, B3, G7);
  and and_4 (and_4_out, Store, to_SRAM);
  assign Memory_data[15:8] = G2 ? Data[15:8] : 8'bz;  // Controlled_Buffer controlled_buffer_2
  assign Memory_data[23:16] = G3 ? Data[23:16] : 8'bz;  // Controlled_Buffer controlled_buffer_3
  assign Memory_data[31:24] = G3 ? Data[31:24] : 8'bz;  // Controlled_Buffer controlled_buffer_4
  and and_5 (Store_R0, and_4_out, or_4_out);
  and and_6 (Store_R1, and_4_out, or_5_out);
  and and_7 (Store_R2, and_4_out, or_6_out);
  and and_8 (Store_R3, and_4_out, or_7_out);
  Register SReg_0 (.D(Memory_data[7:0]), .en(1'b1), .Q(GPU_colors[7:0]), .clk(decoder_1_out0), .clr(1'b0));
  Register SReg_4 (.D(iS4), .en(1'b1), .Q(in1), .clk(iS4Clk));  // open: clr
  assign Memory_data[15:8] = B1 ? Data[7:0] : 8'bz;  // Controlled_Buffer controlled_buffer_5
  assign Memory_data[23:16] = G5 ? Data[7:0] : 8'bz;  // Controlled_Buffer controlled_buffer_6
  or or_8 (G5, B2, G7);
  Pull_Resistor pull_resistor_1 (.node(Memory_data[31:24]));
  assign Memory_data[31:24] = B3 ? Data[7:0] : 8'bz;  // Controlled_Buffer controlled_buffer_7
  assign Memory_data[31:24] = G7 ? Data[15:8] : 8'bz;  // Controlled_Buffer controlled_buffer_8
  Pull_Resistor pull_resistor_2 (.node(Memory_data[23:16]));
  Pull_Resistor pull_resistor_3 (.node(Memory_data[15:8]));
  Pull_Resistor pull_resistor_4 (.node(Memory_data[7:0]));
  and and_9 (and_9_out, to_SRAM, Load);
  Decoder #(.select(4)) decoder_3 (
    .out0(B0), .out1(B1), .out2(B2), .out3(B3), .out4(H0), .out5(G7), .out6(H2), .out7(H3), .out8(G3),
    .out9(W1), .out10(W2), .out11(W3), .sel({Funct3[1:0], Adress[1:0]}), .en(Store));  // open: out12, out13, out14, out15
  not not_1 (not_1_out, Adress[30]);
  not not_2 (not_2_out, Adress[31]);
  RAM #(.addrWidth(18), .databus("bidir")) BYTE_0 (.addr(Adress[19:2]), .data(Memory_data[7:0]));  // open: we, oe, clk
  RAM #(.addrWidth(18), .databus("bidir")) BYTE_1 (.addr(Adress[19:2]), .data(Memory_data[15:8]));  // open: we, oe, clk
  RAM #(.addrWidth(18), .databus("bidir")) BYTE_2 (
    .addr(Adress[19:2]), .data(Memory_data[23:16]));  // open: we, oe, clk
  RAM #(.addrWidth(18), .databus("bidir")) BYTE_3 (
    .addr(Adress[19:2]), .data(Memory_data[31:24]));  // open: we, oe, clk
  and and_10 (to_VRAM, Adress[30], not_2_out);
  and and_11 (to_SP, not_1_out, Adress[31]);
  and and_12 (to_SRAM, not_1_out, not_2_out);
  or or_9 (or_9_out, WO0, BO0, HO0);
  or or_10 (or_10_out, WO0, HO0);
  // AND_Gate and_13 is placed but not wired
  assign out_8[7:0] = or_9_out ? Memory_data[7:0] : 8'bz;  // Controlled_Buffer controlled_buffer_9
  assign out_8[15:8] = or_10_out ? Memory_data[15:8] : 8'bz;  // Controlled_Buffer controlled_buffer_10
  assign out_8[23:16] = WO0 ? Memory_data[23:16] : 8'bz;  // Controlled_Buffer controlled_buffer_11
  assign out_8[31:24] = WO0 ? Memory_data[31:24] : 8'bz;  // Controlled_Buffer controlled_buffer_12
  Decoder #(.enable("false"), .select(2)) decoder_4 (
    .out0(B), .out1(H), .out2(decoder_4_out2), .sel(Funct3[1:0]));  // open: out3
  assign out_8[7:0] = in1_ac ? in1 : 8'bz;  // Controlled_Buffer controlled_buffer_13
  assign out_8[7:0] = in2_ac ? in2 : 8'bz;  // Controlled_Buffer controlled_buffer_14
  assign out_8[7:0] = BO1 ? Memory_data[15:8] : 8'bz;  // Controlled_Buffer controlled_buffer_15
  or or_11 (or_11_out, B0, H0, G3);
  or or_12 (or_12_out, B1, H0, G3);
  or or_13 (or_13_out, B2, G7, G3);
  or or_14 (or_14_out, B3, G7, G3);
  assign out_8[7:0] = or_15_out ? Memory_data[23:16] : 8'bz;  // Controlled_Buffer controlled_buffer_16
  assign out_8[7:0] = BO3 ? Memory_data[31:24] : 8'bz;  // Controlled_Buffer controlled_buffer_17
  or or_15 (or_15_out, BO2, HO1);
  and and_14 (and_14_out, and_18_out, or_11_out);
  and and_15 (and_15_out, and_18_out, or_12_out);
  and and_16 (and_16_out, and_18_out, or_13_out);
  and and_17 (and_17_out, and_18_out, or_14_out);
  and and_18 (and_18_out, Store, to_VRAM);
  assign out_8[15:8] = HO1 ? Memory_data[31:24] : 8'bz;  // Controlled_Buffer controlled_buffer_18
  Multiplexer #(.enable("false"), .width(15)) multiplexer_1 (
    .in0(GPU_ADR), .in1(Adress[16:2]), .out(multiplexer_1_out), .sel(to_VRAM));
  assign bit_extender_1_out = {{7{out_8[7]}}, out_8[7]};  // Bit_Extender bit_extender_1
  and and_19 (and_19_out, B, ~Funct3[2], Load);  // AND_Gate
  RAM #(.addrWidth(15)) ram_1 (
    .addr(multiplexer_1_out), .we(and_14_out), .clk(Clock), .din(Memory_data[7:0]), .dout(GPU_DATA[7:0]));
  RAM #(.addrWidth(15)) ram_2 (
    .addr(multiplexer_1_out), .we(and_15_out), .clk(Clock), .din(Memory_data[15:8]), .dout(GPU_DATA[15:8]));
  RAM #(.addrWidth(15)) ram_3 (
    .addr(multiplexer_1_out), .we(and_16_out), .clk(Clock), .din(Memory_data[23:16]), .dout(GPU_DATA[23:16]));
  RAM #(.addrWidth(15)) ram_4 (
    .addr(multiplexer_1_out), .we(and_17_out), .clk(Clock), .din(Memory_data[31:24]), .dout(GPU_DATA[31:24]));
  assign out_8[15:8] = and_19_out ? bit_extender_1_out : 8'bz;  // Controlled_Buffer controlled_buffer_19
  assign out_8[23:16] = and_19_out ? bit_extender_1_out : 8'bz;  // Controlled_Buffer controlled_buffer_20
  assign out_8[31:24] = and_19_out ? bit_extender_1_out : 8'bz;  // Controlled_Buffer controlled_buffer_21
  assign bit_extender_2_out = {{7{out_8[15]}}, out_8[15]};  // Bit_Extender bit_extender_2
  and and_20 (and_20_out, H, ~Funct3[2], Load);  // AND_Gate
  // Probe on bit_extender_1_out
  assign out_8[23:16] = and_20_out ? bit_extender_2_out : 8'bz;  // Controlled_Buffer controlled_buffer_22
  assign out_8[31:24] = and_20_out ? bit_extender_2_out : 8'bz;  // Controlled_Buffer controlled_buffer_23
  Decoder #(.select(4)) decoder_5 (
    .out0(BO0), .out1(BO1), .out2(BO2), .out3(BO3), .out4(HO0), .out5(HO1), .out6(HO2), .out7(HO3),
    .out8(WO0), .out9(WO1), .out10(WO2), .out11(WO3), .sel({Funct3[1:0], Adress[1:0]}), .en(and_21_out));  // open: out12, out13, out14, out15
  and and_21 (and_21_out, ~to_SP, Load);  // AND_Gate
  // OR_Gate or_16 is placed but not wired

  // Other names for the same wires on the sheet: Adr[31:0] = Adress; Byte_adr[1:0] = Adress[1:0];
  //   Funct_3[2:0] = Funct3; RAM_adress[17:0] = Adress[19:2]; Store_to_VRAM = Adress[30];
  //   Store_to_Special_registers = Adress[31]; clk = Clock; Funct3_2 = Funct3[2]; G4 = B1; G6 = B3;
  //   S0[7:0] = GPU_colors[7:0]; S1[7:0] = GPU_colors[15:8]; H1 = G7; S4[7:0] = in1; S5[7:0] = in2;
  //   Input_data[31:0] = Data; W0 = G3

  // Notes on the sheet:
  //   Register 0
  //   Register 1
  //   Register 2
  //   Register 3
  //   Register 4
  //   Register 5
  //   Register 6
  //   Register 7
  //   Special Registers
  //   In
  //   Special Registers
  //   Unaligned adressing detector
  //   DATA MEMORY
  //   Store and CLK!!
  //   First Input
  //   Second Input
  //   Storing data
  //   RAM selector - for store
  //   Byte steering logic - input
  //   byte
  //   RAM_ADRESS
  //   SRAM
  //   Function decoder
  //   Loading data
  //   VRAM
  //   Function decoder for byte steering
  //   Byte
  //   Half
  //   Word
  //   Byte steering logic - output
  //   Function decoder
endmodule

module Data_memory_v8 (
  input  Load,
  input  Store,
  input  Clock,
  input  [31:0] Data,
  input  [2:0] Funct3,
  input  [31:0] Adress,
  input  [14:0] GPU_ADR,
  output [31:0] out_8,
  output Exception,
  output [31:0] GPU_DATA,
  output [15:0] GPU_colors
);

  wire and_1_out, and_2_out, and_3_out, and_6_out, and_12_out, and_16_out, and_17_out, and_19_out,
       and_20_out, and_21_out, and_22_out, and_23_out, and_25_out, B, B0, B1, B2, B3, BO0, BO1, BO2, BO3,
       decoder_1_out0, decoder_1_out1, decoder_1_out2, decoder_1_out3, decoder_1_out6, decoder_1_out7,
       decoder_2_out0, decoder_2_out1, decoder_2_out2, decoder_2_out3, decoder_2_out4, decoder_2_out5,
       decoder_2_out6, decoder_2_out7, decoder_2_out8, decoder_2_out9, decoder_2_out10, decoder_2_out11,
       decoder_2_out12, decoder_2_out13, decoder_2_out14, decoder_2_out15, decoder_3_out0, decoder_3_out1,
       decoder_3_out2, decoder_3_out3, decoder_3_out4, decoder_3_out5, decoder_3_out6, decoder_3_out7,
       decoder_3_out8, decoder_3_out9, decoder_3_out10, decoder_3_out11, decoder_3_out12, decoder_3_out13,
       decoder_3_out14, decoder_3_out15, decoder_4_out2, decoder_5_out0, decoder_5_out1, decoder_5_out2,
       decoder_5_out3, decoder_5_out4, decoder_5_out5, decoder_5_out6, decoder_5_out7, decoder_5_out8,
       decoder_5_out9, decoder_5_out10, decoder_5_out11, decoder_5_out12, decoder_5_out13, decoder_5_out14,
       decoder_5_out15, G1, G2, G3, G5, G7, H, H0, H2, H3, HO0, HO1, HO2, HO3, in1_ac, in2_ac, iS4Clk,
       iS5Clk, nand_1_out, nand_2_out, nand_3_out, nand_4_out, nand_5_out, nand_6_out, nand_7_out,
       nand_8_out, not_17_out, not_18_out, not_19_out, not_20_out, not_21_out, not_22_out, not_23_out,
       not_24_out, not_25_out, not_26_out, not_27_out, not_44_out, not_45_out, not_46_out, not_47_out,
       not_48_out, not_49_out, not_50_out, not_51_out, not_52_out, not_53_out, not_54_out, not_55_out,
       not_56_out, not_57_out, not_58_out, not_59_out, Store_R0, Store_R1, Store_R2, Store_R3, to_SP,
       to_SRAM, to_VRAM, W1, W2, W3, WO0, WO1, WO2, WO3;
  wire [7:0] bit_extender_1_out, bit_extender_2_out, in1, in2, iS4, iS5, S2, S3, S6, S7;
  wire [14:0] multiplexer_1_out;
  wire [31:0] Memory_data;

  // Probe on GPU_colors[7:0]
  // Probe on GPU_colors[15:8]
  // Probe on S2
  // Probe on S3
  // Probe on in1
  // Probe on in2
  // Probe on S6
  // Probe on S7
  and and_1 (and_1_out, Clock, Store);
  and and_2 (and_2_out, to_SP, and_1_out);
  Decoder #(.select(4)) decoder_1 (
    .out0(decoder_1_out0), .out1(decoder_1_out1), .out2(decoder_1_out2), .out3(decoder_1_out3),
    .out6(decoder_1_out6), .out7(decoder_1_out7), .sel(Adress[3:0]), .en(and_2_out));  // open: out4, out5, out8, out9, out10, out11, out12, out13, out14, out15
  and and_3 (and_3_out, to_SP, Load);
  Decoder #(.select(4)) decoder_2 (
    .out0(decoder_2_out0), .out1(decoder_2_out1), .out2(decoder_2_out2), .out3(decoder_2_out3),
    .out4(decoder_2_out4), .out5(decoder_2_out5), .out6(decoder_2_out6), .out7(decoder_2_out7),
    .out8(decoder_2_out8), .out9(decoder_2_out9), .out10(decoder_2_out10), .out11(decoder_2_out11),
    .out12(decoder_2_out12), .out13(decoder_2_out13), .out14(decoder_2_out14), .out15(decoder_2_out15),
    .sel(Adress[3:0]), .en(and_3_out));
  nor nor_1 (Exception, W3, W2, W1, H3, G7);
  LED led_1 (.in(Exception));
  // NOT_Gate not_1 has open pins: in=decoder_2_out0, out=open
  // NOT_Gate not_2 has open pins: in=decoder_2_out1, out=open
  // NOT_Gate not_3 has open pins: in=decoder_2_out2, out=open
  // NOT_Gate not_4 has open pins: in=decoder_2_out3, out=open
  not not_5 (in1_ac, decoder_2_out4);
  not not_6 (in2_ac, decoder_2_out5);
  // NOT_Gate not_7 has open pins: in=decoder_2_out6, out=open
  // NOT_Gate not_8 has open pins: in=decoder_2_out7, out=open
  // NOT_Gate not_9 has open pins: in=decoder_2_out8, out=open
  // NOT_Gate not_10 has open pins: in=decoder_2_out9, out=open
  // NOT_Gate not_11 has open pins: in=decoder_2_out10, out=open
  // NOT_Gate not_12 has open pins: in=decoder_2_out11, out=open
  // NOT_Gate not_13 has open pins: in=decoder_2_out12, out=open
  // NOT_Gate not_14 has open pins: in=decoder_2_out13, out=open
  // NOT_Gate not_15 has open pins: in=decoder_2_out14, out=open
  // NOT_Gate not_16 has open pins: in=decoder_2_out15, out=open
  Button button_1 (.out(iS4Clk));
  // DipSwitch dipswitch_1: pin names not known
  Button button_2 (.out(iS5Clk));
  // DipSwitch dipswitch_2: pin names not known
  Register SReg_3 (.D(Memory_data[31:24]), .en(1'b1), .Q(S3), .clk(decoder_1_out3), .clr(1'b0));
  Register SReg_7 (.D(Memory_data[31:24]), .en(1'b1), .Q(S7), .clk(decoder_1_out7));  // open: clr
  Register SReg_2 (.D(Memory_data[23:16]), .en(1'b1), .Q(S2), .clk(decoder_1_out2), .clr(1'b0));
  Register SReg_6 (.D(Memory_data[23:16]), .en(1'b1), .Q(S6), .clk(decoder_1_out6));  // open: clr
  and and_4 (G1, G3, B0, H0);
  and and_5 (G2, G3, H0);
  Register SReg_1 (.D(Memory_data[15:8]), .en(1'b1), .Q(GPU_colors[15:8]), .clk(decoder_1_out1), .clr(1'b0));
  Register SReg_5 (.D(iS5), .en(1'b1), .Q(in2), .clk(iS5Clk));  // open: clr
  assign Memory_data[7:0] = not_17_out ? Data[7:0] : 8'bz;  // Controlled_Buffer controlled_buffer_1
  not not_17 (not_17_out, G1);
  not not_18 (not_18_out, G2);
  not not_19 (not_19_out, G1);
  nand nand_1 (nand_1_out, G2, B1);
  nand nand_2 (nand_2_out, G3, G5);
  nand nand_3 (nand_3_out, G3, B3, G7);
  and and_6 (and_6_out, Store, to_SRAM);
  assign Memory_data[15:8] = not_18_out ? Data[15:8] : 8'bz;  // Controlled_Buffer controlled_buffer_2
  assign Memory_data[23:16] = not_20_out ? Data[23:16] : 8'bz;  // Controlled_Buffer controlled_buffer_3
  assign Memory_data[31:24] = not_21_out ? Data[31:24] : 8'bz;  // Controlled_Buffer controlled_buffer_4
  not not_20 (not_20_out, G3);
  not not_21 (not_21_out, G3);
  and and_7 (Store_R0, and_6_out, not_19_out);
  and and_8 (Store_R1, and_6_out, nand_1_out);
  and and_9 (Store_R2, and_6_out, nand_2_out);
  and and_10 (Store_R3, and_6_out, nand_3_out);
  Register SReg_0 (.D(Memory_data[7:0]), .en(1'b1), .Q(GPU_colors[7:0]), .clk(decoder_1_out0), .clr(1'b0));
  Register SReg_4 (.D(iS4), .en(1'b1), .Q(in1), .clk(iS4Clk));  // open: clr
  assign Memory_data[15:8] = not_22_out ? Data[7:0] : 8'bz;  // Controlled_Buffer controlled_buffer_5
  assign Memory_data[23:16] = not_23_out ? Data[7:0] : 8'bz;  // Controlled_Buffer controlled_buffer_6
  not not_22 (not_22_out, B1);
  not not_23 (not_23_out, G5);
  not not_24 (not_24_out, B3);
  and and_11 (G5, B2, G7);
  Pull_Resistor pull_resistor_1 (.node(Memory_data[31:24]));
  assign Memory_data[31:24] = not_24_out ? Data[7:0] : 8'bz;  // Controlled_Buffer controlled_buffer_7
  assign Memory_data[31:24] = not_25_out ? Data[15:8] : 8'bz;  // Controlled_Buffer controlled_buffer_8
  not not_25 (not_25_out, G7);
  Pull_Resistor pull_resistor_2 (.node(Memory_data[23:16]));
  Pull_Resistor pull_resistor_3 (.node(Memory_data[15:8]));
  Pull_Resistor pull_resistor_4 (.node(Memory_data[7:0]));
  and and_12 (and_12_out, to_SRAM, Load);
  Decoder #(.select(4)) decoder_3 (
    .out0(decoder_3_out0), .out1(decoder_3_out1), .out2(decoder_3_out2), .out3(decoder_3_out3),
    .out4(decoder_3_out4), .out5(decoder_3_out5), .out6(decoder_3_out6), .out7(decoder_3_out7),
    .out8(decoder_3_out8), .out9(decoder_3_out9), .out10(decoder_3_out10), .out11(decoder_3_out11),
    .out12(decoder_3_out12), .out13(decoder_3_out13), .out14(decoder_3_out14), .out15(decoder_3_out15),
    .sel({Funct3[1:0], Adress[1:0]}), .en(Store));
  not not_26 (not_26_out, Adress[30]);
  not not_27 (not_27_out, Adress[31]);
  RAM #(.addrWidth(17), .databus("bidir")) BYTE_0 (.addr(Adress[18:2]), .data(Memory_data[7:0]));  // open: we, oe, clk
  RAM #(.addrWidth(17), .databus("bidir")) BYTE_1 (.addr(Adress[18:2]), .data(Memory_data[15:8]));  // open: we, oe, clk
  RAM #(.addrWidth(17), .databus("bidir")) BYTE_2 (
    .addr(Adress[18:2]), .data(Memory_data[23:16]));  // open: we, oe, clk
  RAM #(.addrWidth(17), .databus("bidir")) BYTE_3 (
    .addr(Adress[18:2]), .data(Memory_data[31:24]));  // open: we, oe, clk
  not not_28 (B0, decoder_3_out0);
  not not_29 (B1, decoder_3_out1);
  not not_30 (B2, decoder_3_out2);
  not not_31 (B3, decoder_3_out3);
  not not_32 (H0, decoder_3_out4);
  not not_33 (G7, decoder_3_out5);
  not not_34 (H2, decoder_3_out6);
  not not_35 (H3, decoder_3_out7);
  not not_36 (G3, decoder_3_out8);
  not not_37 (W1, decoder_3_out9);
  not not_38 (W2, decoder_3_out10);
  not not_39 (W3, decoder_3_out11);
  // NOT_Gate not_40 has open pins: in=decoder_3_out12, out=open
  // NOT_Gate not_41 has open pins: in=decoder_3_out13, out=open
  // NOT_Gate not_42 has open pins: in=decoder_3_out14, out=open
  // NOT_Gate not_43 has open pins: in=decoder_3_out15, out=open
  and and_13 (to_VRAM, Adress[30], not_27_out);
  and and_14 (to_SP, not_26_out, Adress[31]);
  and and_15 (to_SRAM, not_26_out, not_27_out);
  and and_16 (and_16_out, WO0, BO0, HO0);
  and and_17 (and_17_out, WO0, HO0);
  // AND_Gate and_18 is placed but not wired
  not not_44 (not_44_out, and_16_out);
  not not_45 (not_45_out, in1_ac);
  assign out_8[7:0] = not_44_out ? Memory_data[7:0] : 8'bz;  // Controlled_Buffer controlled_buffer_9
  assign out_8[15:8] = not_46_out ? Memory_data[15:8] : 8'bz;  // Controlled_Buffer controlled_buffer_10
  assign out_8[23:16] = not_47_out ? Memory_data[23:16] : 8'bz;  // Controlled_Buffer controlled_buffer_11
  assign out_8[31:24] = not_48_out ? Memory_data[31:24] : 8'bz;  // Controlled_Buffer controlled_buffer_12
  not not_46 (not_46_out, and_17_out);
  not not_47 (not_47_out, WO0);
  not not_48 (not_48_out, WO0);
  Decoder #(.enable("false"), .select(2)) decoder_4 (
    .out0(B), .out1(H), .out2(decoder_4_out2), .sel(Funct3[1:0]));  // open: out3
  not not_49 (not_49_out, G1);
  nand nand_4 (nand_4_out, G2, B1);
  nand nand_5 (nand_5_out, G3, G5);
  nand nand_6 (nand_6_out, G3, B3, G7);
  and and_19 (and_19_out, Store, to_VRAM);
  assign out_8[7:0] = not_45_out ? in1 : 8'bz;  // Controlled_Buffer controlled_buffer_13
  assign out_8[7:0] = not_50_out ? in2 : 8'bz;  // Controlled_Buffer controlled_buffer_14
  not not_50 (not_50_out, in2_ac);
  and and_20 (and_20_out, and_19_out, not_49_out);
  and and_21 (and_21_out, and_19_out, nand_4_out);
  and and_22 (and_22_out, and_19_out, nand_5_out);
  and and_23 (and_23_out, and_19_out, nand_6_out);
  assign out_8[7:0] = not_51_out ? Memory_data[15:8] : 8'bz;  // Controlled_Buffer controlled_buffer_15
  assign out_8[7:0] = not_52_out ? Memory_data[23:16] : 8'bz;  // Controlled_Buffer controlled_buffer_16
  not not_51 (not_51_out, BO1);
  not not_52 (not_52_out, BO3);
  not not_53 (not_53_out, HO1);
  and and_24 (BO3, BO2, HO1);
  assign out_8[7:0] = not_53_out ? Memory_data[31:24] : 8'bz;  // Controlled_Buffer controlled_buffer_17
  assign out_8[15:8] = not_54_out ? Memory_data[31:24] : 8'bz;  // Controlled_Buffer controlled_buffer_18
  not not_54 (not_54_out, HO1);
  Multiplexer #(.enable("false"), .width(15)) multiplexer_1 (
    .in0(GPU_ADR), .in1(Adress[16:2]), .out(multiplexer_1_out), .sel(to_VRAM));
  assign bit_extender_1_out = {{7{out_8[7]}}, out_8[7]};  // Bit_Extender bit_extender_1
  not not_55 (not_55_out, nand_7_out);
  nand nand_7 (nand_7_out, B, ~Funct3[2], Load);  // NAND_Gate
  RAM #(.addrWidth(15)) ram_1 (
    .addr(multiplexer_1_out), .we(and_20_out), .clk(Clock), .din(Memory_data[7:0]), .dout(GPU_DATA[7:0]));
  RAM #(.addrWidth(15)) ram_2 (
    .addr(multiplexer_1_out), .we(and_21_out), .clk(Clock), .din(Memory_data[15:8]), .dout(GPU_DATA[15:8]));
  RAM #(.addrWidth(15)) ram_3 (
    .addr(multiplexer_1_out), .we(and_22_out), .clk(Clock), .din(Memory_data[23:16]), .dout(GPU_DATA[23:16]));
  RAM #(.addrWidth(15)) ram_4 (
    .addr(multiplexer_1_out), .we(and_23_out), .clk(Clock), .din(Memory_data[31:24]), .dout(GPU_DATA[31:24]));
  assign out_8[15:8] = not_55_out ? bit_extender_1_out : 8'bz;  // Controlled_Buffer controlled_buffer_19
  not not_56 (not_56_out, nand_7_out);
  assign out_8[23:16] = not_56_out ? bit_extender_1_out : 8'bz;  // Controlled_Buffer controlled_buffer_20
  not not_57 (not_57_out, nand_7_out);
  assign out_8[31:24] = not_57_out ? bit_extender_1_out : 8'bz;  // Controlled_Buffer controlled_buffer_21
  assign bit_extender_2_out = {{7{out_8[15]}}, out_8[15]};  // Bit_Extender bit_extender_2
  // Probe on bit_extender_1_out
  assign out_8[23:16] = not_58_out ? bit_extender_2_out : 8'bz;  // Controlled_Buffer controlled_buffer_22
  assign out_8[31:24] = not_59_out ? bit_extender_2_out : 8'bz;  // Controlled_Buffer controlled_buffer_23
  not not_58 (not_58_out, nand_8_out);
  not not_59 (not_59_out, nand_8_out);
  nand nand_8 (nand_8_out, H, ~Funct3[2], Load);  // NAND_Gate
  Decoder #(.select(4)) decoder_5 (
    .out0(decoder_5_out0), .out1(decoder_5_out1), .out2(decoder_5_out2), .out3(decoder_5_out3),
    .out4(decoder_5_out4), .out5(decoder_5_out5), .out6(decoder_5_out6), .out7(decoder_5_out7),
    .out8(decoder_5_out8), .out9(decoder_5_out9), .out10(decoder_5_out10), .out11(decoder_5_out11),
    .out12(decoder_5_out12), .out13(decoder_5_out13), .out14(decoder_5_out14), .out15(decoder_5_out15),
    .sel({Funct3[1:0], Adress[1:0]}), .en(and_25_out));
  and and_25 (and_25_out, ~to_SP, Load);  // AND_Gate
  not not_60 (BO0, decoder_5_out0);
  not not_61 (BO1, decoder_5_out1);
  not not_62 (BO2, decoder_5_out2);
  not not_63 (BO3, decoder_5_out3);
  not not_64 (HO0, decoder_5_out4);
  not not_65 (HO1, decoder_5_out5);
  not not_66 (HO2, decoder_5_out6);
  not not_67 (HO3, decoder_5_out7);
  not not_68 (WO0, decoder_5_out8);
  not not_69 (WO1, decoder_5_out9);
  not not_70 (WO2, decoder_5_out10);
  not not_71 (WO3, decoder_5_out11);
  // NOT_Gate not_72 has open pins: in=decoder_5_out12, out=open
  // NOT_Gate not_73 has open pins: in=decoder_5_out13, out=open
  // NOT_Gate not_74 has open pins: in=decoder_5_out14, out=open
  // NOT_Gate not_75 has open pins: in=decoder_5_out15, out=open
  // OR_Gate or_1 is placed but not wired

  // Other names for the same wires on the sheet: Adr[31:0] = Adress; Byte_adr[1:0] = Adress[1:0];
  //   Funct_3[2:0] = Funct3; RAM_adress[16:0] = Adress[18:2]; Store_to_VRAM = Adress[30];
  //   Store_to_Special_registers = Adress[31]; clk = Clock; Funct3_2 = Funct3[2]; G4 = B1; G6 = B3;
  //   S0[7:0] = GPU_colors[7:0]; S1[7:0] = GPU_colors[15:8]; H1 = G7; S4[7:0] = in1; S5[7:0] = in2;
  //   Input_data[31:0] = Data; W0 = G3

  // Notes on the sheet:
  //   Register 0
  //   Register 1
  //   Register 2
  //   Register 3
  //   Register 4
  //   Register 5
  //   Register 6
  //   Register 7
  //   Special Registers
  //   In
  //   Special Registers
  //   Unaligned adressing detector
  //   DATA MEMORY
  //   Store and CLK!!
  //   First Input
  //   Second Input
  //   Storing data
  //   RAM selector - for store
  //   Byte steering logic - input
  //   byte
  //   RAM_ADRESS
  //   SRAM
  //   Function decoder
  //   Loading data
  //   VRAM
  //   Function decoder for byte steering
  //   VRAM selector - for store
  //   Byte
  //   Half
  //   Word
  //   Byte steering logic - output
  //   Function decoder
endmodule

module Data_memory_v9 (
  input  Load,
  input  Store,
  input  Clock,
  input  [31:0] Data,
  input  [2:0] Funct3,
  input  [31:0] Adress,
  output [31:0] out_7,
  output Exception,
  output out_9
);

  wire and_1_out, and_2_out, and_3_out, and_4_out, and_5_out, and_6_out, and_7_out, and_8_out, and_9_out,
       and_12_out, and_13_out, and_19_out, and_24_out, and_25_out, and_26_out, and_27_out, and_28_out,
       and_29_out, and_33_out, and_36_out, and_37_out, and_38_out, and_39_out, and_40_out, and_42_out,
       and_43_out, and_44_out, and_45_out, B, B0, B1, B2, B3, BO0, BO1, BO2, BO3, button_3_out,
       counter_1_carry, decoder_1_out0, decoder_1_out1, decoder_1_out2, decoder_1_out3, decoder_1_out6,
       decoder_1_out7, decoder_2_out0, decoder_2_out1, decoder_2_out2, decoder_2_out3, decoder_2_out4,
       decoder_2_out5, decoder_2_out6, decoder_2_out7, decoder_2_out8, decoder_2_out9, decoder_2_out10,
       decoder_2_out11, decoder_2_out12, decoder_2_out13, decoder_2_out14, decoder_2_out15, decoder_3_out0,
       decoder_3_out1, decoder_3_out2, decoder_3_out3, decoder_3_out4, decoder_3_out5, decoder_3_out6,
       decoder_3_out7, decoder_3_out8, decoder_3_out9, decoder_3_out10, decoder_3_out11, decoder_3_out12,
       decoder_3_out13, decoder_3_out14, decoder_3_out15, decoder_4_out0, decoder_4_out1, decoder_4_out2,
       decoder_4_out3, decoder_4_out4, decoder_4_out5, decoder_4_out6, decoder_4_out7, decoder_5_out0,
       decoder_5_out1, decoder_5_out2, decoder_5_out3, decoder_5_out4, decoder_5_out5, decoder_5_out6,
       decoder_5_out7, decoder_5_out8, decoder_5_out9, decoder_5_out10, decoder_5_out11, decoder_5_out12,
       decoder_5_out13, decoder_5_out14, decoder_5_out15, G1, G2, G3, G5, G7, G8, G9, G10, H, H0, H1, H3,
       HO0, HO1, HO2, HO3, in2_ac, iS4Clk, iS5Clk, Load_BYPASS, multiplexer_2_out, multiplexer_3_out,
       multiplexer_4_out, nand_1_out, nand_2_out, nand_4_out, nand_5_out, nand_6_out, nand_7_out, nand_8_out,
       nand_9_out, not_17_out, not_18_out, not_19_out, not_20_out, not_21_out, not_22_out, not_23_out,
       not_25_out, not_26_out, not_27_out, not_28_out, not_29_out, not_30_out, not_31_out, not_32_out,
       not_33_out, not_34_out, not_35_out, not_36_out, not_37_out, not_54_out, not_55_out, not_56_out,
       not_57_out, not_58_out, not_59_out, not_68_out, not_69_out, not_70_out, not_71_out, not_72_out,
       not_73_out, not_74_out, not_75_out, not_76_out, not_77_out, not_78_out, not_79_out, not_80_out,
       not_81_out, not_82_out, not_83_out, not_84_out, or_2_out, SR_input_en, Store_R0, Store_R1, Store_R2,
       Store_R3, Store_VR0, Store_VR1, Store_VR2, Store_VR3, to_SP, to_SRAM, to_VRAM, W1, W2, W3, WO0, WO1,
       WO2, WO3;
  wire [7:0] bit_extender_1_out, bit_extender_2_out, BYTE_0_2_data, BYTE_1_2_data, BYTE_2_2_data,
       BYTE_3_2_data, in1, in2, iS4, iS5, not_24_out, S0, S1, S2, S3, S6, S7;
  wire [8:0] counter_1_q;
  wire [10:0] GPU_ADR, multiplexer_1_out;
  wire [23:0] rgb_video_1_p6;
  wire [31:0] Memory_data;

  // Probe on S0
  // Probe on S1
  // Probe on S2
  // Probe on S3
  // Probe on in1
  // Probe on in2
  // Probe on S6
  // Probe on S7
  and and_1 (and_1_out, Store, to_SRAM);
  and and_2 (and_2_out, ~Clock, Store);  // AND_Gate
  and and_3 (and_3_out, to_SP, and_2_out);
  Decoder #(.select(4)) decoder_1 (
    .out0(decoder_1_out0), .out1(decoder_1_out1), .out2(decoder_1_out2), .out3(decoder_1_out3),
    .out6(decoder_1_out6), .out7(decoder_1_out7), .sel(Adress[3:0]), .en(and_3_out));  // open: out4, out5, out8, out9, out10, out11, out12, out13, out14, out15
  and and_4 (and_4_out, to_SP, Load);
  Decoder #(.select(4)) decoder_2 (
    .out0(decoder_2_out0), .out1(decoder_2_out1), .out2(decoder_2_out2), .out3(decoder_2_out3),
    .out4(decoder_2_out4), .out5(decoder_2_out5), .out6(decoder_2_out6), .out7(decoder_2_out7),
    .out8(decoder_2_out8), .out9(decoder_2_out9), .out10(decoder_2_out10), .out11(decoder_2_out11),
    .out12(decoder_2_out12), .out13(decoder_2_out13), .out14(decoder_2_out14), .out15(decoder_2_out15),
    .sel(Adress[3:0]), .en(and_4_out));
  nand nand_1 (nand_1_out, W3, W2, W1, H3, H1);
  and and_5 (and_5_out, and_1_out, ~Clock);  // AND_Gate
  LED led_1 (.in(nand_1_out));
  // NOT_Gate not_1 has open pins: in=decoder_2_out0, out=open
  // NOT_Gate not_2 has open pins: in=decoder_2_out1, out=open
  // NOT_Gate not_3 has open pins: in=decoder_2_out2, out=open
  // NOT_Gate not_4 has open pins: in=decoder_2_out3, out=open
  not not_5 (out_9, decoder_2_out4);
  not not_6 (in2_ac, decoder_2_out5);
  // NOT_Gate not_7 has open pins: in=decoder_2_out6, out=open
  // NOT_Gate not_8 has open pins: in=decoder_2_out7, out=open
  // NOT_Gate not_9 has open pins: in=decoder_2_out8, out=open
  // NOT_Gate not_10 has open pins: in=decoder_2_out9, out=open
  // NOT_Gate not_11 has open pins: in=decoder_2_out10, out=open
  // NOT_Gate not_12 has open pins: in=decoder_2_out11, out=open
  // NOT_Gate not_13 has open pins: in=decoder_2_out12, out=open
  // NOT_Gate not_14 has open pins: in=decoder_2_out13, out=open
  // NOT_Gate not_15 has open pins: in=decoder_2_out14, out=open
  // NOT_Gate not_16 has open pins: in=decoder_2_out15, out=open
  and and_6 (and_6_out, nand_1_out, and_5_out);
  or or_1 (Exception, and_6_out, and_7_out);
  Button button_1 (.out(iS4Clk));
  // DipSwitch dipswitch_1: pin names not known
  Button button_2 (.out(iS5Clk));
  // DipSwitch dipswitch_2: pin names not known
  nand nand_2 (nand_2_out, WO3, WO2, WO1, HO3, HO1);
  and and_7 (and_7_out, nand_2_out, and_9_out);
  LED led_2 (.in(nand_2_out));
  Register SReg_3 (.D(Memory_data[31:24]), .en(1'b1), .Q(S3), .clk(decoder_1_out3), .clr(1'b0));
  Register SReg_7 (.D(Memory_data[31:24]), .en(1'b1), .Q(S7), .clk(decoder_1_out7));  // open: clr
  assign Memory_data[7:0] = not_17_out ? in1 : 8'bz;  // Controlled_Buffer controlled_buffer_1
  not not_17 (not_17_out, out_9);
  assign Memory_data[7:0] = not_18_out ? in2 : 8'bz;  // Controlled_Buffer controlled_buffer_2
  not not_18 (not_18_out, in2_ac);
  nand nand_3 (SR_input_en, Load, to_SP);
  and and_8 (and_8_out, Load, to_SRAM);
  and and_9 (and_9_out, and_8_out, ~Clock);  // AND_Gate
  Register SReg_2 (.D(Memory_data[23:16]), .en(1'b1), .Q(S2), .clk(decoder_1_out2), .clr(1'b0));
  Register SReg_6 (.D(Memory_data[23:16]), .en(1'b1), .Q(S6), .clk(decoder_1_out6));  // open: clr
  and and_10 (G1, G3, B0, H0);
  and and_11 (G2, G3, H0);
  Register SReg_1 (.D(Memory_data[15:8]), .en(1'b1), .Q(S1), .clk(decoder_1_out1), .clr(1'b0));
  Register SReg_5 (.D(iS5), .en(1'b1), .Q(in2), .clk(iS5Clk));  // open: clr
  assign Memory_data[7:0] = not_19_out ? Data[7:0] : 8'bz;  // Controlled_Buffer controlled_buffer_3
  not not_19 (not_19_out, G1);
  not not_20 (not_20_out, G2);
  not not_21 (not_21_out, G1);
  nand nand_4 (nand_4_out, G2, B1);
  nand nand_5 (nand_5_out, G3, G5);
  nand nand_6 (nand_6_out, G3, B3, G7);
  and and_12 (and_12_out, Store, to_SRAM);
  and and_13 (and_13_out, and_12_out, ~Clock);  // AND_Gate
  assign Memory_data[15:8] = not_20_out ? Data[15:8] : 8'bz;  // Controlled_Buffer controlled_buffer_4
  assign Memory_data[23:16] = not_22_out ? Data[23:16] : 8'bz;  // Controlled_Buffer controlled_buffer_5
  assign Memory_data[31:24] = not_23_out ? Data[31:24] : 8'bz;  // Controlled_Buffer controlled_buffer_6
  not not_22 (not_22_out, G3);
  not not_23 (not_23_out, G3);
  and and_14 (Store_R0, and_13_out, not_21_out);
  and and_15 (Store_R1, and_13_out, nand_4_out);
  and and_16 (Store_R2, and_13_out, nand_5_out);
  and and_17 (Store_R3, and_13_out, nand_6_out);
  Register SReg_0 (.D(Memory_data[7:0]), .en(1'b1), .Q(S0), .clk(decoder_1_out0), .clr(1'b0));
  Register SReg_4 (.D(iS4), .en(1'b1), .Q(in1), .clk(iS4Clk));  // open: clr
  assign not_24_out = ~S0;  // NOT_Gate not_24, 8 bits wide
  assign Memory_data[15:8] = not_25_out ? Data[7:0] : 8'bz;  // Controlled_Buffer controlled_buffer_7
  assign Memory_data[23:16] = not_26_out ? Data[7:0] : 8'bz;  // Controlled_Buffer controlled_buffer_8
  not not_25 (not_25_out, B1);
  not not_26 (not_26_out, G5);
  not not_27 (not_27_out, B3);
  and and_18 (G5, B2, G7);
  Pull_Resistor pull_resistor_1 (.node(Memory_data[31:24]));
  assign Memory_data[31:24] = not_27_out ? Data[7:0] : 8'bz;  // Controlled_Buffer controlled_buffer_9
  assign Memory_data[31:24] = not_28_out ? Data[15:8] : 8'bz;  // Controlled_Buffer controlled_buffer_10
  not not_28 (not_28_out, G7);
  not not_29 (not_29_out, G1);
  nand nand_7 (nand_7_out, G2, B1);
  nand nand_8 (nand_8_out, G3, G5);
  nand nand_9 (nand_9_out, G3, B3, G7);
  and and_19 (and_19_out, Store, to_VRAM);
  _7_Segment_Display u_7_segment_display_1 (
    .g(not_24_out[6]), .f(not_24_out[5]), .a(not_24_out[0]), .b(not_24_out[1]), .e(not_24_out[4]),
    .d(not_24_out[3]), .c(not_24_out[2]), .dp(not_24_out[7]));
  Pull_Resistor pull_resistor_2 (.node(Memory_data[23:16]));
  Pull_Resistor pull_resistor_3 (.node(Memory_data[15:8]));
  Pull_Resistor pull_resistor_4 (.node(Memory_data[7:0]));
  and and_20 (Store_VR0, and_24_out, not_29_out);
  and and_21 (Store_VR1, and_24_out, nand_7_out);
  and and_22 (Store_VR2, and_24_out, nand_8_out);
  and and_23 (Store_VR3, and_24_out, nand_9_out);
  and and_24 (and_24_out, and_19_out, ~Clock);  // AND_Gate
  not not_30 (not_30_out, Store_R0);
  not not_31 (not_31_out, not_30_out);
  and and_25 (and_25_out, to_SRAM, Load);
  not not_32 (not_32_out, Store_R1);
  not not_33 (not_33_out, not_32_out);
  not not_34 (not_34_out, Store_R2);
  not not_35 (not_35_out, not_34_out);
  not not_36 (not_36_out, Store_R3);
  not not_37 (not_37_out, not_36_out);
  and and_26 (and_26_out, not_31_out, Store_R0);
  and and_27 (and_27_out, not_33_out, Store_R1);
  and and_28 (and_28_out, not_35_out, Store_R2);
  and and_29 (and_29_out, not_37_out, Store_R3);
  Decoder #(.select(4)) decoder_3 (
    .out0(decoder_3_out0), .out1(decoder_3_out1), .out2(decoder_3_out2), .out3(decoder_3_out3),
    .out4(decoder_3_out4), .out5(decoder_3_out5), .out6(decoder_3_out6), .out7(decoder_3_out7),
    .out8(decoder_3_out8), .out9(decoder_3_out9), .out10(decoder_3_out10), .out11(decoder_3_out11),
    .out12(decoder_3_out12), .out13(decoder_3_out13), .out14(decoder_3_out14), .out15(decoder_3_out15),
    .sel({Funct3[1:0], Adress[1:0]}), .en(Store));
  RAM #(.addrWidth(17), .databus("bidir")) BYTE_0 (.addr(Adress[18:2]), .data(Memory_data[7:0]));  // open: we, oe, clk
  RAM #(.addrWidth(17), .databus("bidir")) BYTE_1 (.addr(Adress[18:2]), .data(Memory_data[15:8]));  // open: we, oe, clk
  RAM #(.addrWidth(17), .databus("bidir")) BYTE_2 (
    .addr(Adress[18:2]), .data(Memory_data[23:16]));  // open: we, oe, clk
  RAM #(.addrWidth(17), .databus("bidir")) BYTE_3 (
    .addr(Adress[18:2]), .data(Memory_data[31:24]));  // open: we, oe, clk
  not not_38 (B0, decoder_3_out0);
  not not_39 (B1, decoder_3_out1);
  not not_40 (B2, decoder_3_out2);
  not not_41 (B3, decoder_3_out3);
  not not_42 (H0, decoder_3_out4);
  not not_43 (H1, decoder_3_out5);
  not not_44 (G7, decoder_3_out6);
  not not_45 (H3, decoder_3_out7);
  not not_46 (G3, decoder_3_out8);
  not not_47 (W1, decoder_3_out9);
  not not_48 (W2, decoder_3_out10);
  not not_49 (W3, decoder_3_out11);
  // NOT_Gate not_50 has open pins: in=decoder_3_out12, out=open
  // NOT_Gate not_51 has open pins: in=decoder_3_out13, out=open
  // NOT_Gate not_52 has open pins: in=decoder_3_out14, out=open
  // NOT_Gate not_53 has open pins: in=decoder_3_out15, out=open
  and and_30 (to_VRAM, Adress[30], not_55_out);
  and and_31 (to_SP, not_54_out, Adress[31]);
  not not_54 (not_54_out, Adress[30]);
  and and_32 (to_SRAM, not_54_out, not_55_out);
  not not_55 (not_55_out, Adress[31]);
  and and_33 (and_33_out, WO0, BO0, HO0);
  and and_34 (G9, WO0, HO0);
  not not_56 (not_56_out, G8);
  and and_35 (G8, SR_input_en, and_33_out);
  assign out_7[7:0] = not_56_out ? Memory_data[7:0] : 8'bz;  // Controlled_Buffer controlled_buffer_11
  assign out_7[15:8] = not_57_out ? Memory_data[15:8] : 8'bz;  // Controlled_Buffer controlled_buffer_12
  assign out_7[23:16] = not_58_out ? Memory_data[23:16] : 8'bz;  // Controlled_Buffer controlled_buffer_13
  assign out_7[31:24] = not_59_out ? Memory_data[31:24] : 8'bz;  // Controlled_Buffer controlled_buffer_14
  not not_57 (not_57_out, G9);
  not not_58 (not_58_out, WO0);
  not not_59 (not_59_out, WO0);
  Decoder #(.select(3)) decoder_4 (
    .out0(decoder_4_out0), .out1(decoder_4_out1), .out2(decoder_4_out2), .out3(decoder_4_out3),
    .out4(decoder_4_out4), .out5(decoder_4_out5), .out6(decoder_4_out6), .out7(decoder_4_out7), .sel(Funct3),
    .en(Load));
  and and_36 (and_36_out, to_VRAM, Load);
  not not_60 (B, decoder_4_out0);
  not not_61 (H, decoder_4_out1);
  // NOT_Gate not_62 has open pins: in=decoder_4_out2, out=open
  // NOT_Gate not_63 has open pins: in=decoder_4_out3, out=open
  // NOT_Gate not_64 has open pins: in=decoder_4_out4, out=open
  // NOT_Gate not_65 has open pins: in=decoder_4_out5, out=open
  // NOT_Gate not_66 has open pins: in=decoder_4_out6, out=open
  // NOT_Gate not_67 has open pins: in=decoder_4_out7, out=open
  not not_68 (not_68_out, Store_VR0);
  not not_69 (not_69_out, not_68_out);
  and and_37 (and_37_out, not_69_out, Store_VR0);
  not not_70 (not_70_out, Store_VR1);
  not not_71 (not_71_out, not_70_out);
  and and_38 (and_38_out, not_71_out, Store_VR1);
  not not_72 (not_72_out, Store_VR2);
  not not_73 (not_73_out, not_72_out);
  and and_39 (and_39_out, not_73_out, Store_VR2);
  not not_74 (not_74_out, Store_VR3);
  not not_75 (not_75_out, not_74_out);
  and and_40 (and_40_out, not_75_out, Store_VR3);
  assign out_7[7:0] = not_76_out ? Memory_data[15:8] : 8'bz;  // Controlled_Buffer controlled_buffer_15
  assign out_7[7:0] = not_77_out ? Memory_data[23:16] : 8'bz;  // Controlled_Buffer controlled_buffer_16
  not not_76 (not_76_out, BO1);
  not not_77 (not_77_out, G10);
  not not_78 (not_78_out, BO3);
  and and_41 (G10, BO2, HO2);
  Multiplexer #(.enable("false"), .width(11)) multiplexer_1 (
    .in0(GPU_ADR), .in1(Adress[12:2]), .out(multiplexer_1_out), .sel(to_VRAM));
  or or_2 (or_2_out, and_36_out, Load_BYPASS);
  assign out_7[7:0] = not_78_out ? Memory_data[31:24] : 8'bz;  // Controlled_Buffer controlled_buffer_17
  assign out_7[15:8] = not_79_out ? Memory_data[31:24] : 8'bz;  // Controlled_Buffer controlled_buffer_18
  not not_79 (not_79_out, HO2);
  RAM #(.addrWidth(11), .databus("bidir")) BYTE_0_2 (
    .addr(multiplexer_1_out), .data(BYTE_0_2_data));  // open: we, oe, clk
  RAM #(.addrWidth(11), .databus("bidir")) BYTE_1_2 (
    .addr(multiplexer_1_out), .data(BYTE_1_2_data));  // open: we, oe, clk
  RAM #(.addrWidth(11), .databus("bidir")) BYTE_2_2 (
    .addr(multiplexer_1_out), .data(BYTE_2_2_data));  // open: we, oe, clk
  RAM #(.addrWidth(11), .databus("bidir")) BYTE_3_2 (
    .addr(multiplexer_1_out), .data(BYTE_3_2_data));  // open: we, oe, clk
  assign bit_extender_1_out = {{7{out_7[7]}}, out_7[7]};  // Bit_Extender bit_extender_1
  not not_80 (not_80_out, B);
  assign out_7[15:8] = not_80_out ? bit_extender_1_out : 8'bz;  // Controlled_Buffer controlled_buffer_19
  not not_81 (not_81_out, B);
  assign out_7[23:16] = not_81_out ? bit_extender_1_out : 8'bz;  // Controlled_Buffer controlled_buffer_20
  not not_82 (not_82_out, B);
  assign out_7[31:24] = not_82_out ? bit_extender_1_out : 8'bz;  // Controlled_Buffer controlled_buffer_21
  assign bit_extender_2_out = {{7{out_7[15]}}, out_7[15]};  // Bit_Extender bit_extender_2
  // Probe on bit_extender_1_out
  assign out_7[23:16] = not_83_out ? bit_extender_2_out : 8'bz;  // Controlled_Buffer controlled_buffer_22
  assign out_7[31:24] = not_84_out ? bit_extender_2_out : 8'bz;  // Controlled_Buffer controlled_buffer_23
  not not_83 (not_83_out, H);
  not not_84 (not_84_out, H);
  Decoder #(.select(4)) decoder_5 (
    .out0(decoder_5_out0), .out1(decoder_5_out1), .out2(decoder_5_out2), .out3(decoder_5_out3),
    .out4(decoder_5_out4), .out5(decoder_5_out5), .out6(decoder_5_out6), .out7(decoder_5_out7),
    .out8(decoder_5_out8), .out9(decoder_5_out9), .out10(decoder_5_out10), .out11(decoder_5_out11),
    .out12(decoder_5_out12), .out13(decoder_5_out13), .out14(decoder_5_out14), .out15(decoder_5_out15),
    .sel({Funct3[1:0], Adress[1:0]}), .en(and_42_out));
  and and_42 (and_42_out, ~to_SP, Load);  // AND_Gate
  not not_85 (BO0, decoder_5_out0);
  not not_86 (BO1, decoder_5_out1);
  not not_87 (BO2, decoder_5_out2);
  not not_88 (BO3, decoder_5_out3);
  not not_89 (HO0, decoder_5_out4);
  not not_90 (HO1, decoder_5_out5);
  not not_91 (HO2, decoder_5_out6);
  not not_92 (HO3, decoder_5_out7);
  not not_93 (WO0, decoder_5_out8);
  not not_94 (WO1, decoder_5_out9);
  not not_95 (WO2, decoder_5_out10);
  not not_96 (WO3, decoder_5_out11);
  // NOT_Gate not_97 has open pins: in=decoder_5_out12, out=open
  // NOT_Gate not_98 has open pins: in=decoder_5_out13, out=open
  // NOT_Gate not_99 has open pins: in=decoder_5_out14, out=open
  // NOT_Gate not_100 has open pins: in=decoder_5_out15, out=open
  and and_43 (and_43_out, to_VRAM, Store);
  assign {BYTE_3_2_data, BYTE_2_2_data, BYTE_1_2_data, BYTE_0_2_data} = and_43_out ? Memory_data : 32'bz;  // Controlled_Buffer controlled_buffer_24
  assign Memory_data = and_44_out ? {BYTE_3_2_data, BYTE_2_2_data, BYTE_1_2_data, BYTE_0_2_data} : 32'bz;  // Controlled_Buffer controlled_buffer_25
  and and_44 (and_44_out, to_VRAM, Load);
  and and_45 (and_45_out, Clock, ~to_VRAM);  // AND_Gate
  Counter #(.max('h108), .width(9)) counter_1 (
    .Q({counter_1_q[8], GPU_ADR[2:0], counter_1_q[4:0]}), .carry(counter_1_carry), .clk(and_45_out));  // open: load, D, count, clr
  not not_101 (Load_BYPASS, to_VRAM);
  Button button_3 (.out(button_3_out));
  // RGB_Video #(.height(256), .width(256)) rgb_video_1: pin names not known; wires that end beside it: button_3_out, and_45_out, 1'b1, {GPU_ADR[2:0], counter_1_q[4:0]}, GPU_ADR[10:3], rgb_video_1_p6
  Counter #(.max('h96)) counter_2 (.Q(GPU_ADR[10:3]), .clk(counter_1_carry));  // open: load, D, count, carry, clr
  Pull_Resistor pull_resistor_5 (.node({BYTE_3_2_data, BYTE_2_2_data, BYTE_1_2_data, BYTE_0_2_data}));
  Multiplexer #(.enable("false"), .select(4)) multiplexer_2 (
    .in0(BYTE_0_2_data[0]), .in1(BYTE_0_2_data[1]), .in2(BYTE_0_2_data[2]), .in3(BYTE_0_2_data[3]),
    .in4(BYTE_0_2_data[4]), .in5(BYTE_0_2_data[5]), .in6(BYTE_0_2_data[6]), .in7(BYTE_0_2_data[7]),
    .in8(BYTE_1_2_data[0]), .in9(BYTE_1_2_data[1]), .in10(BYTE_1_2_data[2]), .in11(BYTE_1_2_data[3]),
    .in12(BYTE_1_2_data[4]), .in13(BYTE_1_2_data[5]), .in14(BYTE_1_2_data[6]), .in15(BYTE_1_2_data[7]),
    .out(multiplexer_2_out), .sel(counter_1_q[3:0]));
  Multiplexer #(.enable("false"), .select(4)) multiplexer_3 (
    .in0(BYTE_2_2_data[0]), .in1(BYTE_2_2_data[1]), .in2(BYTE_2_2_data[2]), .in3(BYTE_2_2_data[3]),
    .in4(BYTE_2_2_data[4]), .in5(BYTE_2_2_data[5]), .in6(BYTE_2_2_data[6]), .in7(BYTE_2_2_data[7]),
    .in8(BYTE_3_2_data[0]), .in9(BYTE_3_2_data[1]), .in10(BYTE_3_2_data[2]), .in11(BYTE_3_2_data[3]),
    .in12(BYTE_3_2_data[4]), .in13(BYTE_3_2_data[5]), .in14(BYTE_3_2_data[6]), .in15(BYTE_3_2_data[7]),
    .out(multiplexer_3_out), .sel(counter_1_q[3:0]));
  Multiplexer multiplexer_4 (
    .in0(multiplexer_2_out), .in1(multiplexer_3_out), .out(multiplexer_4_out), .sel(counter_1_q[4]), .en(1'b1));
  Multiplexer #(.enable("false"), .width(24)) multiplexer_5 (
    .in0({24{1'b0}}), .in1({24{1'b1}}), .out(rgb_video_1_p6), .sel(multiplexer_4_out));
  // OR_Gate or_3 is placed but not wired

  // Other names for the same wires on the sheet: Adr[31:0] = Adress; Byte_adr[1:0] = Adress[1:0];
  //   Funct_3[2:0] = Funct3; RAM_adress[16:0] = Adress[18:2]; VRAM_adress[10:0] = Adress[12:2];
  //   Store_to_VRAM = Adress[30]; Store_to_Special_registers = Adress[31]; clk = Clock; G4 = B1; G6 = B3; H2 = G7;
  //   S4[7:0] = in1; in1_ac = out_9; S5[7:0] = in2; Input_data[31:0] = Data; SR_input[7:0] = Memory_data[7:0];
  //   W0 = G3

  // Notes on the sheet:
  //   Register 0
  //   Register 1
  //   Register 2
  //   Register 3
  //   Register 4
  //   Register 5
  //   Register 6
  //   Register 7
  //   Special Registers
  //   In
  //   Special Registers
  //   ** Note: not all registers are in the final version
  //   DATA MEMORY
  //   First Input
  //   Second Input
  //   Unaligned adressing detector
  //   Storing data
  //   SRAM selector - for store
  //   Byte steering logic - input
  //   VRAM selector - for store
  //   SRAM
  //   Function decoder
  //   byte
  //   VRAM_ADRESS
  //   RAM_ADRESS
  //   Loading data
  //   ** Note: this is not the same as on the final version, cause I cannot create a dual-port RAM here
  //   (But it behaves in a similar way)
  //   VRAM
  //   Function decoder for byte steering
  //   Byte
  //   Half
  //   Byte steering logic - output
  //   Function decoder
  //   Imitation of a connected VGA monitor (cropped)
endmodule

module Memory_adder_v1 (
  input  plusOne,
  input  [14:0] In,
  output [14:0] Out
);

  wire and_1_out, and_2_out, and_3_out, and_4_out, and_5_out, and_6_out, and_7_out, and_8_out, and_9_out,
       and_10_out, and_11_out, and_12_out, and_13_out, and_14_out;

  xor xor_1 (Out[0], plusOne, In[0]);
  and and_1 (and_1_out, In[0], plusOne);
  xor xor_2 (Out[1], and_1_out, In[1]);
  and and_2 (and_2_out, In[1], and_1_out);
  and and_3 (and_3_out, In[2], and_2_out);
  xor xor_3 (Out[2], and_2_out, In[2]);
  xor xor_4 (Out[3], and_3_out, In[3]);
  and and_4 (and_4_out, In[3], and_3_out);
  xor xor_5 (Out[4], and_4_out, In[4]);
  and and_5 (and_5_out, In[4], and_4_out);
  xor xor_6 (Out[5], and_5_out, In[5]);
  and and_6 (and_6_out, In[5], and_5_out);
  and and_7 (and_7_out, In[6], and_6_out);
  xor xor_7 (Out[6], and_6_out, In[6]);
  xor xor_8 (Out[7], and_7_out, In[7]);
  and and_8 (and_8_out, In[7], and_7_out);
  xor xor_9 (Out[8], and_8_out, In[8]);
  and and_9 (and_9_out, In[8], and_8_out);
  xor xor_10 (Out[9], and_9_out, In[9]);
  and and_10 (and_10_out, In[9], and_9_out);
  and and_11 (and_11_out, In[10], and_10_out);
  xor xor_11 (Out[10], and_10_out, In[10]);
  xor xor_12 (Out[11], and_11_out, In[11]);
  and and_12 (and_12_out, In[11], and_11_out);
  xor xor_13 (Out[12], and_12_out, In[12]);
  and and_13 (and_13_out, In[12], and_12_out);
  xor xor_14 (Out[13], and_13_out, In[13]);
  and and_14 (and_14_out, In[13], and_13_out);
  xor xor_15 (Out[14], and_14_out, In[14]);
endmodule

module test (
  input  [31:0] Input,
  output [31:0] \output 
);

  wire nand_1_out;

  nand nand_1 (nand_1_out, Input[0], Input[1]);
  RAM #(.addrWidth(24)) ram_1 (.addr(Input[25:2]), .we(nand_1_out), .dout(\output [7:0]));  // open: clk, din
  RAM #(.addrWidth(24)) ram_2 (.addr(Input[25:2]), .we(nand_1_out), .dout(\output [15:8]));  // open: clk, din
  RAM #(.addrWidth(24)) ram_3 (.addr(Input[25:2]), .we(nand_1_out), .dout(\output [23:16]));  // open: clk, din
  RAM #(.addrWidth(24)) ram_4 (.addr(Input[25:2]), .we(nand_1_out), .dout(\output [31:24]));  // open: clk, din
endmodule

module imm_generator_v1 (
  input  [31:0] in,
  output [31:0] out
);

  // Probe on in[31:20]
  assign out = {{20{in[31]}}, in[31:20]};  // Bit_Extender bit_extender_1
  // Probe on out
endmodule

module Imm_generator_v2 (
  input  [31:0] in,
  input  [2:0] in_2,
  output [31:0] out
);

  wire [31:0] bit_extender_1_out, bit_extender_2_out, bit_extender_3_out, bit_extender_4_out,
       bit_extender_5_out, bit_extender_6_out, bit_extender_7_out;

  assign bit_extender_1_out = {{20{in[31]}}, in[31:20]};  // Bit_Extender bit_extender_1
  assign bit_extender_2_out = {{20{in[31]}}, {in[31:25], in[11:7]}};  // Bit_Extender bit_extender_2
  assign bit_extender_3_out = {{11{in[31]}}, {in[31], in[19:12], in[20], in[30:21], 1'b0}};  // Bit_Extender bit_extender_3
  Multiplexer #(.enable("false"), .select(2), .width(32)) multiplexer_1 (
    .in0({in[31:12], {12{1'b0}}}), .in1(bit_extender_1_out), .in2(bit_extender_3_out),
    .in3(bit_extender_2_out), .out(out), .sel(in_2[1:0]));
  assign bit_extender_4_out = {{20{in[31]}}, in[31:20]};  // Bit_Extender bit_extender_4
  assign bit_extender_5_out = {{20{in[31]}}, {in[31:25], in[11:7]}};  // Bit_Extender bit_extender_5
  assign bit_extender_6_out = {{20{in[31]}}, {in[31:25], in[7], in[11:8]}};  // Bit_Extender bit_extender_6
  // Probe on bit_extender_4_out
  // Probe on bit_extender_4_out
  // Probe on bit_extender_4_out
  // Probe on bit_extender_5_out
  // Probe on bit_extender_5_out
  // Probe on bit_extender_5_out
  // Probe on bit_extender_6_out
  // Probe on bit_extender_6_out
  // Probe on bit_extender_6_out
  // Probe on {in[31:12], {12{1'b0}}}
  // Probe on {in[31:12], {12{1'b0}}}
  // Probe on {in[31:12], {12{1'b0}}}
  // Probe on bit_extender_7_out
  // Probe on bit_extender_7_out
  assign bit_extender_7_out = {{12{in[31]}}, {in[31], in[19:12], in[20], in[30:21]}};  // Bit_Extender bit_extender_7
  // Probe on bit_extender_7_out
  Multiplexer #(.enable("false"), .select(3), .width(32)) multiplexer_2 (
    .in0(bit_extender_4_out), .in1(bit_extender_5_out), .in2(bit_extender_6_out),
    .in3({in[31:12], {12{1'b0}}}), .in4(bit_extender_7_out), .sel(in_2));  // open: in5, in6, in7, out

  // Other names for the same wires on the sheet: instruction[31:0] = in; sel[2:0] = in_2

  // Notes on the sheet:
  //   U
  //   I
  //   S
  //   UJ
  //   I-Type
  //   S-Type
  //   SB-Type
  //   U-Type
  //   UJ-Type
  //   Hex
  //   Dec
  //   Bin
  //   Hex
  //   Dec
  //   Bin
  //   Hex
  //   Dec
  //   Bin
  //   Hex
  //   Dec
  //   Bin
  //   Hex
  //   Dec
  //   Bin
endmodule

module Imm_generator_v3 (
  input  [31:0] in,
  input  [2:0] in_2,
  output [31:0] out
);

  wire decoder_1_out0, decoder_1_out1, decoder_1_out2, decoder_1_out3, decoder_1_out4;
  wire [31:0] bit_extender_1_out, bit_extender_2_out, bit_extender_3_out, bit_extender_4_out;

  Decoder #(.enable("false"), .select(3)) decoder_1 (
    .out0(decoder_1_out0), .out1(decoder_1_out1), .out2(decoder_1_out2), .out3(decoder_1_out3),
    .out4(decoder_1_out4), .sel(in_2));  // open: out5, out6, out7
  LED I_Type (.in(decoder_1_out0));
  LED S_Type (.in(decoder_1_out1));
  LED SB_Type (.in(decoder_1_out2));
  LED U_Type (.in(decoder_1_out3));
  LED UJ_Type (.in(decoder_1_out4));
  assign bit_extender_1_out = {{20{in[31]}}, in[31:20]};  // Bit_Extender bit_extender_1
  assign bit_extender_2_out = {{20{in[31]}}, {in[31:25], in[11:7]}};  // Bit_Extender bit_extender_2
  assign bit_extender_3_out = {{20{in[31]}}, {in[31], in[7], in[30:25], in[11:8]}};  // Bit_Extender bit_extender_3
  assign bit_extender_4_out = {{12{in[31]}}, {in[31], in[19:12], in[20], in[30:21]}};  // Bit_Extender bit_extender_4
  // NOT_Gate not_1 is placed but not wired
  // Probe on bit_extender_1_out
  // Probe on bit_extender_1_out
  // Probe on bit_extender_1_out
  // Probe on bit_extender_2_out
  // Probe on bit_extender_2_out
  // Probe on bit_extender_2_out
  // Probe on bit_extender_3_out
  // Probe on bit_extender_3_out
  // Probe on bit_extender_3_out
  // Probe on {in[31:12], {12{1'b0}}}
  // Probe on {in[31:12], {12{1'b0}}}
  // Probe on {in[31:12], {12{1'b0}}}
  // Probe on bit_extender_4_out
  // Probe on bit_extender_4_out
  // Probe on bit_extender_4_out
  Multiplexer #(.enable("false"), .select(3), .width(32)) multiplexer_1 (
    .in0(bit_extender_1_out), .in1(bit_extender_2_out), .in2(bit_extender_3_out),
    .in3({in[31:12], {12{1'b0}}}), .in4(bit_extender_4_out), .out(out), .sel(in_2));  // open: in5, in6, in7
  // NOT_Gate not_2 is placed but not wired

  // Other names for the same wires on the sheet: instruction[31:0] = in; sel[2:0] = in_2

  // Notes on the sheet:
  //   I-Type
  //   S-Type
  //   SB-Type
  //   U-Type
  //   UJ-Type
  //   Bin
  //   Bin
  //   Bin
  //   Bin
  //   Bin
  //   Hex
  //   Dec
  //   Hex
  //   Dec
  //   Hex
  //   Dec
  //   Hex
  //   Dec
  //   Hex
  //   Dec
endmodule

module Imm_generator_v4 (
  input  [31:0] Ins,
  input  [2:0] Sel,
  output [31:0] Out
);

  wire and_1_out, and_2_out, and_3_out, and_5_out, and_7_out, and_8_out, and_9_out, and_10_out,
       decoder_1_out0, decoder_1_out1, decoder_1_out2, decoder_1_out3, decoder_1_out4, decoder_1_out5,
       decoder_1_out6, decoder_1_out7, decoder_2_out0, decoder_2_out1, decoder_2_out2, decoder_2_out3,
       decoder_2_out4, not_1_out, not_2_out, not_3_out, not_4_out, not_5_out, not_9_out, not_10_out,
       not_11_out, not_12_out, not_13_out, not_14_out, not_15_out, not_16_out, not_17_out, not_18_out,
       not_19_out, not_20_out, not_21_out, not_22_out;
  wire [0:0] and_4_out, and_6_out;
  wire [3:3] or_1_out;

  not not_1 (not_1_out, decoder_1_out0);
  not not_2 (not_2_out, decoder_1_out1);
  not not_3 (not_3_out, decoder_1_out2);
  not not_4 (not_4_out, decoder_1_out3);
  not not_5 (not_5_out, decoder_1_out4);
  // NOT_Gate not_6 has open pins: in=decoder_1_out5, out=open
  // NOT_Gate not_7 has open pins: in=decoder_1_out6, out=open
  // NOT_Gate not_8 has open pins: in=decoder_1_out7, out=open
  Decoder #(.enable("false"), .select(3)) decoder_1 (
    .out0(decoder_1_out0), .out1(decoder_1_out1), .out2(decoder_1_out2), .out3(decoder_1_out3),
    .out4(decoder_1_out4), .out5(decoder_1_out5), .out6(decoder_1_out6), .out7(decoder_1_out7), .sel(Sel));
  LED I_Type (.in(not_1_out));
  LED S_Type (.in(not_2_out));
  LED SB_Type (.in(not_3_out));
  LED U_Type (.in(not_4_out));
  LED UJ_Type (.in(not_5_out));
  and and_1 (and_1_out, not_3_out, and_2_out);
  and and_2 (and_2_out, not_2_out, not_1_out);
  and and_3 (and_3_out, not_3_out, not_2_out);
  not not_9 (not_9_out, not_2_out);
  and and_4 (and_4_out[0], not_9_out, Ins[7]);
  not not_10 (not_10_out, and_3_out);
  or or_1 (or_1_out[3], and_5_out, and_8_out);
  and and_5 (and_5_out, Ins[31], not_11_out);
  not not_11 (not_11_out, and_2_out);
  assign Out[15:8] = not_12_out ? {{4{Ins[31]}}, or_1_out[3], Ins[30:28]} : 8'bz;  // Controlled_Buffer controlled_buffer_1
  not not_12 (not_12_out, and_1_out);
  not not_13 (not_13_out, and_1_out);
  not not_14 (not_14_out, not_1_out);
  and and_6 (and_6_out[0], not_14_out, Ins[20]);
  assign Out[7:0] = not_15_out ? {Ins[27:21], and_6_out[0]} : 8'bz;  // Controlled_Buffer controlled_buffer_2
  not not_15 (not_15_out, and_7_out);
  and and_7 (and_7_out, not_5_out, not_1_out);
  assign {Out[23:20], Out[11:8]} = not_16_out ? {{4{Ins[31]}}, Ins[20], Ins[30:28]} : 8'bz;  // Controlled_Buffer controlled_buffer_3
  not not_16 (not_16_out, not_5_out);
  assign Out[27:20] = not_18_out ? Ins[27:20] : 8'bz;  // Controlled_Buffer controlled_buffer_4
  assign {Out[11:8], Out[31:28]} = not_17_out ? {4'b0000, Ins[31:28]} : 8'bz;  // Controlled_Buffer controlled_buffer_5
  not not_17 (not_17_out, not_4_out);
  not not_18 (not_18_out, not_4_out);
  assign Out[7:0] = not_10_out ? {Ins[27:25], Ins[11:8], and_4_out[0]} : 8'bz;  // Controlled_Buffer controlled_buffer_6
  and and_8 (and_8_out, Ins[7], not_19_out);
  not not_19 (not_19_out, not_3_out);
  assign Out[23:16] = not_13_out ? {8{Ins[31]}} : 8'bz;  // Controlled_Buffer controlled_buffer_7
  assign Out[31:24] = not_20_out ? {8{Ins[31]}} : 8'bz;  // Controlled_Buffer controlled_buffer_8
  not not_20 (not_20_out, and_9_out);
  and and_9 (and_9_out, not_5_out, and_1_out);
  assign Out[7:0] = not_22_out ? {8{1'b0}} : 8'bz;  // Controlled_Buffer controlled_buffer_9
  assign Out[19:12] = not_21_out ? Ins[19:12] : 8'bz;  // Controlled_Buffer controlled_buffer_10
  not not_21 (not_21_out, and_10_out);
  not not_22 (not_22_out, not_4_out);
  and and_10 (and_10_out, not_4_out, not_5_out);
  Pull_Resistor pull_resistor_1 (.node(Out));
  Decoder #(.enable("false"), .select(3)) decoder_2 (
    .out0(decoder_2_out0), .out1(decoder_2_out1), .out2(decoder_2_out2), .out3(decoder_2_out3),
    .out4(decoder_2_out4), .sel(Sel));  // open: out5, out6, out7
  LED I_Type_2 (.in(decoder_2_out0));
  LED S_Type_2 (.in(decoder_2_out1));
  LED SB_Type_2 (.in(decoder_2_out2));
  LED U_Type_2 (.in(decoder_2_out3));
  LED UJ_Type_2 (.in(decoder_2_out4));

  // Other names for the same wires on the sheet: Select[2:0] = Sel

  // Notes on the sheet:
  //   "Optimized" immediate generator
  //   Just for output LEDs (not in actual CPU)
endmodule
module Shifter_v1 (
  input  in_1,
  input  in_2,
  input  in_3,
  input  in_4,
  input  in_5,
  input  in_6,
  input  in_7,
  input  in_8,
  input  in_9,
  input  in_10,
  input  in_11,
  input  in_12,
  input  in_13,
  input  in_14,
  input  in_15,
  input  in_16,
  input  in_17,
  input  in_18,
  input  in_19,
  input  in_20,
  input  in_21,
  input  in_22,
  input  in_23,
  input  in_24,
  input  in_25,
  input  in_26,
  input  in_27,
  input  in_28,
  input  in_29,
  input  in_30,
  input  in_31,
  input  in_32,
  input  in_33,
  input  _1,
  input  _2,
  input  _4,
  input  in_37,
  input  _16,
  output [31:0] out_39
);

  wire multiplexer_1_out, multiplexer_2_out, multiplexer_3_out, multiplexer_4_out, multiplexer_5_out,
       multiplexer_6_out, multiplexer_7_out, multiplexer_8_out, multiplexer_9_out, multiplexer_10_out,
       multiplexer_11_out, multiplexer_12_out, multiplexer_13_out, multiplexer_14_out, multiplexer_15_out,
       multiplexer_16_out, multiplexer_17_out, multiplexer_18_out, multiplexer_19_out, multiplexer_20_out,
       multiplexer_21_out, multiplexer_22_out, multiplexer_23_out, multiplexer_24_out, multiplexer_25_out,
       multiplexer_26_out, multiplexer_27_out, multiplexer_28_out, multiplexer_29_out, multiplexer_30_out,
       multiplexer_31_out, multiplexer_32_out, multiplexer_33_out, multiplexer_34_out, multiplexer_35_out,
       multiplexer_36_out, multiplexer_37_out, multiplexer_38_out, multiplexer_39_out, multiplexer_40_out,
       multiplexer_41_out, multiplexer_42_out, multiplexer_43_out, multiplexer_44_out, multiplexer_45_out,
       multiplexer_46_out, multiplexer_47_out, multiplexer_48_out, multiplexer_49_out, multiplexer_50_out,
       multiplexer_51_out, multiplexer_52_out, multiplexer_53_out, multiplexer_54_out, multiplexer_55_out,
       multiplexer_56_out, multiplexer_57_out, multiplexer_58_out, multiplexer_59_out, multiplexer_60_out,
       multiplexer_61_out, multiplexer_62_out, multiplexer_63_out, multiplexer_64_out, multiplexer_65_out,
       multiplexer_66_out, multiplexer_67_out, multiplexer_68_out, multiplexer_69_out, multiplexer_70_out,
       multiplexer_71_out, multiplexer_72_out, multiplexer_73_out, multiplexer_74_out, multiplexer_75_out,
       multiplexer_76_out, multiplexer_77_out, multiplexer_78_out, multiplexer_79_out, multiplexer_80_out,
       multiplexer_81_out, multiplexer_82_out, multiplexer_83_out, multiplexer_84_out, multiplexer_85_out,
       multiplexer_86_out, multiplexer_87_out, multiplexer_88_out, multiplexer_89_out, multiplexer_90_out,
       multiplexer_91_out, multiplexer_92_out, multiplexer_93_out, multiplexer_94_out, multiplexer_95_out,
       multiplexer_96_out, multiplexer_97_out, multiplexer_98_out, multiplexer_99_out, multiplexer_100_out,
       multiplexer_101_out, multiplexer_102_out, multiplexer_103_out, multiplexer_104_out,
       multiplexer_105_out, multiplexer_106_out, multiplexer_107_out, multiplexer_108_out,
       multiplexer_109_out, multiplexer_110_out, multiplexer_111_out, multiplexer_112_out,
       multiplexer_113_out, multiplexer_114_out, multiplexer_115_out, multiplexer_116_out,
       multiplexer_117_out, multiplexer_118_out, multiplexer_119_out, multiplexer_120_out,
       multiplexer_121_out, multiplexer_122_out, multiplexer_123_out, multiplexer_124_out,
       multiplexer_125_out, multiplexer_126_out, multiplexer_127_out, multiplexer_128_out;

  Multiplexer #(.enable("false")) multiplexer_1 (.in0(in_2), .in1(in_33), .out(multiplexer_1_out), .sel(_1));
  Multiplexer #(.enable("false")) multiplexer_2 (.in0(in_3), .in1(in_2), .out(multiplexer_2_out), .sel(_1));
  Multiplexer #(.enable("false")) multiplexer_3 (.in0(in_4), .in1(in_3), .out(multiplexer_3_out), .sel(_1));
  Multiplexer #(.enable("false")) multiplexer_4 (.in0(in_5), .in1(in_4), .out(multiplexer_4_out), .sel(_1));
  Multiplexer #(.enable("false")) multiplexer_5 (.in0(in_6), .in1(in_5), .out(multiplexer_5_out), .sel(_1));
  Multiplexer #(.enable("false")) multiplexer_6 (.in0(in_7), .in1(in_6), .out(multiplexer_6_out), .sel(_1));
  Multiplexer #(.enable("false")) multiplexer_7 (.in0(in_8), .in1(in_7), .out(multiplexer_7_out), .sel(_1));
  Multiplexer #(.enable("false")) multiplexer_8 (.in0(in_9), .in1(in_8), .out(multiplexer_8_out), .sel(_1));
  Multiplexer #(.enable("false")) multiplexer_9 (.in0(in_10), .in1(in_9), .out(multiplexer_9_out), .sel(_1));
  Multiplexer #(.enable("false")) multiplexer_10 (.in0(in_11), .in1(in_10), .out(multiplexer_10_out), .sel(_1));
  Multiplexer #(.enable("false")) multiplexer_11 (.in0(in_12), .in1(in_11), .out(multiplexer_11_out), .sel(_1));
  Multiplexer #(.enable("false")) multiplexer_12 (.in0(in_13), .in1(in_12), .out(multiplexer_12_out), .sel(_1));
  Multiplexer #(.enable("false")) multiplexer_13 (.in0(in_14), .in1(in_13), .out(multiplexer_13_out), .sel(_1));
  Multiplexer #(.enable("false")) multiplexer_14 (.in0(in_15), .in1(in_14), .out(multiplexer_14_out), .sel(_1));
  Multiplexer #(.enable("false")) multiplexer_15 (.in0(in_16), .in1(in_15), .out(multiplexer_15_out), .sel(_1));
  Multiplexer #(.enable("false")) multiplexer_16 (.in0(in_17), .in1(in_16), .out(multiplexer_16_out), .sel(_1));
  Multiplexer #(.enable("false")) multiplexer_17 (.in0(in_18), .in1(in_17), .out(multiplexer_17_out), .sel(_1));
  Multiplexer #(.enable("false")) multiplexer_18 (.in0(in_19), .in1(in_18), .out(multiplexer_18_out), .sel(_1));
  Multiplexer #(.enable("false")) multiplexer_19 (.in0(in_20), .in1(in_19), .out(multiplexer_19_out), .sel(_1));
  Multiplexer #(.enable("false")) multiplexer_20 (.in0(in_21), .in1(in_20), .out(multiplexer_20_out), .sel(_1));
  Multiplexer #(.enable("false")) multiplexer_21 (.in0(in_22), .in1(in_21), .out(multiplexer_21_out), .sel(_1));
  Multiplexer #(.enable("false")) multiplexer_22 (.in0(in_23), .in1(in_22), .out(multiplexer_22_out), .sel(_1));
  Multiplexer #(.enable("false")) multiplexer_23 (.in0(in_24), .in1(in_23), .out(multiplexer_23_out), .sel(_1));
  Multiplexer #(.enable("false")) multiplexer_24 (.in0(in_25), .in1(in_24), .out(multiplexer_24_out), .sel(_1));
  Multiplexer #(.enable("false")) multiplexer_25 (.in0(in_26), .in1(in_25), .out(multiplexer_25_out), .sel(_1));
  Multiplexer #(.enable("false")) multiplexer_26 (.in0(in_27), .in1(in_26), .out(multiplexer_26_out), .sel(_1));
  Multiplexer #(.enable("false")) multiplexer_27 (.in0(in_28), .in1(in_27), .out(multiplexer_27_out), .sel(_1));
  Multiplexer #(.enable("false")) multiplexer_28 (.in0(in_29), .in1(in_28), .out(multiplexer_28_out), .sel(_1));
  Multiplexer #(.enable("false")) multiplexer_29 (.in0(in_30), .in1(in_29), .out(multiplexer_29_out), .sel(_1));
  Multiplexer #(.enable("false")) multiplexer_30 (.in0(in_31), .in1(in_30), .out(multiplexer_30_out), .sel(_1));
  Multiplexer #(.enable("false")) multiplexer_31 (.in0(in_32), .in1(in_31), .out(multiplexer_31_out), .sel(_1));
  Multiplexer #(.enable("false")) multiplexer_32 (.in0(in_33), .in1(in_32), .out(multiplexer_32_out), .sel(_1));
  Multiplexer #(.enable("false")) multiplexer_33 (
    .in0(multiplexer_1_out), .in1(multiplexer_31_out), .out(multiplexer_33_out), .sel(_2));
  Multiplexer #(.enable("false")) multiplexer_34 (
    .in0(multiplexer_2_out), .in1(multiplexer_32_out), .out(multiplexer_34_out), .sel(_2));
  Multiplexer #(.enable("false")) multiplexer_35 (
    .in0(multiplexer_3_out), .in1(multiplexer_1_out), .out(multiplexer_35_out), .sel(_2));
  Multiplexer #(.enable("false")) multiplexer_36 (
    .in0(multiplexer_4_out), .in1(multiplexer_2_out), .out(multiplexer_36_out), .sel(_2));
  Multiplexer #(.enable("false")) multiplexer_37 (
    .in0(multiplexer_5_out), .in1(multiplexer_3_out), .out(multiplexer_37_out), .sel(_2));
  Multiplexer #(.enable("false")) multiplexer_38 (
    .in0(multiplexer_6_out), .in1(multiplexer_4_out), .out(multiplexer_38_out), .sel(_2));
  Multiplexer #(.enable("false")) multiplexer_39 (
    .in0(multiplexer_7_out), .in1(multiplexer_5_out), .out(multiplexer_39_out), .sel(_2));
  Multiplexer #(.enable("false")) multiplexer_40 (
    .in0(multiplexer_8_out), .in1(multiplexer_6_out), .out(multiplexer_40_out), .sel(_2));
  Multiplexer #(.enable("false")) multiplexer_41 (
    .in0(multiplexer_9_out), .in1(multiplexer_7_out), .out(multiplexer_41_out), .sel(_2));
  Multiplexer #(.enable("false")) multiplexer_42 (
    .in0(multiplexer_10_out), .in1(multiplexer_8_out), .out(multiplexer_42_out), .sel(_2));
  Multiplexer #(.enable("false")) multiplexer_43 (
    .in0(multiplexer_11_out), .in1(multiplexer_9_out), .out(multiplexer_43_out), .sel(_2));
  Multiplexer #(.enable("false")) multiplexer_44 (
    .in0(multiplexer_12_out), .in1(multiplexer_10_out), .out(multiplexer_44_out), .sel(_2));
  Multiplexer #(.enable("false")) multiplexer_45 (
    .in0(multiplexer_13_out), .in1(multiplexer_11_out), .out(multiplexer_45_out), .sel(_2));
  Multiplexer #(.enable("false")) multiplexer_46 (
    .in0(multiplexer_14_out), .in1(multiplexer_12_out), .out(multiplexer_46_out), .sel(_2));
  Multiplexer #(.enable("false")) multiplexer_47 (
    .in0(multiplexer_15_out), .in1(multiplexer_13_out), .out(multiplexer_47_out), .sel(_2));
  Multiplexer #(.enable("false")) multiplexer_48 (
    .in0(multiplexer_16_out), .in1(multiplexer_14_out), .out(multiplexer_48_out), .sel(_2));
  Multiplexer #(.enable("false")) multiplexer_49 (
    .in0(multiplexer_17_out), .in1(multiplexer_15_out), .out(multiplexer_49_out), .sel(_2));
  Multiplexer #(.enable("false")) multiplexer_50 (
    .in0(multiplexer_18_out), .in1(multiplexer_16_out), .out(multiplexer_50_out), .sel(_2));
  Multiplexer #(.enable("false")) multiplexer_51 (
    .in0(multiplexer_19_out), .in1(multiplexer_17_out), .out(multiplexer_51_out), .sel(_2));
  Multiplexer #(.enable("false")) multiplexer_52 (
    .in0(multiplexer_20_out), .in1(multiplexer_18_out), .out(multiplexer_52_out), .sel(_2));
  Multiplexer #(.enable("false")) multiplexer_53 (
    .in0(multiplexer_21_out), .in1(multiplexer_19_out), .out(multiplexer_53_out), .sel(_2));
  Multiplexer #(.enable("false")) multiplexer_54 (
    .in0(multiplexer_22_out), .in1(multiplexer_20_out), .out(multiplexer_54_out), .sel(_2));
  Multiplexer #(.enable("false")) multiplexer_55 (
    .in0(multiplexer_23_out), .in1(multiplexer_21_out), .out(multiplexer_55_out), .sel(_2));
  Multiplexer #(.enable("false")) multiplexer_56 (
    .in0(multiplexer_24_out), .in1(multiplexer_22_out), .out(multiplexer_56_out), .sel(_2));
  Multiplexer #(.enable("false")) multiplexer_57 (
    .in0(multiplexer_25_out), .in1(multiplexer_23_out), .out(multiplexer_57_out), .sel(_2));
  Multiplexer #(.enable("false")) multiplexer_58 (
    .in0(multiplexer_26_out), .in1(multiplexer_24_out), .out(multiplexer_58_out), .sel(_2));
  Multiplexer #(.enable("false")) multiplexer_59 (
    .in0(multiplexer_27_out), .in1(multiplexer_25_out), .out(multiplexer_59_out), .sel(_2));
  Multiplexer #(.enable("false")) multiplexer_60 (
    .in0(multiplexer_28_out), .in1(multiplexer_26_out), .out(multiplexer_60_out), .sel(_2));
  Multiplexer #(.enable("false")) multiplexer_61 (
    .in0(multiplexer_29_out), .in1(multiplexer_27_out), .out(multiplexer_61_out), .sel(_2));
  Multiplexer #(.enable("false")) multiplexer_62 (
    .in0(multiplexer_30_out), .in1(multiplexer_28_out), .out(multiplexer_62_out), .sel(_2));
  Multiplexer #(.enable("false")) multiplexer_63 (
    .in0(multiplexer_31_out), .in1(multiplexer_29_out), .out(multiplexer_63_out), .sel(_2));
  Multiplexer #(.enable("false")) multiplexer_64 (
    .in0(multiplexer_32_out), .in1(multiplexer_30_out), .out(multiplexer_64_out), .sel(_2));
  Multiplexer #(.enable("false")) multiplexer_65 (
    .in0(multiplexer_33_out), .in1(multiplexer_61_out), .out(multiplexer_65_out), .sel(_4));
  Multiplexer #(.enable("false")) multiplexer_66 (
    .in0(multiplexer_34_out), .in1(multiplexer_62_out), .out(multiplexer_66_out), .sel(_4));
  Multiplexer #(.enable("false")) multiplexer_67 (
    .in0(multiplexer_35_out), .in1(multiplexer_63_out), .out(multiplexer_67_out), .sel(_4));
  Multiplexer #(.enable("false")) multiplexer_68 (
    .in0(multiplexer_36_out), .in1(multiplexer_64_out), .out(multiplexer_68_out), .sel(_4));
  Multiplexer #(.enable("false")) multiplexer_69 (
    .in0(multiplexer_37_out), .in1(multiplexer_33_out), .out(multiplexer_69_out), .sel(_4));
  Multiplexer #(.enable("false")) multiplexer_70 (
    .in0(multiplexer_38_out), .in1(multiplexer_34_out), .out(multiplexer_70_out), .sel(_4));
  Multiplexer #(.enable("false")) multiplexer_71 (
    .in0(multiplexer_39_out), .in1(multiplexer_35_out), .out(multiplexer_71_out), .sel(_4));
  Multiplexer #(.enable("false")) multiplexer_72 (
    .in0(multiplexer_40_out), .in1(multiplexer_36_out), .out(multiplexer_72_out), .sel(_4));
  Multiplexer #(.enable("false")) multiplexer_73 (
    .in0(multiplexer_41_out), .in1(multiplexer_37_out), .out(multiplexer_73_out), .sel(_4));
  Multiplexer #(.enable("false")) multiplexer_74 (
    .in0(multiplexer_42_out), .in1(multiplexer_38_out), .out(multiplexer_74_out), .sel(_4));
  Multiplexer #(.enable("false")) multiplexer_75 (
    .in0(multiplexer_43_out), .in1(multiplexer_39_out), .out(multiplexer_75_out), .sel(_4));
  Multiplexer #(.enable("false")) multiplexer_76 (
    .in0(multiplexer_44_out), .in1(multiplexer_40_out), .out(multiplexer_76_out), .sel(_4));
  Multiplexer #(.enable("false")) multiplexer_77 (
    .in0(multiplexer_45_out), .in1(multiplexer_41_out), .out(multiplexer_77_out), .sel(_4));
  Multiplexer #(.enable("false")) multiplexer_78 (
    .in0(multiplexer_46_out), .in1(multiplexer_42_out), .out(multiplexer_78_out), .sel(_4));
  Multiplexer #(.enable("false")) multiplexer_79 (
    .in0(multiplexer_47_out), .in1(multiplexer_43_out), .out(multiplexer_79_out), .sel(_4));
  Multiplexer #(.enable("false")) multiplexer_80 (
    .in0(multiplexer_48_out), .in1(multiplexer_44_out), .out(multiplexer_80_out), .sel(_4));
  Multiplexer #(.enable("false")) multiplexer_81 (
    .in0(multiplexer_49_out), .in1(multiplexer_45_out), .out(multiplexer_81_out), .sel(_4));
  Multiplexer #(.enable("false")) multiplexer_82 (
    .in0(multiplexer_50_out), .in1(multiplexer_46_out), .out(multiplexer_82_out), .sel(_4));
  Multiplexer #(.enable("false")) multiplexer_83 (
    .in0(multiplexer_51_out), .in1(multiplexer_47_out), .out(multiplexer_83_out), .sel(_4));
  Multiplexer #(.enable("false")) multiplexer_84 (
    .in0(multiplexer_52_out), .in1(multiplexer_48_out), .out(multiplexer_84_out), .sel(_4));
  Multiplexer #(.enable("false")) multiplexer_85 (
    .in0(multiplexer_53_out), .in1(multiplexer_49_out), .out(multiplexer_85_out), .sel(_4));
  Multiplexer #(.enable("false")) multiplexer_86 (
    .in0(multiplexer_54_out), .in1(multiplexer_50_out), .out(multiplexer_86_out), .sel(_4));
  Multiplexer #(.enable("false")) multiplexer_87 (
    .in0(multiplexer_55_out), .in1(multiplexer_51_out), .out(multiplexer_87_out), .sel(_4));
  Multiplexer #(.enable("false")) multiplexer_88 (
    .in0(multiplexer_56_out), .in1(multiplexer_52_out), .out(multiplexer_88_out), .sel(_4));
  Multiplexer #(.enable("false")) multiplexer_89 (
    .in0(multiplexer_57_out), .in1(multiplexer_53_out), .out(multiplexer_89_out), .sel(_4));
  Multiplexer #(.enable("false")) multiplexer_90 (
    .in0(multiplexer_58_out), .in1(multiplexer_54_out), .out(multiplexer_90_out), .sel(_4));
  Multiplexer #(.enable("false")) multiplexer_91 (
    .in0(multiplexer_59_out), .in1(multiplexer_55_out), .out(multiplexer_91_out), .sel(_4));
  Multiplexer #(.enable("false")) multiplexer_92 (
    .in0(multiplexer_60_out), .in1(multiplexer_56_out), .out(multiplexer_92_out), .sel(_4));
  Multiplexer #(.enable("false")) multiplexer_93 (
    .in0(multiplexer_61_out), .in1(multiplexer_57_out), .out(multiplexer_93_out), .sel(_4));
  Multiplexer #(.enable("false")) multiplexer_94 (
    .in0(multiplexer_62_out), .in1(multiplexer_58_out), .out(multiplexer_94_out), .sel(_4));
  Multiplexer #(.enable("false")) multiplexer_95 (
    .in0(multiplexer_63_out), .in1(multiplexer_59_out), .out(multiplexer_95_out), .sel(_4));
  Multiplexer #(.enable("false")) multiplexer_96 (
    .in0(multiplexer_64_out), .in1(multiplexer_60_out), .out(multiplexer_96_out), .sel(_4));
  Multiplexer #(.enable("false")) multiplexer_97 (
    .in0(multiplexer_65_out), .in1(multiplexer_89_out), .out(multiplexer_97_out), .sel(in_37));
  Multiplexer #(.enable("false")) multiplexer_98 (
    .in0(multiplexer_66_out), .in1(multiplexer_90_out), .out(multiplexer_98_out), .sel(in_37));
  Multiplexer #(.enable("false")) multiplexer_99 (
    .in0(multiplexer_67_out), .in1(multiplexer_91_out), .out(multiplexer_99_out), .sel(in_37));
  Multiplexer #(.enable("false")) multiplexer_100 (
    .in0(multiplexer_68_out), .in1(multiplexer_92_out), .out(multiplexer_100_out), .sel(in_37));
  Multiplexer #(.enable("false")) multiplexer_101 (
    .in0(multiplexer_69_out), .in1(multiplexer_93_out), .out(multiplexer_101_out), .sel(in_37));
  Multiplexer #(.enable("false")) multiplexer_102 (
    .in0(multiplexer_70_out), .in1(multiplexer_94_out), .out(multiplexer_102_out), .sel(in_37));
  Multiplexer #(.enable("false")) multiplexer_103 (
    .in0(multiplexer_71_out), .in1(multiplexer_95_out), .out(multiplexer_103_out), .sel(in_37));
  Multiplexer #(.enable("false")) multiplexer_104 (
    .in0(multiplexer_72_out), .in1(multiplexer_96_out), .out(multiplexer_104_out), .sel(in_37));
  Multiplexer #(.enable("false")) multiplexer_105 (
    .in0(multiplexer_73_out), .in1(multiplexer_65_out), .out(multiplexer_105_out), .sel(in_37));
  Multiplexer #(.enable("false")) multiplexer_106 (
    .in0(multiplexer_74_out), .in1(multiplexer_66_out), .out(multiplexer_106_out), .sel(in_37));
  Multiplexer #(.enable("false")) multiplexer_107 (
    .in0(multiplexer_75_out), .in1(multiplexer_67_out), .out(multiplexer_107_out), .sel(in_37));
  Multiplexer #(.enable("false")) multiplexer_108 (
    .in0(multiplexer_76_out), .in1(multiplexer_68_out), .out(multiplexer_108_out), .sel(in_37));
  Multiplexer #(.enable("false")) multiplexer_109 (
    .in0(multiplexer_77_out), .in1(multiplexer_69_out), .out(multiplexer_109_out), .sel(in_37));
  Multiplexer #(.enable("false")) multiplexer_110 (
    .in0(multiplexer_78_out), .in1(multiplexer_70_out), .out(multiplexer_110_out), .sel(in_37));
  Multiplexer #(.enable("false")) multiplexer_111 (
    .in0(multiplexer_79_out), .in1(multiplexer_71_out), .out(multiplexer_111_out), .sel(in_37));
  Multiplexer #(.enable("false")) multiplexer_112 (
    .in0(multiplexer_80_out), .in1(multiplexer_72_out), .out(multiplexer_112_out), .sel(in_37));
  Multiplexer #(.enable("false")) multiplexer_113 (
    .in0(multiplexer_81_out), .in1(multiplexer_73_out), .out(multiplexer_113_out), .sel(in_37));
  Multiplexer #(.enable("false")) multiplexer_114 (
    .in0(multiplexer_82_out), .in1(multiplexer_74_out), .out(multiplexer_114_out), .sel(in_37));
  Multiplexer #(.enable("false")) multiplexer_115 (
    .in0(multiplexer_83_out), .in1(multiplexer_75_out), .out(multiplexer_115_out), .sel(in_37));
  Multiplexer #(.enable("false")) multiplexer_116 (
    .in0(multiplexer_84_out), .in1(multiplexer_76_out), .out(multiplexer_116_out), .sel(in_37));
  Multiplexer #(.enable("false")) multiplexer_117 (
    .in0(multiplexer_85_out), .in1(multiplexer_77_out), .out(multiplexer_117_out), .sel(in_37));
  Multiplexer #(.enable("false")) multiplexer_118 (
    .in0(multiplexer_86_out), .in1(multiplexer_78_out), .out(multiplexer_118_out), .sel(in_37));
  Multiplexer #(.enable("false")) multiplexer_119 (
    .in0(multiplexer_87_out), .in1(multiplexer_79_out), .out(multiplexer_119_out), .sel(in_37));
  Multiplexer #(.enable("false")) multiplexer_120 (
    .in0(multiplexer_88_out), .in1(multiplexer_80_out), .out(multiplexer_120_out), .sel(in_37));
  Multiplexer #(.enable("false")) multiplexer_121 (
    .in0(multiplexer_89_out), .in1(multiplexer_81_out), .out(multiplexer_121_out), .sel(in_37));
  Multiplexer #(.enable("false")) multiplexer_122 (
    .in0(multiplexer_90_out), .in1(multiplexer_82_out), .out(multiplexer_122_out), .sel(in_37));
  Multiplexer #(.enable("false")) multiplexer_123 (
    .in0(multiplexer_91_out), .in1(multiplexer_83_out), .out(multiplexer_123_out), .sel(in_37));
  Multiplexer #(.enable("false")) multiplexer_124 (
    .in0(multiplexer_92_out), .in1(multiplexer_84_out), .out(multiplexer_124_out), .sel(in_37));
  Multiplexer #(.enable("false")) multiplexer_125 (
    .in0(multiplexer_93_out), .in1(multiplexer_85_out), .out(multiplexer_125_out), .sel(in_37));
  Multiplexer #(.enable("false")) multiplexer_126 (
    .in0(multiplexer_94_out), .in1(multiplexer_86_out), .out(multiplexer_126_out), .sel(in_37));
  Multiplexer #(.enable("false")) multiplexer_127 (
    .in0(multiplexer_95_out), .in1(multiplexer_87_out), .out(multiplexer_127_out), .sel(in_37));
  Multiplexer #(.enable("false")) multiplexer_128 (
    .in0(multiplexer_96_out), .in1(multiplexer_88_out), .out(multiplexer_128_out), .sel(in_37));
  Multiplexer #(.enable("false")) multiplexer_129 (
    .in0(multiplexer_97_out), .in1(multiplexer_113_out), .out(out_39[0]), .sel(_16));
  Multiplexer #(.enable("false")) multiplexer_130 (
    .in0(multiplexer_98_out), .in1(multiplexer_114_out), .out(out_39[1]), .sel(_16));
  Multiplexer #(.enable("false")) multiplexer_131 (
    .in0(multiplexer_99_out), .in1(multiplexer_115_out), .out(out_39[2]), .sel(_16));
  Multiplexer #(.enable("false")) multiplexer_132 (
    .in0(multiplexer_100_out), .in1(multiplexer_116_out), .out(out_39[3]), .sel(_16));
  Multiplexer #(.enable("false")) multiplexer_133 (
    .in0(multiplexer_101_out), .in1(multiplexer_117_out), .out(out_39[4]), .sel(_16));
  Multiplexer #(.enable("false")) multiplexer_134 (
    .in0(multiplexer_102_out), .in1(multiplexer_118_out), .out(out_39[5]), .sel(_16));
  Multiplexer #(.enable("false")) multiplexer_135 (
    .in0(multiplexer_103_out), .in1(multiplexer_119_out), .out(out_39[6]), .sel(_16));
  Multiplexer #(.enable("false")) multiplexer_136 (
    .in0(multiplexer_104_out), .in1(multiplexer_120_out), .out(out_39[7]), .sel(_16));
  Multiplexer #(.enable("false")) multiplexer_137 (
    .in0(multiplexer_105_out), .in1(multiplexer_121_out), .out(out_39[8]), .sel(_16));
  Multiplexer #(.enable("false")) multiplexer_138 (
    .in0(multiplexer_106_out), .in1(multiplexer_122_out), .out(out_39[9]), .sel(_16));
  Multiplexer #(.enable("false")) multiplexer_139 (
    .in0(multiplexer_107_out), .in1(multiplexer_123_out), .out(out_39[10]), .sel(_16));
  Multiplexer #(.enable("false")) multiplexer_140 (
    .in0(multiplexer_108_out), .in1(multiplexer_124_out), .out(out_39[11]), .sel(_16));
  Multiplexer #(.enable("false")) multiplexer_141 (
    .in0(multiplexer_109_out), .in1(multiplexer_125_out), .out(out_39[12]), .sel(_16));
  Multiplexer #(.enable("false")) multiplexer_142 (
    .in0(multiplexer_110_out), .in1(multiplexer_126_out), .out(out_39[13]), .sel(_16));
  Multiplexer #(.enable("false")) multiplexer_143 (
    .in0(multiplexer_111_out), .in1(multiplexer_127_out), .out(out_39[14]), .sel(_16));
  Multiplexer #(.enable("false")) multiplexer_144 (
    .in0(multiplexer_112_out), .in1(multiplexer_128_out), .out(out_39[15]), .sel(_16));
  Multiplexer #(.enable("false")) multiplexer_145 (
    .in0(multiplexer_113_out), .in1(multiplexer_97_out), .out(out_39[16]), .sel(_16));
  Multiplexer #(.enable("false")) multiplexer_146 (
    .in0(multiplexer_114_out), .in1(multiplexer_98_out), .out(out_39[17]), .sel(_16));
  Multiplexer #(.enable("false")) multiplexer_147 (
    .in0(multiplexer_115_out), .in1(multiplexer_99_out), .out(out_39[18]), .sel(_16));
  Multiplexer #(.enable("false")) multiplexer_148 (
    .in0(multiplexer_116_out), .in1(multiplexer_100_out), .out(out_39[19]), .sel(_16));
  Multiplexer #(.enable("false")) multiplexer_149 (
    .in0(multiplexer_117_out), .in1(multiplexer_101_out), .out(out_39[20]), .sel(_16));
  Multiplexer #(.enable("false")) multiplexer_150 (
    .in0(multiplexer_118_out), .in1(multiplexer_102_out), .out(out_39[21]), .sel(_16));
  Multiplexer #(.enable("false")) multiplexer_151 (
    .in0(multiplexer_119_out), .in1(multiplexer_103_out), .out(out_39[22]), .sel(_16));
  Multiplexer #(.enable("false")) multiplexer_152 (
    .in0(multiplexer_120_out), .in1(multiplexer_104_out), .out(out_39[23]), .sel(_16));
  Multiplexer #(.enable("false")) multiplexer_153 (
    .in0(multiplexer_121_out), .in1(multiplexer_105_out), .out(out_39[24]), .sel(_16));
  Multiplexer #(.enable("false")) multiplexer_154 (
    .in0(multiplexer_122_out), .in1(multiplexer_106_out), .out(out_39[25]), .sel(_16));
  Multiplexer #(.enable("false")) multiplexer_155 (
    .in0(multiplexer_123_out), .in1(multiplexer_107_out), .out(out_39[26]), .sel(_16));
  Multiplexer #(.enable("false")) multiplexer_156 (
    .in0(multiplexer_124_out), .in1(multiplexer_108_out), .out(out_39[27]), .sel(_16));
  Multiplexer #(.enable("false")) multiplexer_157 (
    .in0(multiplexer_125_out), .in1(multiplexer_109_out), .out(out_39[28]), .sel(_16));
  Multiplexer #(.enable("false")) multiplexer_158 (
    .in0(multiplexer_126_out), .in1(multiplexer_110_out), .out(out_39[29]), .sel(_16));
  Multiplexer #(.enable("false")) multiplexer_159 (
    .in0(multiplexer_127_out), .in1(multiplexer_111_out), .out(out_39[30]), .sel(_16));
  Multiplexer #(.enable("false")) multiplexer_160 (
    .in0(multiplexer_128_out), .in1(multiplexer_112_out), .out(out_39[31]), .sel(_16));

  // Notes on the sheet:
  //   8
endmodule

module Shifter_simple_v1 (
  input  ARITMETIC,
  input  [31:0] in_2,
  input  in_3,
  input  SRL,
  input  in_5,
  input  [4:0] in_6,
  input  Shifter_enable,
  output [31:0] out_8,
  output Shifter_busy
);

  wire and_1_out, and_2_out, Clock_out, comparator_1_eq, not_1_out, not_2_out, Reset_out;
  wire [4:0] counter_1_q, register_1_q;
  wire [31:0] controlled_buffer_1_out, register_2_q, shifter_1_out, shifter_2_out;
  wire [31:31] multiplexer_1_out;

  Button Clock (.out(Clock_out));
  assign controlled_buffer_1_out = in_3 ? in_2 : 32'bz;  // Controlled_Buffer controlled_buffer_1
  Register #(.width(5)) register_1 (.D(in_6), .Q(register_1_q), .clk(and_1_out));  // open: en, clr
  and and_1 (and_1_out, Clock_out, Shifter_enable);
  Counter #(.max('h1f), .width(5)) counter_1 (
    .Q(counter_1_q), .clk(and_2_out), .clr(Reset_out));  // open: load, D, count, carry
  and and_2 (and_2_out, and_1_out, not_1_out);
  Button Reset (.out(Reset_out));
  Multiplexer #(.enable("false")) multiplexer_1 (
    .in0(1'b0), .in1(controlled_buffer_1_out[31]), .out(multiplexer_1_out[31]), .sel(ARITMETIC));
  Shifter #(.shift("lr"), .width(32)) shifter_1 (.in(controlled_buffer_1_out), .\dist (5'b00001), .out(shifter_1_out));
  assign out_8 = not_2_out ? shifter_2_out : 32'bz;  // Controlled_Buffer controlled_buffer_2
  Shifter #(.width(32)) shifter_2 (.in(controlled_buffer_1_out), .\dist (5'b00001), .out(shifter_2_out));
  assign controlled_buffer_1_out = in_5 ? register_2_q : 32'bz;  // Controlled_Buffer controlled_buffer_3
  Register #(.width(32)) register_2 (.D(out_8), .Q(register_2_q), .clk(and_2_out), .clr(Reset_out));  // open: en
  Comparator #(.width(5)) comparator_1 (.a(register_1_q), .b(counter_1_q), .eq(comparator_1_eq));  // open: gt, lt
  not not_1 (not_1_out, comparator_1_eq);
  assign out_8 = SRL ? {multiplexer_1_out[31], shifter_1_out[30:0]} : 32'bz;  // Controlled_Buffer controlled_buffer_4
  // Probe on controlled_buffer_1_out
  not not_2 (not_2_out, SRL);
  and and_3 (Shifter_busy, not_1_out, Shifter_enable);
  LED led_1 (.in(Shifter_busy));
endmodule

module Shifter_simple_v2 (
  input  Right,
  input  Right_Aritmetic,
  input  Left,
  input  [31:0] rs1,
  input  Clock_in,
  input  [4:0] rs2,
  input  Shifter_enable,
  output [31:0] rd
);

  wire and_1_out, and_3_out, Clock_2_out, Clock_out, comparator_1_eq, not_1_out, or_1_out, or_2_out,
       Reset_out;
  wire [4:0] counter_1_q;
  wire [31:0] controlled_buffer_1_out;
  wire [31:31] and_2_out;

  Button Clock (.out(Clock_out));
  Button Clock_2 (.out(Clock_2_out));
  Button Reset (.out(Reset_out));
  or or_1 (or_1_out, Right_Aritmetic, Right);
  assign controlled_buffer_1_out = Clock_in ? rs1 : 32'bz;  // Controlled_Buffer controlled_buffer_1
  Register #(.width(32)) register_1 (.D(controlled_buffer_1_out), .Q(rd), .clk(or_2_out), .clr(Reset_out));  // open: en
  or or_2 (or_2_out, Clock_out, and_1_out);
  and and_1 (and_1_out, Clock_2_out, not_1_out, Shifter_enable);
  Counter #(.max('h1f), .width(5)) counter_1 (
    .Q(counter_1_q), .clk(and_1_out), .clr(Reset_out));  // open: load, D, count, carry
  and and_2 (and_2_out[31], rd[31], Right_Aritmetic);
  Comparator #(.width(5)) comparator_1 (.a(rs2), .b(counter_1_q), .eq(comparator_1_eq));  // open: gt, lt
  assign controlled_buffer_1_out = or_1_out ? {and_2_out[31], rd[31:1]} : 32'bz;  // Controlled_Buffer controlled_buffer_2
  not not_1 (not_1_out, comparator_1_eq);
  and and_3 (and_3_out, not_1_out, Shifter_enable);
  LED Shifter_Busy (.in(and_3_out));
  assign controlled_buffer_1_out = Left ? {rd[30:0], 1'b0} : 32'bz;  // Controlled_Buffer controlled_buffer_3

  // Notes on the sheet:
  //   Right Shift
  //   Left Shift
endmodule

module shifter_v3 (
  input  SH_LAOD,
  input  [4:0] RS2,
  input  in_3,
  input  [2:0] in_4,
  input  SH_PROPAGATE,
  input  Reset,
  output output_enable,
  output SH_BUSY
);

  wire and_1_out, and_2_out, and_3_out, and_4_out, d_ff_1_qn, d_ff_2_qn, decoder_1_out1, decoder_1_out5,
       nand_1_out, not_1_out, not_2_out, not_3_out, not_4_out, not_5_out, not_6_out, not_7_out, or_1_out,
       or_2_out, or_3_out, or_4_out, or_5_out, or_6_out, v3_1_out, v3_2_out, v3_3_out, v3_4_out, v12_2_out,
       v12_3_out, xnor_1_out, xnor_2_out, xnor_3_out, xnor_4_out, xnor_5_out;
  wire [4:0] shifter_counter_v1_1_out_3;

  Decoder #(.select(3)) decoder_1 (
    .out1(decoder_1_out1), .out5(decoder_1_out5), .sel(in_4), .en(SH_PROPAGATE));  // open: out0, out2, out3, out4, out6, out7
  not not_1 (not_1_out, decoder_1_out1);
  not not_2 (not_2_out, decoder_1_out5);
  nand nand_1 (nand_1_out, not_1_out, not_2_out);
  or or_1 (or_1_out, not_1_out, not_3_out);
  or or_2 (or_2_out, not_3_out, not_2_out);
  D_Flip_Flop d_ff_1 (.clk(in_3), .D(v3_3_out), .Qn(d_ff_1_qn), .reset(Reset));  // open: Q, preset
  and v3_3 (v3_3_out, not_5_out, nand_1_out);
  not not_3 (not_3_out, v3_2_out);
  not not_4 (not_4_out, SH_LAOD);
  and v3_1 (v3_1_out, d_ff_1_qn, nand_1_out);
  and v3_2 (v3_2_out, not_4_out, v3_1_out);
  and v3_4 (v3_4_out, in_3, v3_2_out);
  shifter_counter_v1 shifter_counter_v1_1 (.out_3(shifter_counter_v1_1_out_3), .Clk(v3_4_out), .R(Reset));
  or or_3 (or_3_out, RS2[0], RS2[1]);
  or or_4 (or_4_out, or_3_out, or_6_out);
  or or_5 (or_5_out, RS2[2], RS2[3]);
  or or_6 (or_6_out, or_5_out, RS2[4]);
  xnor xnor_1 (xnor_1_out, RS2[0], shifter_counter_v1_1_out_3[0]);
  xnor xnor_2 (xnor_2_out, RS2[1], shifter_counter_v1_1_out_3[1]);
  xnor xnor_3 (xnor_3_out, RS2[2], shifter_counter_v1_1_out_3[2]);
  xnor xnor_4 (xnor_4_out, RS2[3], shifter_counter_v1_1_out_3[3]);
  xnor xnor_5 (xnor_5_out, RS2[4], shifter_counter_v1_1_out_3[4]);
  not not_5 (not_5_out, or_4_out);
  and and_1 (and_1_out, xnor_1_out, xnor_2_out);
  and and_2 (and_2_out, and_1_out, and_3_out);
  and and_3 (and_3_out, xnor_3_out, xnor_4_out);
  and and_4 (and_4_out, and_2_out, xnor_5_out);
  not not_6 (not_6_out, and_4_out);
  not not_7 (not_7_out, in_3);
  and v12_2 (v12_2_out, and_4_out, v3_2_out);
  and v12_3 (v12_3_out, v3_2_out, not_6_out);
  D_Flip_Flop d_ff_2 (.clk(not_7_out), .D(v12_2_out), .Qn(d_ff_2_qn), .reset(Reset));  // open: Q, preset
  and v14_1 (output_enable, d_ff_2_qn, d_ff_1_qn);
  and v14_1_2 (SH_BUSY, v12_3_out, d_ff_1_qn);

  // Notes on the sheet:
  //   zero
  //   left
  //   right
  //   zero
  //   equal
endmodule

module shifter_v4 (
  input  SH_LAOD,
  input  [31:0] RS2,
  input  in_3,
  input  [2:0] in_4,
  input  SH_PROPAGATE,
  input  Reset,
  input  I,
  input  [31:0] Input,
  output out_9,
  output out_10,
  output [31:0] Out
);

  wire and_1_out, and_2_out, and_3_out, and_5_out, d_ff_1_qn, d_ff_2_qn, decoder_1_out1, decoder_1_out5,
       Left, nand_1_out, not_1_out, not_2_out, not_3_out, not_4_out, not_6_out, not_7_out, not_8_out,
       not_9_out, not_10_out, not_11_out, or_3_out, or_4_out, or_5_out, or_6_out, Right, v3_1_out, v3_2_out,
       v3_3_out, v3_4_out, v12_2_out, v12_3_out, xnor_1_out, xnor_2_out, xnor_3_out, xnor_4_out, xnor_5_out;
  wire [1:1] register_1_q;
  wire [4:0] shifter_counter_v1_1_out_3;
  wire [31:0] controlled_buffer_1_out, register_1_q_2;

  Decoder #(.select(3)) decoder_1 (
    .out1(decoder_1_out1), .out5(decoder_1_out5), .sel(in_4), .en(SH_PROPAGATE));  // open: out0, out2, out3, out4, out6, out7
  not not_1 (not_1_out, decoder_1_out1);
  not not_2 (not_2_out, decoder_1_out5);
  nand nand_1 (nand_1_out, not_1_out, not_2_out);
  or or_1 (Left, not_1_out, not_3_out);
  or or_2 (Right, not_3_out, not_2_out);
  // Probe on Input
  D_Flip_Flop d_ff_1 (.clk(in_3), .D(v3_3_out), .Qn(d_ff_1_qn), .reset(Reset));  // open: Q, preset
  and v3_3 (v3_3_out, not_6_out, nand_1_out);
  not not_3 (not_3_out, v3_2_out);
  not not_4 (not_4_out, SH_LAOD);
  and v3_1 (v3_1_out, d_ff_1_qn, nand_1_out);
  and v3_2 (v3_2_out, not_4_out, v3_1_out);
  and v3_4 (v3_4_out, in_3, v3_2_out);
  shifter_counter_v1 shifter_counter_v1_1 (.out_3(shifter_counter_v1_1_out_3), .Clk(v3_4_out), .R(Reset));
  assign controlled_buffer_1_out = SH_LAOD ? Input : 32'bz;  // Controlled_Buffer controlled_buffer_1
  // NOT_Gate not_5 is placed but not wired
  or or_3 (or_3_out, RS2[0], RS2[1]);
  or or_4 (or_4_out, or_3_out, or_6_out);
  or or_5 (or_5_out, RS2[2], RS2[3]);
  or or_6 (or_6_out, or_5_out, RS2[4]);
  xnor xnor_1 (xnor_1_out, RS2[0], shifter_counter_v1_1_out_3[0]);
  xnor xnor_2 (xnor_2_out, RS2[1], shifter_counter_v1_1_out_3[1]);
  xnor xnor_3 (xnor_3_out, RS2[2], shifter_counter_v1_1_out_3[2]);
  xnor xnor_4 (xnor_4_out, RS2[3], shifter_counter_v1_1_out_3[3]);
  xnor xnor_5 (xnor_5_out, RS2[4], shifter_counter_v1_1_out_3[4]);
  Register #(.width(32)) register_1 (
    .D(controlled_buffer_1_out), .Q({register_1_q_2[30:0], register_1_q[1]}), .clk(in_3));  // open: en, clr
  not not_6 (not_6_out, or_4_out);
  and and_1 (and_1_out, xnor_1_out, xnor_2_out);
  and and_2 (and_2_out, and_1_out, and_3_out);
  and and_3 (and_3_out, xnor_3_out, xnor_4_out);
  and and_4 (register_1_q_2[31], register_1_q_2[30], I);
  assign controlled_buffer_1_out = not_7_out ? register_1_q_2 : 32'bz;  // Controlled_Buffer controlled_buffer_2
  not not_7 (not_7_out, Right);
  assign Out = not_8_out ? {register_1_q_2[30:0], register_1_q[1]} : 32'bz;  // Controlled_Buffer controlled_buffer_3
  not not_8 (not_8_out, out_9);
  and and_5 (and_5_out, and_2_out, xnor_5_out);
  not not_9 (not_9_out, and_5_out);
  not not_10 (not_10_out, in_3);
  and v12_2 (v12_2_out, and_5_out, v3_2_out);
  and v12_3 (v12_3_out, v3_2_out, not_9_out);
  assign controlled_buffer_1_out = not_11_out ? {register_1_q_2[29:0], register_1_q[1], 1'b0} : 32'bz;  // Controlled_Buffer controlled_buffer_4
  not not_11 (not_11_out, Left);
  D_Flip_Flop d_ff_2 (.clk(not_10_out), .D(v12_2_out), .Qn(d_ff_2_qn), .reset(Reset));  // open: Q, preset
  and v14_1 (out_9, d_ff_2_qn, d_ff_1_qn);
  and v14_1_2 (out_10, v12_3_out, d_ff_1_qn);

  // Other names for the same wires on the sheet: Clk = in_3; Output_Enable = out_9; Shifter_Busy = out_10;
  //   Shifter_load = SH_LAOD

  // Notes on the sheet:
  //   zero
  //   left
  //   right
  //   zero
  //   Right Shift
  //   equal
  //   Left Shift
endmodule

module SH_TEST (
  input  CLK,
  input  SH_LOAD,
  input  in_3,
  input  [31:0] Input,
  input  [2:0] Funct3,
  input  [4:0] RS2,
  input  I,
  output [31:0] Out
);

  wire and_1_out, and_3_out, and_4_out, not_1_out, or_1_out, OUT_EN, SH_BUSY, SH_EN, SH_LEFT, SH_RIGHT;
  wire [0:0] register_2_q_2;
  wire [5:0] CTR;
  wire [7:0] rom_1_data;
  wire [7:4] register_1_q;
  wire [31:0] controlled_buffer_1_out, register_2_q;

  // Probe on CTR
  ROM #(.addrWidth(17)) rom_1 (.addr({3'b000, CTR, RS2, Funct3}), .data(rom_1_data));
  and and_1 (and_1_out, ~OUT_EN, SH_EN);  // AND_Gate
  shifter_counter_v2 shifter_counter_v2_1 (.out_3(CTR), .Clk(and_1_out), .R(in_3));
  or or_1 (or_1_out, SH_BUSY, SH_LOAD);
  not not_1 (not_1_out, SH_EN);
  and and_2 (SH_EN, CLK, or_1_out);
  Register register_1 (
    .D(rom_1_data), .Q({register_1_q, OUT_EN, SH_BUSY, SH_RIGHT, SH_LEFT}), .clk(not_1_out), .clr(in_3));  // open: en
  // Probe on Input
  assign controlled_buffer_1_out = SH_LOAD ? Input : 32'bz;  // Controlled_Buffer controlled_buffer_1
  // NOT_Gate not_2 is placed but not wired
  and and_3 (and_3_out, SH_RIGHT, ~SH_LOAD);  // AND_Gate
  and and_4 (and_4_out, ~SH_LOAD, SH_LEFT);  // AND_Gate
  Register #(.width(32)) register_2 (
    .D(controlled_buffer_1_out), .Q({register_2_q[30:0], register_2_q_2[0]}), .clk(SH_EN), .clr(in_3));  // open: en
  and and_5 (register_2_q[31], register_2_q[30], I);
  assign Out = OUT_EN ? {register_2_q[30:0], register_2_q_2[0]} : 32'bz;  // Controlled_Buffer controlled_buffer_2
  assign controlled_buffer_1_out = and_3_out ? register_2_q : 32'bz;  // Controlled_Buffer controlled_buffer_3
  assign controlled_buffer_1_out = and_4_out ? {register_2_q[29:0], register_2_q_2[0], 1'b0} : 32'bz;  // Controlled_Buffer controlled_buffer_4

  // Other names for the same wires on the sheet: rst = in_3; Shifter_load = SH_LOAD; X[31:0] = Input

  // Notes on the sheet:
  //   contents of rom_1 (hex, n*v repeats v):
  //   compressed eJzt3DGOI9gNANF8TzFHmGQN3/9kBhaONmjDkGWSvx4mGLxIJKtD6f/+9c9fv//699f/f/z+9ee/
  //   /Q9OWP+2/97f30PL/6m3v4e3/d/29ffwlj/t6e/htv/X/fw93PK3e/l72O3/dx9/D7s83WP68+ve
  //   dv9t87zu7ffePt91X7vvtXm3+/o9r88/7dfu99o+7mU/97Gve9jf/u5hX/exn3vZZ4ev3+/6/Nt8
  //   7Z7X5r3m7ffdPt9r3nbvbfPUPH3/6c/n2R7677bvZ/I3e+l/236/wZ/01P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
  //   Right Shift
  //   Left Shift
endmodule

module shifter_v5 (
  input  I,
  input  [2:0] Funct3,
  input  [4:0] RS2,
  input  CLK,
  input  in_5,
  input  SH_LOAD,
  input  in_7,
  input  [31:0] Input,
  output out_9,
  output out_10,
  output [31:0] Out
);

  wire and_1_out, and_3_out, comparator_1_eq, controlled_inverter_1_out, CTR_EN, decoder_1_out1,
       decoder_1_out5, not_1_out, or_1_out, OUT_EN, SH_EN, SH_LEFT, SH_RIGHT, SH_STORE;
  wire [0:0] register_2_q_2;
  wire [5:0] CTR;
  wire [7:0] rom_1_data;
  wire [7:4] register_1_q;
  wire [31:0] controlled_buffer_2_out, controlled_buffer_5_out, pre_calc, register_2_q, shifter_1_out,
       shifter_2_out, shifter_3_out;

  // Probe on Out
  // Probe on pre_calc
  Decoder #(.enable("false"), .select(3)) decoder_1 (
    .out1(decoder_1_out1), .out5(decoder_1_out5), .sel(Funct3));  // open: out0, out2, out3, out4, out6, out7
  ROM #(.addrWidth(17)) rom_1 (.addr({2'b00, in_5, CTR, RS2, Funct3}), .data(rom_1_data));
  assign pre_calc = decoder_1_out1 ? shifter_1_out : 32'bz;  // Controlled_Buffer controlled_buffer_1
  Shifter #(.width(32)) shifter_1 (.in(Input), .\dist (RS2), .out(shifter_1_out));
  assign controlled_buffer_2_out = not_1_out ? shifter_2_out : 32'bz;  // Controlled_Buffer controlled_buffer_2
  Shifter #(.shift("lr"), .width(32)) shifter_2 (.in(Input), .\dist (RS2), .out(shifter_2_out));
  assign controlled_buffer_2_out = I ? shifter_3_out : 32'bz;  // Controlled_Buffer controlled_buffer_3
  Shifter #(.shift("ar"), .width(32)) shifter_3 (.in(Input), .\dist (RS2), .out(shifter_3_out));
  not not_1 (not_1_out, I);
  assign pre_calc = decoder_1_out5 ? controlled_buffer_2_out : 32'bz;  // Controlled_Buffer controlled_buffer_4
  not not_2 (out_10, OUT_EN);
  shifter_counter_v2 shifter_counter_v2_1 (.out_3(CTR), .Clk(CTR_EN), .R(in_7));
  assign controlled_inverter_1_out = OUT_EN ? ~comparator_1_eq : 1'bz;  // Controlled_Inverter controlled_inverter_1
  Comparator #(.width(32)) comparator_1 (.a(pre_calc), .b(Out), .eq(comparator_1_eq));  // open: gt, lt
  Pull_Resistor pull_resistor_1 (.node(controlled_inverter_1_out));
  or or_1 (or_1_out, out_9, in_5);
  LED led_1 (.in(controlled_inverter_1_out));
  and and_1 (and_1_out, SH_LOAD, CLK);
  or or_2 (SH_STORE, and_1_out, SH_EN);
  and and_2 (SH_EN, CLK, or_1_out);
  and and_3 (and_3_out, or_1_out, ~CLK);  // AND_Gate
  Register register_1 (
    .D(rom_1_data), .Q({register_1_q, OUT_EN, out_9, SH_RIGHT, SH_LEFT}), .clk(CLK));  // open: en, clr
  and and_4 (CTR_EN, and_3_out, ~OUT_EN);  // AND_Gate
  assign controlled_buffer_5_out = SH_LOAD ? Input : 32'bz;  // Controlled_Buffer controlled_buffer_5
  Register #(.width(32)) register_2 (
    .D(controlled_buffer_5_out), .Q({register_2_q[30:0], register_2_q_2[0]}), .clk(SH_STORE));  // open: en, clr
  and and_5 (register_2_q[31], register_2_q[30], I);
  assign Out = OUT_EN ? {register_2_q[30:0], register_2_q_2[0]} : 32'bz;  // Controlled_Buffer controlled_buffer_6
  assign controlled_buffer_5_out = SH_RIGHT ? register_2_q : 32'bz;  // Controlled_Buffer controlled_buffer_7
  assign controlled_buffer_5_out = SH_LEFT ? {register_2_q[29:0], register_2_q_2[0], 1'b0} : 32'bz;  // Controlled_Buffer controlled_buffer_8

  // Other names for the same wires on the sheet: F3[2:0] = Funct3; Shifter_load = in_5; SH_BUSY = out_9; rst = in_7;
  //   SH_LATCH = SH_LOAD; X[31:0] = Input

  // Notes on the sheet:
  //   contents of rom_1 (hex, n*v repeats v):
  //   compressed eJzt27FuYlsMhtGep0hNFRSF8P5PNtEoBaIAocNh2/6XUlwtaa6w/e0STuevy/fx8+Py8fn/7/9/
  //   D58f338+c4T1z/Ztf+8hy496ew+z/Wxf72GWt/b0Hnr71f28h17eu5f3UNvv7uM91PLqHqs/P93V
  //   7l9tnumufu/q83V3t/t2m7e6u9+z+/yrPe1+0/ZxL/u5j33dw/72dw/7uo/93Ms+Ndz9ft3nr+Zu
  //   9+w2bzdXv2/1+aa52r2rzZPm1fdf/fm8tof+te37mbxnL/172+83eEtP/W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
  //   Right Shift
  //   Left Shift
endmodule

module shifter_v6 (
  input  I,
  input  [2:0] Funct3,
  input  [4:0] RS2,
  input  CLK,
  input  in_5,
  input  SH_LOAD,
  input  in_7,
  input  [31:0] Input,
  output out_9,
  output out_10,
  output [31:0] Out,
  output out_12
);

  wire and_1_out, and_2_out, and_3_out, and_6_out, button_1_out, comparator_1_eq, controlled_inverter_1_out,
       CTR_EN, decoder_1_out1, decoder_1_out5, not_2_out, not_3_out, or_1_out, OUT_EN, SH_LEFT, SH_RIGHT,
       SH_STORE, SH_STR_EN;
  wire [0:0] register_2_q_2;
  wire [5:0] CTR;
  wire [7:0] rom_1_data;
  wire [7:3] register_1_q;
  wire [31:0] controlled_buffer_2_out, controlled_buffer_3_out, pre_calc, register_2_q, shifter_1_out,
       shifter_2_out, shifter_3_out;

  // Probe on Out
  // Probe on pre_calc
  ROM #(.addrWidth(17)) rom_1 (
    .addr({2'b00, in_5, CTR, RS2, Funct3}), .data({rom_1_data[7:5], SH_STR_EN, rom_1_data[3:0]}));
  shifter_counter_v2 shifter_counter_v2_1 (.out_3(CTR), .Clk(CTR_EN), .R(in_7));
  not not_1 (out_10, OUT_EN);
  Counter counter_1 (.clk(out_9));  // open: load, D, count, Q, carry, clr
  or or_1 (or_1_out, out_9, in_5);
  and and_1 (and_1_out, SH_LOAD, CLK);
  and and_2 (and_2_out, CLK, SH_STR_EN);
  and and_3 (and_3_out, or_1_out, ~CLK);  // AND_Gate
  Register register_1 (
    .D({rom_1_data[7:5], SH_STR_EN, rom_1_data[3:0]}), .Q({register_1_q, out_9, SH_RIGHT, SH_LEFT}), .clk(CLK));  // open: en, clr
  or or_2 (SH_STORE, and_1_out, and_2_out);
  and and_4 (CTR_EN, and_3_out, ~OUT_EN);  // AND_Gate
  SR_LATCH sr_latch_1 (.nQ(OUT_EN), .S(register_1_q[3]), .R(in_7));  // open: Q
  Decoder #(.enable("false"), .select(3)) decoder_1 (
    .out1(decoder_1_out1), .out5(decoder_1_out5), .sel(Funct3));  // open: out0, out2, out3, out4, out6, out7
  assign pre_calc = decoder_1_out1 ? shifter_1_out : 32'bz;  // Controlled_Buffer controlled_buffer_1
  Shifter #(.width(32)) shifter_1 (.in(Input), .\dist (RS2), .out(shifter_1_out));
  assign controlled_buffer_2_out = not_2_out ? shifter_2_out : 32'bz;  // Controlled_Buffer controlled_buffer_2
  Shifter #(.shift("lr"), .width(32)) shifter_2 (.in(Input), .\dist (RS2), .out(shifter_2_out));
  Shifter #(.shift("ar"), .width(32)) shifter_3 (.in(Input), .\dist (RS2), .out(shifter_3_out));
  not not_2 (not_2_out, I);
  assign controlled_buffer_3_out = SH_LOAD ? Input : 32'bz;  // Controlled_Buffer controlled_buffer_3
  assign pre_calc = decoder_1_out5 ? controlled_buffer_2_out : 32'bz;  // Controlled_Buffer controlled_buffer_4
  assign controlled_buffer_2_out = I ? shifter_3_out : 32'bz;  // Controlled_Buffer controlled_buffer_5
  Comparator #(.width(32)) comparator_1 (.a(pre_calc), .b(Out), .eq(comparator_1_eq));  // open: gt, lt
  Pull_Resistor pull_resistor_1 (.node(comparator_1_eq));
  Register #(.width(32)) register_2 (
    .D(controlled_buffer_3_out), .Q({register_2_q[30:0], register_2_q_2[0]}), .clk(SH_STORE));  // open: en, clr
  Counter counter_2 (.clk(SH_STORE));  // open: load, D, count, Q, carry, clr
  assign controlled_inverter_1_out = OUT_EN ? ~comparator_1_eq : 1'bz;  // Controlled_Inverter controlled_inverter_1
  Pull_Resistor pull_resistor_2 (.node(controlled_inverter_1_out));
  and and_5 (register_2_q[31], register_2_q[30], I);
  assign Out = OUT_EN ? {register_2_q[30:0], register_2_q_2[0]} : 32'bz;  // Controlled_Buffer controlled_buffer_6
  Register #(.width(1)) register_3 (.Q(out_12), .clk(and_6_out), .clr(button_1_out));  // open: D, en
  and and_6 (and_6_out, not_3_out, OUT_EN);
  not not_3 (not_3_out, CLK);
  assign controlled_buffer_3_out = SH_RIGHT ? register_2_q : 32'bz;  // Controlled_Buffer controlled_buffer_7
  Counter counter_3 (.clk(out_12), .clr(button_1_out));  // open: load, D, count, Q, carry
  Button button_1 (.out(button_1_out));
  LED led_1 (.in(out_12));
  assign controlled_buffer_3_out = SH_LEFT ? {register_2_q[29:0], register_2_q_2[0], 1'b0} : 32'bz;  // Controlled_Buffer controlled_buffer_8

  // Other names for the same wires on the sheet: F3[2:0] = Funct3; Shifter_load = in_5; SH_BUSY = out_9; rst = in_7;
  //   SH_LATCH = SH_LOAD; X[31:0] = Input

  // Notes on the sheet:
  //   contents of rom_1 (hex, n*v repeats v):
  //   compressed eJzt3M1KI1EQhuF9rsK1KxtJm/u/shEnYSQMKIf81Ff1MAvph16cU/Uis0jc9vfT8fXt5fTy9vXv
  //   6+fh7eV4ft49j3i2/9nP1/vfLi9sOyE/yHU9aiKr7ay8QWbKShlqIrfrQE0T5V5bV1N/edyO1dRN
  //   nrlRNWVLrf3VOg3J3lb1802WvN3knbirdNhEhzskSs+597xVNZky5Sn3NFM3TxATNAvzMh3TqS3m
  //   ZRYm6OYVZcpMp9zTlN2qi3SYe4c79JC8TeSdeI5U303185G626p1GpK0P+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
  //   Right Shift
  //   Left Shift
endmodule

module Shifter_v20 (
  input  I,
  input  [2:0] Funct3,
  input  [4:0] RS2,
  input  CLK,
  input  SH_LOAD,
  input  in_6,
  input  RF_STORE,
  input  [31:0] Data_IN,
  input  PCE,
  input  RST,
  output OUT_EN,
  output CPU_BUSY,
  output [31:0] Out
);

  wire and_2_out, and_3_out, and_4_out, and_6_out, and_7_out, CTR_EN, not_2_out, or_1_out, or_4_out,
       OUT_EN_t, rst_t, SH_BUSY, SH_LEFT, SH_RIGHT, SH_STORE, SH_STR_EN;
  wire [0:0] register_2_q_2;
  wire [5:0] CTR;
  wire [7:0] rom_1_data;
  wire [7:3] register_1_q;
  wire [31:0] controlled_buffer_1_out, register_2_q;

  ROM #(.addrWidth(17)) rom_1 (
    .addr({1'b0, RST, in_6, CTR, RS2, Funct3}), .data({rom_1_data[7:5], SH_STR_EN, rom_1_data[3:0]}));
  not not_1 (OUT_EN, OUT_EN_t);
  and and_1 (CPU_BUSY, ~RF_STORE, SH_BUSY);  // AND_Gate
  Register register_1 (
    .D({rom_1_data[7:5], SH_STR_EN, rom_1_data[3:0]}), .Q({register_1_q, SH_BUSY, SH_RIGHT, SH_LEFT}),
    .clk(CLK));  // open: en, clr
  shifter_counter_v2 shifter_counter_v2_1 (.out_3(CTR), .Clk(CTR_EN), .R(rst_t));
  and and_2 (and_2_out, SH_LOAD, CLK);
  and and_3 (and_3_out, CLK, SH_STR_EN);
  or or_1 (or_1_out, SH_BUSY, in_6);
  not not_2 (not_2_out, rst_t);
  or or_2 (rst_t, PCE, RST);
  or or_3 (SH_STORE, and_2_out, and_3_out);
  and and_4 (and_4_out, or_1_out, ~CLK);  // AND_Gate
  and and_5 (CTR_EN, and_4_out, ~OUT_EN_t);  // AND_Gate
  and and_6 (and_6_out, rom_1_data[3], not_2_out);
  or or_4 (or_4_out, rst_t, rom_1_data[3]);
  and and_7 (and_7_out, or_4_out, CLK);
  D_Flip_Flop d_ff_1 (.clk(and_7_out), .D(and_6_out), .Q(OUT_EN_t));  // open: Qn, preset, reset
  and and_8 (register_2_q[31], register_2_q[30], I);
  assign controlled_buffer_1_out = SH_RIGHT ? register_2_q : 32'bz;  // Controlled_Buffer controlled_buffer_1
  assign controlled_buffer_1_out = SH_LOAD ? Data_IN : 32'bz;  // Controlled_Buffer controlled_buffer_2
  assign Out = OUT_EN_t ? {register_2_q[30:0], register_2_q_2[0]} : 32'bz;  // Controlled_Buffer controlled_buffer_3
  Register #(.width(32)) register_2 (
    .D(controlled_buffer_1_out), .Q({register_2_q[30:0], register_2_q_2[0]}), .clk(SH_STORE));  // open: en, clr
  assign controlled_buffer_1_out = SH_LEFT ? {register_2_q[29:0], register_2_q_2[0], 1'b0} : 32'bz;  // Controlled_Buffer controlled_buffer_4

  // Other names for the same wires on the sheet: F3[2:0] = Funct3; Shifter_load = in_6; SH_LATCH = SH_LOAD;
  //   X[31:0] = Data_IN

  // Notes on the sheet:
  //   Inputs
  //   Decoder
  //   Outputs
  //   contents of rom_1 (hex, n*v repeats v):
  //   compressed eJzt3M1KI1EQhuF9rsK1KxtJm/u/shEnYSQMKIf81Ff1MAvph16cU/Uis0jc9vfT8fXt5fTy9vXv
  //   6+fh7eV4ft49j3i2/9nP1/vfLi9sOyE/yHU9aiKr7ay8QWbKShlqIrfrQE0T5V5bV1N/edyO1dRN
  //   nrlRNWVLrf3VOg3J3lb1802WvN3knbirdNhEhzskSs+597xVNZky5Sn3NFM3TxATNAvzMh3TqS3m
  //   ZRYm6OYVZcpMp9zTlN2qi3SYe4c79JC8TeSdeI5U303185G626p1GpK0P+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
  //   Logic
  //   SHIFTER
  //   Shifter
  //   Right Shift
  //   Left Shift
endmodule

module VRAM (
);

  wire button_1_out, clock_1_out, counter_1_carry, counter_2_carry, multiplexer_1_out;
  wire [2:0] counter_1_q;
  wire [4:0] counter_2_q;
  wire [7:0] multiplexer_2_out, rom_1_data;
  wire [15:8] counter_3_q;

  Clock clock_1 (.out(clock_1_out));
  Counter #(.max('h7), .width(3)) counter_1 (
    .Q(counter_1_q), .carry(counter_1_carry), .clk(clock_1_out), .clr(button_1_out));  // open: load, D, count
  Button button_1 (.out(button_1_out));
  Counter #(.max('h1f), .width(5)) counter_2 (
    .Q(counter_2_q), .carry(counter_2_carry), .clk(counter_1_carry), .clr(button_1_out));  // open: load, D, count
  ROM #(.addrWidth(16)) rom_1 (.addr({counter_3_q, counter_2_q, counter_1_q}), .data(rom_1_data));
  Counter #(.max('h96)) counter_3 (
    .Q(counter_3_q), .clk(counter_2_carry), .clr(button_1_out));  // open: load, D, count, carry
  Multiplexer #(.enable("false"), .select(3)) multiplexer_1 (
    .in0(rom_1_data[0]), .in1(rom_1_data[1]), .in2(rom_1_data[2]), .in3(rom_1_data[3]), .in4(rom_1_data[4]),
    .in5(rom_1_data[5]), .in6(rom_1_data[6]), .in7(rom_1_data[7]), .out(multiplexer_1_out), .sel(counter_1_q));
  Multiplexer #(.enable("false"), .width(8)) multiplexer_2 (
    .in0(8'h98), .in1(8'hf1), .out(multiplexer_2_out), .sel(multiplexer_1_out));
  // RGB_Video #(.height(256), .width(256)) rgb_video_1: pin names not known; wires that end beside it: button_1_out, clock_1_out, 1'b1, {counter_2_q, counter_1_q}, counter_3_q, multiplexer_2_out

  // Notes on the sheet:
  //   contents of rom_1 (hex, n*v repeats v):
  //   compressed eJzt0smpZTEQBNG9rAgTnqSryRyN/pvQ342GWBckReZ5j3d5h7d5izd5g9fDa7zKK7yPl3mJF3m/
  //   cB/3cg93cxd3cge3h9u4lVu4HzdzEzdyf+E8zuUczuYszuQMTg+ncSqncD5O5iRO5PzCfuzLPuzN
  //   XuzJHuwedmNXdmF/7MxO7Mj+hfVYl3VYm7VYkzVYPazGqqzC+liZlViR9QvzMS/zMDdzMSdzMHuY
  //   jVmZhfkxMzMxI/MXxmNcxmFsxmJMxmD0MBqjMgrjY2RGYkTGL/RHv/RD3/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
endmodule

module GPU_v1 (
  input  [31:0] GPU_Data_in,
  output [14:0] GPU_Adress_out
);

  wire and_1_out, and_2_out, and_3_out, clock_1_out, comparator_1_eq, comparator_2_lt, comparator_3_eq,
       comparator_4_lt, comparator_5_eq, comparator_6_eq, controlled_buffer_1_out, dipswitch_1_p1,
       multiplexer_1_out, or_1_out, or_2_out, or_3_out, or_4_out, RESET_out;
  wire [3:0] multiplexer_2_out;
  wire [4:0] counter_1_q;
  wire [7:0] Y;
  wire [8:0] X;

  // DipSwitch #(.number(2)) dipswitch_1: pin names not known; wires that end beside it: dipswitch_1_p1
  Clock clock_1 (.out(clock_1_out));
  and and_1 (and_1_out, dipswitch_1_p1, clock_1_out);
  Counter #(.max('h1ff), .width(9)) HCounter (.Q(X), .clk(and_1_out), .clr(or_1_out));  // open: load, D, count, carry
  or or_1 (or_1_out, or_4_out, comparator_1_eq);
  Counter VCounter (.Q(Y), .clk(comparator_1_eq), .clr(or_2_out));  // open: load, D, count, carry
  or or_2 (or_2_out, or_4_out, comparator_3_eq);
  // Probe on counter_1_q
  Multiplexer #(.enable("false"), .select(5)) multiplexer_1 (
    .in0(GPU_Data_in[0]), .in1(GPU_Data_in[1]), .in2(GPU_Data_in[2]), .in3(GPU_Data_in[3]),
    .in4(GPU_Data_in[4]), .in5(GPU_Data_in[5]), .in6(GPU_Data_in[6]), .in7(GPU_Data_in[7]),
    .in8(GPU_Data_in[8]), .in9(GPU_Data_in[9]), .in10(GPU_Data_in[10]), .in11(GPU_Data_in[11]),
    .in12(GPU_Data_in[12]), .in13(GPU_Data_in[13]), .in14(GPU_Data_in[14]), .in15(GPU_Data_in[15]),
    .in16(GPU_Data_in[16]), .in17(GPU_Data_in[17]), .in18(GPU_Data_in[18]), .in19(GPU_Data_in[19]),
    .in20(GPU_Data_in[20]), .in21(GPU_Data_in[21]), .in22(GPU_Data_in[22]), .in23(GPU_Data_in[23]),
    .in24(GPU_Data_in[24]), .in25(GPU_Data_in[25]), .in26(GPU_Data_in[26]), .in27(GPU_Data_in[27]),
    .in28(GPU_Data_in[28]), .in29(GPU_Data_in[29]), .in30(GPU_Data_in[30]), .in31(GPU_Data_in[31]),
    .out(multiplexer_1_out), .sel(counter_1_q));
  Comparator #(.mode("unsigned"), .width(9)) comparator_1 (.a(9'h108), .b(X), .eq(comparator_1_eq));  // open: gt, lt
  Comparator #(.mode("unsigned"), .width(9)) comparator_2 (.a(X), .b(9'hc7), .lt(comparator_2_lt));  // open: gt, eq
  Comparator #(.mode("unsigned")) comparator_3 (.a(8'h9d), .b(Y), .eq(comparator_3_eq));  // open: gt, lt
  Comparator #(.mode("unsigned")) comparator_4 (.a(Y), .b(8'h96), .lt(comparator_4_lt));  // open: gt, eq
  Multiplexer #(.enable("false"), .width(4)) multiplexer_2 (
    .in0(4'b1111), .in1(4'b0100), .out(multiplexer_2_out), .sel(multiplexer_1_out));
  and and_2 (and_2_out, comparator_4_lt, comparator_2_lt);
  assign controlled_buffer_1_out = and_1_out ? and_2_out : 1'bz;  // Controlled_Buffer controlled_buffer_1
  Counter #(.max('h1f), .width(5)) counter_1 (
    .Q(counter_1_q), .clk(controlled_buffer_1_out), .clr(or_3_out));  // open: load, D, count, carry
  Pull_Resistor pull_resistor_1 (.node(controlled_buffer_1_out));
  or or_3 (or_3_out, or_4_out, comparator_5_eq);
  Comparator #(.mode("unsigned"), .width(5)) comparator_5 (
    .a(counter_1_q), .b(5'b11110), .eq(comparator_5_eq));  // open: gt, lt
  Counter #(.max('h7fff), .width(15)) counter_2 (
    .Q(GPU_Adress_out), .clk(comparator_5_eq), .clr(or_4_out));  // open: load, D, count, carry
  and and_3 (and_3_out, and_1_out, and_2_out);
  Button RESET (.out(RESET_out));
  Comparator #(.mode("unsigned"), .width(15)) comparator_6 (
    .a(GPU_Adress_out), .b(15'h3e9), .eq(comparator_6_eq));  // open: gt, lt
  or or_4 (or_4_out, RESET_out, comparator_6_eq);
  // RGB_Video #(.height(256), .width(256)) rgb_video_1: pin names not known; wires that end beside it: RESET_out, and_3_out, 1'b1, X[7:0], Y, multiplexer_2_out

  // Notes on the sheet:
  //   9bits
  //   H - Front Porch
  //   V - Front Porch
endmodule

module GPU_v2 (
  input  Clock,
  input  Reset,
  input  [31:0] GPU_Data_in,
  input  [15:0] Colors,
  output [7:0] out_5,
  output [7:0] out_6,
  output out_7,
  output [14:0] GPU_Adress_out,
  output out_9,
  output out_10,
  output [7:0] Data
);

  wire and_1_out, comparator_1_eq, comparator_2_lt, comparator_3_eq, comparator_4_lt, comparator_5_eq,
       comparator_6_eq, controlled_buffer_1_out, multiplexer_1_out, not_1_out, or_1_out, or_2_out, or_3_out,
       or_4_out;
  wire [5:0] counter_1_q;
  wire [8:8] X;

  Counter #(.max('h1ff), .width(9)) HCounter (
    .Q({X[8], out_5}), .clk(Clock), .clr(or_1_out));  // open: load, D, count, carry
  or or_1 (or_1_out, or_4_out, comparator_1_eq);
  Counter VCounter (.Q(out_6), .clk(comparator_1_eq), .clr(or_2_out));  // open: load, D, count, carry
  or or_2 (or_2_out, or_4_out, comparator_3_eq);
  Comparator #(.mode("unsigned"), .width(9)) comparator_1 (
    .a(9'hc8), .b({X[8], out_5}), .eq(comparator_1_eq));  // open: gt, lt
  Comparator #(.mode("unsigned"), .width(9)) comparator_2 (
    .a({X[8], out_5}), .b(9'hc7), .lt(comparator_2_lt));  // open: gt, eq
  Comparator #(.mode("unsigned")) comparator_3 (.a(8'h9d), .b(out_6), .eq(comparator_3_eq));  // open: gt, lt
  Comparator #(.mode("unsigned")) comparator_4 (.a(out_6), .b(8'h96), .lt(comparator_4_lt));  // open: gt, eq
  Multiplexer #(.enable("false"), .select(5)) multiplexer_1 (
    .in0(GPU_Data_in[0]), .in1(GPU_Data_in[1]), .in2(GPU_Data_in[2]), .in3(GPU_Data_in[3]),
    .in4(GPU_Data_in[4]), .in5(GPU_Data_in[5]), .in6(GPU_Data_in[6]), .in7(GPU_Data_in[7]),
    .in8(GPU_Data_in[8]), .in9(GPU_Data_in[9]), .in10(GPU_Data_in[10]), .in11(GPU_Data_in[11]),
    .in12(GPU_Data_in[12]), .in13(GPU_Data_in[13]), .in14(GPU_Data_in[14]), .in15(GPU_Data_in[15]),
    .in16(GPU_Data_in[16]), .in17(GPU_Data_in[17]), .in18(GPU_Data_in[18]), .in19(GPU_Data_in[19]),
    .in20(GPU_Data_in[20]), .in21(GPU_Data_in[21]), .in22(GPU_Data_in[22]), .in23(GPU_Data_in[23]),
    .in24(GPU_Data_in[24]), .in25(GPU_Data_in[25]), .in26(GPU_Data_in[26]), .in27(GPU_Data_in[27]),
    .in28(GPU_Data_in[28]), .in29(GPU_Data_in[29]), .in30(GPU_Data_in[30]), .in31(GPU_Data_in[31]),
    .out(multiplexer_1_out), .sel(counter_1_q[4:0]));
  and and_1 (and_1_out, comparator_4_lt, comparator_2_lt);
  assign controlled_buffer_1_out = Clock ? and_1_out : 1'bz;  // Controlled_Buffer controlled_buffer_1
  not not_1 (not_1_out, multiplexer_1_out);
  assign Data = multiplexer_1_out ? Colors[7:0] : 8'bz;  // Controlled_Buffer controlled_buffer_2
  Counter #(.max('h3f), .width(6)) counter_1 (
    .Q(counter_1_q), .clk(controlled_buffer_1_out), .clr(or_3_out));  // open: load, D, count, carry
  Pull_Resistor pull_resistor_1 (.node(controlled_buffer_1_out));
  or or_3 (or_3_out, or_4_out, comparator_5_eq);
  and and_2 (out_10, Clock, and_1_out);
  assign Data = not_1_out ? Colors[15:8] : 8'bz;  // Controlled_Buffer controlled_buffer_3
  Comparator #(.mode("unsigned"), .width(6)) comparator_5 (
    .a(counter_1_q), .b(6'b100000), .eq(comparator_5_eq));  // open: gt, lt
  Counter #(.max('h7fff), .width(15)) counter_2 (
    .Q(GPU_Adress_out), .clk(comparator_5_eq), .clr(or_4_out));  // open: load, D, count, carry
  or or_4 (or_4_out, comparator_6_eq, Reset);
  Comparator #(.mode("unsigned"), .width(15)) comparator_6 (
    .a(GPU_Adress_out), .b(15'h3aa), .eq(comparator_6_eq));  // open: gt, lt

  assign out_7 = 1'b1;
  assign out_9 = Reset;

  // Other names for the same wires on the sheet: Clk = Clock; X[7:0] = out_5; Y[7:0] = out_6

  // Notes on the sheet:
  //   9bits
  //   H - Front Porch
  //   V - Front Porch
  //   H_Counter
endmodule

module GPU_v3 (
  input  Clock,
  input  Reset,
  input  [31:0] GPU_Data_in,
  input  [31:0] Colors,
  output [7:0] X,
  output [7:0] Y,
  output Rst,
  output Clk,
  output [10:0] GPU_Adress_out,
  output EN,
  output [7:0] Data
);

  wire and_3_out, comparator_1_eq, comparator_2_eq, comparator_3_eq, comparator_4_eq, comparator_5_eq,
       comparator_6_eq, comparator_7_eq, comparator_8_eq, comparator_9_eq, d_ff_1_qn, d_ff_2_qn, d_ff_3_q,
       d_ff_4_q, Displ, or_1_out, or_2_out, or_3_out, or_4_out, or_5_out, or_6_out, or_7_out, or_8_out;
  wire [1:0] multiplexer_1_out;
  wire [4:0] counter_3_q;
  wire [8:8] X_t;
  wire [9:8] Y_t;

  and and_1 (Clk, Clock, Displ);
  // NOT_Gate not_1 is placed but not wired
  Counter #(.max('h1ff), .width(9)) counter_1 (
    .Q({X_t[8], X}), .clk(Clock), .clr(or_1_out));  // open: load, D, count, carry
  or or_1 (or_1_out, comparator_4_eq, Reset);
  Counter #(.max('h3ff), .width(10)) counter_2 (
    .Q({Y_t, Y}), .clk(comparator_4_eq), .clr(or_2_out));  // open: load, D, count, carry
  or or_2 (or_2_out, comparator_8_eq, Reset);
  Comparator #(.width(9)) comparator_1 (.a({X_t[8], X}), .b(9'hc8), .eq(comparator_1_eq));  // open: gt, lt
  Comparator #(.width(9)) comparator_2 (.a({X_t[8], X}), .b(9'hd2), .eq(comparator_2_eq));  // open: gt, lt
  Comparator #(.width(9)) comparator_3 (.a({X_t[8], X}), .b(9'hf2), .eq(comparator_3_eq));  // open: gt, lt
  Comparator #(.width(9)) comparator_4 (.a({X_t[8], X}), .b(9'h108), .eq(comparator_4_eq));  // open: gt, lt
  Comparator #(.width(10)) comparator_5 (.a({Y_t, Y}), .b(10'h96), .eq(comparator_5_eq));  // open: gt, lt
  Comparator #(.width(10)) comparator_6 (.a({Y_t, Y}), .b(10'h97), .eq(comparator_6_eq));  // open: gt, lt
  Comparator #(.width(10)) comparator_7 (.a({Y_t, Y}), .b(10'h98), .eq(comparator_7_eq));  // open: gt, lt
  Comparator #(.width(10)) comparator_8 (.a({Y_t, Y}), .b(10'h9d), .eq(comparator_8_eq));  // open: gt, lt
  D_Flip_Flop d_ff_1 (.clk(Clock), .Qn(d_ff_1_qn), .preset(comparator_2_eq), .reset(or_3_out));  // open: D, Q
  or or_3 (or_3_out, comparator_3_eq, Reset);
  D_Flip_Flop d_ff_2 (.clk(Clock), .Qn(d_ff_2_qn), .preset(comparator_6_eq), .reset(or_4_out));  // open: D, Q
  or or_4 (or_4_out, comparator_7_eq, Reset);
  or or_5 (or_5_out, comparator_8_eq, Reset);
  D_Flip_Flop d_ff_3 (.Q(d_ff_3_q), .preset(or_6_out), .reset(comparator_1_eq));  // open: clk, D, Qn
  or or_6 (or_6_out, comparator_4_eq, Reset);
  D_Flip_Flop d_ff_4 (.Q(d_ff_4_q), .preset(or_5_out), .reset(comparator_5_eq));  // open: clk, D, Qn
  and and_2 (Displ, d_ff_4_q, d_ff_3_q);
  and and_3 (and_3_out, ~Clock, Displ);  // AND_Gate
  LED HSYNC (.in(d_ff_1_qn));
  LED VSYNC (.in(d_ff_2_qn));
  // NOR_Gate nor_1 has open pins: in0=d_ff_4_q, in1=d_ff_3_q, out=open
  Counter #(.max('h1f), .width(5)) counter_3 (
    .Q(counter_3_q), .clk(and_3_out), .clr(or_7_out));  // open: load, D, count, carry
  or or_7 (or_7_out, Reset, comparator_9_eq);
  D_Flip_Flop d_ff_5 ();  // open: clk, D, Q, Qn, preset, reset
  or or_8 (or_8_out, comparator_8_eq, Reset);
  Multiplexer #(.enable("false"), .select(4)) multiplexer_1 (
    .in0(GPU_Data_in[0]), .in1(GPU_Data_in[2]), .in2(GPU_Data_in[4]), .in3(GPU_Data_in[6]),
    .in4(GPU_Data_in[8]), .in5(GPU_Data_in[10]), .in6(GPU_Data_in[12]), .in7(GPU_Data_in[14]),
    .in8(GPU_Data_in[16]), .in9(GPU_Data_in[18]), .in10(GPU_Data_in[20]), .in11(GPU_Data_in[22]),
    .in12(GPU_Data_in[24]), .in13(GPU_Data_in[26]), .in14(GPU_Data_in[28]), .in15(GPU_Data_in[30]),
    .out(multiplexer_1_out[0]), .sel(counter_3_q[3:0]));
  Multiplexer #(.enable("false"), .select(4)) multiplexer_2 (
    .in0(GPU_Data_in[1]), .in1(GPU_Data_in[3]), .in2(GPU_Data_in[5]), .in3(GPU_Data_in[7]),
    .in4(GPU_Data_in[9]), .in5(GPU_Data_in[11]), .in6(GPU_Data_in[13]), .in7(GPU_Data_in[15]),
    .in8(GPU_Data_in[17]), .in9(GPU_Data_in[19]), .in10(GPU_Data_in[21]), .in11(GPU_Data_in[23]),
    .in12(GPU_Data_in[25]), .in13(GPU_Data_in[27]), .in14(GPU_Data_in[29]), .in15(GPU_Data_in[31]),
    .out(multiplexer_1_out[1]), .sel(counter_3_q[3:0]));
  Multiplexer #(.enable("false"), .select(2), .width(8)) multiplexer_3 (
    .in0(Colors[7:0]), .in1(Colors[15:8]), .in2(Colors[23:16]), .in3(Colors[31:24]), .out(Data),
    .sel(multiplexer_1_out));
  Counter #(.max('h7ff), .width(11)) counter_4 (
    .Q(GPU_Adress_out), .clk(comparator_9_eq), .clr(or_8_out));  // open: load, D, count, carry
  Comparator #(.width(5)) comparator_9 (.a(counter_3_q), .b(5'b10000), .eq(comparator_9_eq));  // open: gt, lt
  // NOT_Gate not_2 is placed but not wired

  assign EN = 1'b1;
  assign Rst = Reset;

  // Other names for the same wires on the sheet: Clk_t = Clock; X_t[7:0] = X; Y_t[7:0] = Y

  // Notes on the sheet:
  //   Display
  //   Front Porch
  //   Sync pulse
  //   Back porch
  //   Display
  //   Front Porch
  //   Sync pulse
  //   Back porch
  //   H_Sync
  //   V_Sync
endmodule

module GPU_v4 (
  input  Clock,
  input  Reset,
  input  [31:0] GPU_Data_in,
  input  [31:0] Colors,
  output [7:0] X,
  output [7:0] Y,
  output Rst,
  output Clk,
  output EN,
  output [10:0] GPU_Adress_out,
  output [7:0] Data
);

  wire and_2_out, comparator_1_eq, comparator_2_eq, comparator_3_eq, comparator_4_eq, comparator_5_eq,
       comparator_5_lt, comparator_6_eq, comparator_7_eq, comparator_8_eq, d_ff_1_q, Display, not_3_out,
       or_1_out, or_2_out, or_3_out;
  wire [1:0] multiplexer_1_out;
  wire [3:0] counter_3_q;
  wire [8:8] X_t;
  wire [9:8] Y_t;

  and and_1 (Clk, Clock, Display);
  Counter #(.max('h1ff), .width(9)) counter_1 (
    .Q({X_t[8], X}), .clk(Clock), .clr(or_1_out));  // open: load, D, count, carry
  or or_1 (or_1_out, comparator_4_eq, Reset);
  Counter #(.max('h3ff), .width(10)) counter_2 (
    .Q({Y_t, Y}), .clk(comparator_4_eq), .clr(or_2_out));  // open: load, D, count, carry
  or or_2 (or_2_out, comparator_8_eq, Reset);
  Comparator #(.width(9)) comparator_1 (.a({X_t[8], X}), .b(9'hc8), .eq(comparator_1_eq));  // open: gt, lt
  Comparator #(.width(9)) comparator_2 (.a({X_t[8], X}), .b(9'hd2), .eq(comparator_2_eq));  // open: gt, lt
  Comparator #(.width(9)) comparator_3 (.a({X_t[8], X}), .b(9'hf2), .eq(comparator_3_eq));  // open: gt, lt
  Comparator #(.width(9)) comparator_4 (.a({X_t[8], X}), .b(9'h108), .eq(comparator_4_eq));  // open: gt, lt
  Comparator #(.width(10)) comparator_5 (
    .a({Y_t, Y}), .b(10'h96), .eq(comparator_5_eq), .lt(comparator_5_lt));  // open: gt
  Comparator #(.width(10)) comparator_6 (.a({Y_t, Y}), .b(10'h97), .eq(comparator_6_eq));  // open: gt, lt
  Comparator #(.width(10)) comparator_7 (.a({Y_t, Y}), .b(10'h98), .eq(comparator_7_eq));  // open: gt, lt
  Comparator #(.width(10)) comparator_8 (.a({Y_t, Y}), .b(10'h9d), .eq(comparator_8_eq));  // open: gt, lt
  // NOT_Gate not_1 is placed but not wired
  or or_3 (or_3_out, comparator_4_eq, Reset);
  // NOT_Gate not_2 has open pins: in=comparator_5_eq, out=open
  not not_3 (not_3_out, comparator_8_eq);
  and and_2 (and_2_out, Display, ~Clock);  // AND_Gate
  D_Flip_Flop d_ff_1 (.Q(d_ff_1_q), .preset(or_3_out), .reset(comparator_1_eq));  // open: clk, D, Qn
  Counter #(.max('h7fff), .width(15)) counter_3 (
    .Q({GPU_Adress_out, counter_3_q}), .clk(and_2_out), .clr(Reset));  // open: load, D, count, carry
  LED HSYNC ();  // open: in
  LED VSYNC ();  // open: in
  and and_3 (Display, d_ff_1_q, comparator_5_lt);
  Multiplexer #(.enable("false"), .select(4)) multiplexer_1 (
    .in0(GPU_Data_in[0]), .in1(GPU_Data_in[2]), .in2(GPU_Data_in[4]), .in3(GPU_Data_in[6]),
    .in4(GPU_Data_in[8]), .in5(GPU_Data_in[10]), .in6(GPU_Data_in[12]), .in7(GPU_Data_in[14]),
    .in8(GPU_Data_in[16]), .in9(GPU_Data_in[18]), .in10(GPU_Data_in[20]), .in11(GPU_Data_in[22]),
    .in12(GPU_Data_in[24]), .in13(GPU_Data_in[26]), .in14(GPU_Data_in[28]), .in15(GPU_Data_in[30]),
    .out(multiplexer_1_out[0]), .sel(counter_3_q));
  Multiplexer #(.enable("false"), .select(4)) multiplexer_2 (
    .in0(GPU_Data_in[1]), .in1(GPU_Data_in[3]), .in2(GPU_Data_in[5]), .in3(GPU_Data_in[7]),
    .in4(GPU_Data_in[9]), .in5(GPU_Data_in[11]), .in6(GPU_Data_in[13]), .in7(GPU_Data_in[15]),
    .in8(GPU_Data_in[17]), .in9(GPU_Data_in[19]), .in10(GPU_Data_in[21]), .in11(GPU_Data_in[23]),
    .in12(GPU_Data_in[25]), .in13(GPU_Data_in[27]), .in14(GPU_Data_in[29]), .in15(GPU_Data_in[31]),
    .out(multiplexer_1_out[1]), .sel(counter_3_q));
  Multiplexer #(.select(2), .width(8)) multiplexer_3 (
    .in0(Colors[7:0]), .in1(Colors[15:8]), .in2(Colors[23:16]), .in3(Colors[31:24]), .out(Data),
    .sel(multiplexer_1_out), .en(Display));
  // NOT_Gate not_4 is placed but not wired

  assign EN = 1'b1;
  assign Rst = Reset;

  // Other names for the same wires on the sheet: Clk_t = Clock; X_t[7:0] = X; Y_t[7:0] = Y

  // Notes on the sheet:
  //   Display
  //   Front Porch
  //   Sync pulse
  //   Back porch
  //   Display
  //   Front Porch
  //   Sync pulse
  //   Back porch
  //   !BLANK
  //   H_Sync
  //   V_Sync
endmodule

module GPU_v5 (
  input  Clock,
  input  Reset,
  input  [31:0] GPU_Data_in,
  output [7:0] X,
  output [7:0] Y,
  output Rst,
  output Clk,
  output EN,
  output [10:0] GPU_Adress_out,
  output [7:0] Data
);

  wire comparator_1_eq, comparator_2_eq, comparator_3_eq, comparator_4_eq, comparator_5_eq, comparator_6_eq,
       comparator_7_eq, comparator_8_eq, d_ff_1_q, d_ff_2_q, Display, multiplexer_1_out, multiplexer_2_out,
       multiplexer_3_out, or_1_out, or_2_out, or_3_out, or_4_out;
  wire [8:8] X_t;
  wire [9:8] Y_t;

  and and_1 (Clk, Clock, Display);
  Counter #(.max('h1ff), .width(9)) counter_1 (
    .Q({X_t[8], GPU_Adress_out[2:0], X[4:0]}), .clk(Clock), .clr(or_1_out));  // open: load, D, count, carry
  or or_1 (or_1_out, comparator_4_eq, Reset);
  Counter #(.max('h3ff), .width(10)) counter_2 (
    .Q({Y_t, GPU_Adress_out[10:3]}), .clk(comparator_4_eq), .clr(or_2_out));  // open: load, D, count, carry
  or or_2 (or_2_out, comparator_8_eq, Reset);
  Comparator #(.width(9)) comparator_1 (
    .a({X_t[8], GPU_Adress_out[2:0], X[4:0]}), .b(9'hc8), .eq(comparator_1_eq));  // open: gt, lt
  Comparator #(.width(9)) comparator_2 (
    .a({X_t[8], GPU_Adress_out[2:0], X[4:0]}), .b(9'hd2), .eq(comparator_2_eq));  // open: gt, lt
  Comparator #(.width(9)) comparator_3 (
    .a({X_t[8], GPU_Adress_out[2:0], X[4:0]}), .b(9'hf2), .eq(comparator_3_eq));  // open: gt, lt
  Comparator #(.width(9)) comparator_4 (
    .a({X_t[8], GPU_Adress_out[2:0], X[4:0]}), .b(9'h108), .eq(comparator_4_eq));  // open: gt, lt
  Comparator #(.width(10)) comparator_5 (
    .a({Y_t, GPU_Adress_out[10:3]}), .b(10'h96), .eq(comparator_5_eq));  // open: gt, lt
  Comparator #(.width(10)) comparator_6 (
    .a({Y_t, GPU_Adress_out[10:3]}), .b(10'h97), .eq(comparator_6_eq));  // open: gt, lt
  Comparator #(.width(10)) comparator_7 (
    .a({Y_t, GPU_Adress_out[10:3]}), .b(10'h98), .eq(comparator_7_eq));  // open: gt, lt
  Comparator #(.width(10)) comparator_8 (
    .a({Y_t, GPU_Adress_out[10:3]}), .b(10'h9d), .eq(comparator_8_eq));  // open: gt, lt
  Pull_Resistor pull_resistor_1 (.node(GPU_Data_in));
  // NOT_Gate not_1 is placed but not wired
  or or_3 (or_3_out, comparator_4_eq, Reset);
  or or_4 (or_4_out, comparator_8_eq, Reset);
  D_Flip_Flop d_ff_1 (.Q(d_ff_1_q), .preset(or_3_out), .reset(comparator_1_eq));  // open: clk, D, Qn
  D_Flip_Flop d_ff_2 (.Q(d_ff_2_q), .preset(or_4_out), .reset(comparator_5_eq));  // open: clk, D, Qn
  Multiplexer #(.enable("false"), .select(4)) multiplexer_1 (
    .in0(GPU_Data_in[0]), .in1(GPU_Data_in[1]), .in2(GPU_Data_in[2]), .in3(GPU_Data_in[3]),
    .in4(GPU_Data_in[4]), .in5(GPU_Data_in[5]), .in6(GPU_Data_in[6]), .in7(GPU_Data_in[7]),
    .in8(GPU_Data_in[8]), .in9(GPU_Data_in[9]), .in10(GPU_Data_in[10]), .in11(GPU_Data_in[11]),
    .in12(GPU_Data_in[12]), .in13(GPU_Data_in[13]), .in14(GPU_Data_in[14]), .in15(GPU_Data_in[15]),
    .out(multiplexer_1_out), .sel(X[3:0]));
  Multiplexer #(.enable("false"), .select(4)) multiplexer_2 (
    .in0(GPU_Data_in[16]), .in1(GPU_Data_in[17]), .in2(GPU_Data_in[18]), .in3(GPU_Data_in[19]),
    .in4(GPU_Data_in[20]), .in5(GPU_Data_in[21]), .in6(GPU_Data_in[22]), .in7(GPU_Data_in[23]),
    .in8(GPU_Data_in[24]), .in9(GPU_Data_in[25]), .in10(GPU_Data_in[26]), .in11(GPU_Data_in[27]),
    .in12(GPU_Data_in[28]), .in13(GPU_Data_in[29]), .in14(GPU_Data_in[30]), .in15(GPU_Data_in[31]),
    .out(multiplexer_2_out), .sel(X[3:0]));
  and and_2 (Display, d_ff_1_q, d_ff_2_q);
  Multiplexer multiplexer_3 (
    .in0(multiplexer_1_out), .in1(multiplexer_2_out), .out(multiplexer_3_out), .sel(X[4]), .en(Display));
  Multiplexer #(.enable("false"), .width(8)) multiplexer_4 (
    .in0({8{1'b0}}), .in1({8{1'b1}}), .out(Data), .sel(multiplexer_3_out));
  LED HSYNC ();  // open: in
  LED VSYNC ();  // open: in
  // NOT_Gate not_2 is placed but not wired

  assign EN = 1'b1;
  assign Rst = Reset;
  assign X[7:5] = GPU_Adress_out[2:0];
  assign Y = GPU_Adress_out[10:3];

  // Other names for the same wires on the sheet: X_t[7:0] = {GPU_Adress_out[2:0], X[4:0]};
  //   Y_t[7:0] = GPU_Adress_out[10:3]; Clk_t = Clock

  // Notes on the sheet:
  //   Display
  //   Front Porch
  //   Sync pulse
  //   Back porch
  //   Display
  //   Front Porch
  //   Sync pulse
  //   Back porch
  //   !BLANK
  //   H_Sync
  //   V_Sync
endmodule

module Branch_comparator (
  input  [2:0] Funct3,
  input  [31:0] in_2,
  input  [31:0] in_3,
  output Branch
);

  wire comparator_1_eq, comparator_1_gt, comparator_1_lt, comparator_2_eq, comparator_2_gt, comparator_2_lt,
       not_1_out, or_1_out, or_2_out;

  Comparator #(.width(32)) comparator_1 (
    .a(in_2), .b(in_3), .gt(comparator_1_gt), .eq(comparator_1_eq), .lt(comparator_1_lt));
  or or_1 (or_1_out, comparator_2_gt, comparator_2_eq);
  Comparator #(.mode("unsigned"), .width(32)) comparator_2 (
    .a(in_2), .b(in_3), .gt(comparator_2_gt), .eq(comparator_2_eq), .lt(comparator_2_lt));
  not not_1 (not_1_out, comparator_1_eq);
  or or_2 (or_2_out, comparator_1_eq, comparator_1_gt);
  Multiplexer #(.enable("false"), .select(3)) multiplexer_1 (
    .in0(comparator_1_eq), .in1(not_1_out), .in4(comparator_1_lt), .in5(or_2_out), .in6(comparator_2_lt),
    .in7(or_1_out), .out(Branch), .sel(Funct3));  // open: in2, in3
endmodule

module shifter_counter_v1 (
  input  Clk,
  input  R,
  output [4:0] out_3
);

  wire d_ff_1_qn, d_ff_2_qn, d_ff_3_qn, d_ff_4_qn, d_ff_5_qn;

  D_Flip_Flop d_ff_1 (.clk(Clk), .D(d_ff_1_qn), .Q(out_3[0]), .Qn(d_ff_1_qn), .reset(R));  // open: preset
  D_Flip_Flop d_ff_2 (.clk(d_ff_1_qn), .D(d_ff_2_qn), .Q(out_3[1]), .Qn(d_ff_2_qn), .reset(R));  // open: preset
  D_Flip_Flop d_ff_3 (.clk(d_ff_2_qn), .D(d_ff_3_qn), .Q(out_3[2]), .Qn(d_ff_3_qn), .reset(R));  // open: preset
  D_Flip_Flop d_ff_4 (.clk(d_ff_3_qn), .D(d_ff_4_qn), .Q(out_3[3]), .Qn(d_ff_4_qn), .reset(R));  // open: preset
  D_Flip_Flop d_ff_5 (.clk(d_ff_4_qn), .D(d_ff_5_qn), .Q(out_3[4]), .Qn(d_ff_5_qn), .reset(R));  // open: preset
endmodule

module shifter_counter_v2 (
  input  Clk,
  input  R,
  output [5:0] out_3
);

  wire d_ff_1_qn, d_ff_2_qn, d_ff_3_qn, d_ff_4_qn, d_ff_5_qn, d_ff_6_qn;

  D_Flip_Flop d_ff_1 (.clk(Clk), .D(d_ff_1_qn), .Q(out_3[0]), .Qn(d_ff_1_qn), .reset(R));  // open: preset
  D_Flip_Flop d_ff_2 (.clk(d_ff_1_qn), .D(d_ff_2_qn), .Q(out_3[1]), .Qn(d_ff_2_qn), .reset(R));  // open: preset
  D_Flip_Flop d_ff_3 (.clk(d_ff_2_qn), .D(d_ff_3_qn), .Q(out_3[2]), .Qn(d_ff_3_qn), .reset(R));  // open: preset
  D_Flip_Flop d_ff_4 (.clk(d_ff_3_qn), .D(d_ff_4_qn), .Q(out_3[3]), .Qn(d_ff_4_qn), .reset(R));  // open: preset
  D_Flip_Flop d_ff_5 (.clk(d_ff_4_qn), .D(d_ff_5_qn), .Q(out_3[4]), .Qn(d_ff_5_qn), .reset(R));  // open: preset
  D_Flip_Flop d_ff_6 (.clk(d_ff_5_qn), .D(d_ff_6_qn), .Q(out_3[5]), .Qn(d_ff_6_qn), .reset(R));  // open: preset
endmodule

module AND (
  input  in_1,
  input  in_2,
  output out_3
);

  and and_1 (out_3, in_1, in_2);
endmodule

module IS61C6416AL (
  input  [15:0] ADRESS,
  input  n_LB,
  input  n_WE,
  input  n_OE,
  input  [15:0] in_5,
  input  n_UB,
  output [15:0] out_7
);

  wire and_1_out, and_2_out, and_3_out, and_4_out, not_1_out, not_2_out, not_3_out, not_4_out;
  wire [7:0] ram_1_data, ram_2_data;

  not not_1 (not_1_out, n_LB);
  not not_2 (not_2_out, n_OE);
  not not_3 (not_3_out, n_UB);
  and and_1 (and_1_out, not_2_out, not_1_out);
  and and_2 (and_2_out, n_OE, not_1_out);
  and and_3 (and_3_out, not_2_out, not_3_out);
  and and_4 (and_4_out, n_OE, not_3_out);
  RAM #(.addrWidth(16), .databus("bidir"), .trigger("falling")) ram_1 (
    .addr(ADRESS), .data(ram_1_data));  // open: we, oe, clk
  RAM #(.addrWidth(16), .databus("bidir"), .trigger("falling")) ram_2 (
    .addr(ADRESS), .data(ram_2_data));  // open: we, oe, clk
  assign out_7 = n_OE ? {ram_2_data, ram_1_data} : 16'bz;  // Controlled_Buffer controlled_buffer_1
  assign {ram_2_data, ram_1_data} = not_4_out ? in_5 : 16'bz;  // Controlled_Buffer controlled_buffer_2
  not not_4 (not_4_out, n_OE);
endmodule

module Debugging_unit_v1 (
  input  [6:0] in_1,
  input  [4:0] in_2,
  input  [4:0] in_3,
  input  [4:0] in_4,
  output out_5
);

  wire decoder_1_out0, decoder_1_out1, decoder_1_out2, decoder_1_out3, decoder_1_out4, decoder_1_out5,
       decoder_1_out6, decoder_1_out7, decoder_1_out8, decoder_1_out9, decoder_1_out10, decoder_1_out11,
       decoder_1_out12, decoder_1_out13, decoder_1_out14, decoder_1_out15, decoder_1_out16, decoder_1_out17,
       decoder_1_out18, decoder_1_out19, decoder_1_out20, decoder_1_out21, decoder_1_out22, decoder_1_out23,
       decoder_1_out24, decoder_1_out25, decoder_1_out26, decoder_1_out27, decoder_1_out28, decoder_1_out29,
       decoder_1_out30, decoder_1_out31, decoder_2_out0, decoder_2_out1, decoder_2_out2, decoder_2_out3,
       decoder_2_out4, decoder_2_out5, decoder_2_out6, decoder_2_out7, decoder_2_out8, decoder_2_out9,
       decoder_2_out10, decoder_2_out11, decoder_2_out12, decoder_2_out13, decoder_2_out14, decoder_2_out15,
       decoder_2_out16, decoder_2_out17, decoder_2_out18, decoder_2_out19, decoder_2_out20, decoder_2_out21,
       decoder_2_out22, decoder_2_out23, decoder_2_out24, decoder_2_out25, decoder_2_out26, decoder_2_out27,
       decoder_2_out28, decoder_2_out29, decoder_2_out30, decoder_2_out31, decoder_3_out0, decoder_3_out1,
       decoder_3_out2, decoder_3_out3, decoder_3_out4, decoder_3_out5, decoder_3_out6, decoder_3_out7,
       decoder_3_out8, decoder_3_out9, decoder_3_out10, decoder_3_out11, decoder_3_out12, decoder_3_out13,
       decoder_3_out14, decoder_3_out15, decoder_3_out16, decoder_3_out17, decoder_3_out18, decoder_3_out19,
       decoder_3_out20, decoder_3_out21, decoder_3_out22, decoder_3_out23, decoder_3_out24, decoder_3_out25,
       decoder_3_out26, decoder_3_out27, decoder_3_out28, decoder_3_out29, decoder_3_out30, decoder_3_out31,
       decoder_4_out0, decoder_4_out1, decoder_4_out2, decoder_4_out3, decoder_4_out4, decoder_4_out5,
       decoder_4_out6, decoder_4_out7, decoder_4_out8, decoder_4_out9, decoder_4_out10, decoder_4_out11,
       decoder_4_out12, decoder_4_out13, decoder_4_out14, decoder_4_out15, decoder_4_out16, decoder_4_out17,
       decoder_4_out18, decoder_4_out19, decoder_4_out20, decoder_4_out21, decoder_4_out22, decoder_4_out23,
       decoder_4_out24, decoder_4_out25, decoder_4_out26, decoder_4_out27, decoder_4_out28, decoder_4_out29,
       decoder_4_out30, decoder_4_out31;

  Decoder #(.select(5)) decoder_1 (
    .out0(decoder_1_out0), .out1(decoder_1_out1), .out2(decoder_1_out2), .out3(decoder_1_out3),
    .out4(decoder_1_out4), .out5(decoder_1_out5), .out6(decoder_1_out6), .out7(decoder_1_out7),
    .out8(decoder_1_out8), .out9(decoder_1_out9), .out10(decoder_1_out10), .out11(decoder_1_out11),
    .out12(decoder_1_out12), .out13(decoder_1_out13), .out14(decoder_1_out14), .out15(decoder_1_out15),
    .out16(decoder_1_out16), .out17(decoder_1_out17), .out18(decoder_1_out18), .out19(decoder_1_out19),
    .out20(decoder_1_out20), .out21(decoder_1_out21), .out22(decoder_1_out22), .out23(decoder_1_out23),
    .out24(decoder_1_out24), .out25(decoder_1_out25), .out26(decoder_1_out26), .out27(decoder_1_out27),
    .out28(decoder_1_out28), .out29(decoder_1_out29), .out30(decoder_1_out30), .out31(decoder_1_out31),
    .sel(in_1[5:1]), .en(in_1[0]));
  LED add (.in(decoder_1_out0));
  LED sub (.in(decoder_1_out1));
  LED slr (.in(decoder_1_out2));
  LED sll (.in(decoder_1_out3));
  LED \xor  (.in(decoder_1_out4));
  LED \or  (.in(decoder_1_out5));
  LED sra (.in(decoder_1_out6));
  LED \and  (.in(decoder_1_out7));
  LED lb (.in(decoder_1_out8));
  LED lh (.in(decoder_1_out9));
  LED lw (.in(decoder_1_out10));
  LED lbu (.in(decoder_1_out11));
  LED lhu (.in(decoder_1_out12));
  LED addi (.in(decoder_1_out13));
  LED slli (.in(decoder_1_out14));
  LED xori (.in(decoder_1_out15));
  LED srai (.in(decoder_1_out16));
  LED srli (.in(decoder_1_out17));
  LED ori (.in(decoder_1_out18));
  LED andi (.in(decoder_1_out19));
  LED sb (.in(decoder_1_out20));
  LED sh (.in(decoder_1_out21));
  LED sw (.in(decoder_1_out22));
  LED beq (.in(decoder_1_out23));
  LED bne (.in(decoder_1_out24));
  LED blt (.in(decoder_1_out25));
  LED bge (.in(decoder_1_out26));
  LED bltu (.in(decoder_1_out27));
  LED bgeu (.in(decoder_1_out28));
  LED lui (.in(decoder_1_out29));
  LED jal (.in(decoder_1_out30));
  LED jalr (.in(decoder_1_out31));
  Decoder #(.select(5)) decoder_2 (
    .out0(decoder_2_out0), .out1(decoder_2_out1), .out2(decoder_2_out2), .out3(decoder_2_out3),
    .out4(decoder_2_out4), .out5(decoder_2_out5), .out6(decoder_2_out6), .out7(decoder_2_out7),
    .out8(decoder_2_out8), .out9(decoder_2_out9), .out10(decoder_2_out10), .out11(decoder_2_out11),
    .out12(decoder_2_out12), .out13(decoder_2_out13), .out14(decoder_2_out14), .out15(decoder_2_out15),
    .out16(decoder_2_out16), .out17(decoder_2_out17), .out18(decoder_2_out18), .out19(decoder_2_out19),
    .out20(decoder_2_out20), .out21(decoder_2_out21), .out22(decoder_2_out22), .out23(decoder_2_out23),
    .out24(decoder_2_out24), .out25(decoder_2_out25), .out26(decoder_2_out26), .out27(decoder_2_out27),
    .out28(decoder_2_out28), .out29(decoder_2_out29), .out30(decoder_2_out30), .out31(decoder_2_out31),
    .sel(in_2));  // open: en
  Decoder #(.select(5)) decoder_3 (
    .out0(decoder_3_out0), .out1(decoder_3_out1), .out2(decoder_3_out2), .out3(decoder_3_out3),
    .out4(decoder_3_out4), .out5(decoder_3_out5), .out6(decoder_3_out6), .out7(decoder_3_out7),
    .out8(decoder_3_out8), .out9(decoder_3_out9), .out10(decoder_3_out10), .out11(decoder_3_out11),
    .out12(decoder_3_out12), .out13(decoder_3_out13), .out14(decoder_3_out14), .out15(decoder_3_out15),
    .out16(decoder_3_out16), .out17(decoder_3_out17), .out18(decoder_3_out18), .out19(decoder_3_out19),
    .out20(decoder_3_out20), .out21(decoder_3_out21), .out22(decoder_3_out22), .out23(decoder_3_out23),
    .out24(decoder_3_out24), .out25(decoder_3_out25), .out26(decoder_3_out26), .out27(decoder_3_out27),
    .out28(decoder_3_out28), .out29(decoder_3_out29), .out30(decoder_3_out30), .out31(decoder_3_out31),
    .sel(in_3));  // open: en
  LED zero (.in(decoder_2_out0));
  LED ra (.in(decoder_2_out1));
  LED sp (.in(decoder_2_out2));
  LED gp (.in(decoder_2_out3));
  LED tp (.in(decoder_2_out4));
  LED t0 (.in(decoder_2_out5));
  LED t1 (.in(decoder_2_out6));
  LED t2 (.in(decoder_2_out7));
  LED s0 (.in(decoder_2_out8));
  LED s1 (.in(decoder_2_out9));
  LED a0 (.in(decoder_2_out10));
  LED a1 (.in(decoder_2_out11));
  LED a2 (.in(decoder_2_out12));
  LED a3 (.in(decoder_2_out13));
  LED a4 (.in(decoder_2_out14));
  LED a5 (.in(decoder_2_out15));
  LED a6 (.in(decoder_2_out16));
  LED a7 (.in(decoder_2_out17));
  LED s2 (.in(decoder_2_out18));
  LED s3 (.in(decoder_2_out19));
  LED s4 (.in(decoder_2_out20));
  LED s5 (.in(decoder_2_out21));
  LED s6 (.in(decoder_2_out22));
  LED s7 (.in(decoder_2_out23));
  LED s8 (.in(decoder_2_out24));
  LED s9 (.in(decoder_2_out25));
  LED s10 (.in(decoder_2_out26));
  LED s11 (.in(decoder_2_out27));
  LED t3 (.in(decoder_2_out28));
  LED t4 (.in(decoder_2_out29));
  LED t5 (.in(decoder_2_out30));
  LED t6 (.in(decoder_2_out31));
  LED zero_2 (.in(decoder_3_out0));
  LED ra_2 (.in(decoder_3_out1));
  LED sp_2 (.in(decoder_3_out2));
  LED gp_2 (.in(decoder_3_out3));
  LED tp_2 (.in(decoder_3_out4));
  LED t0_2 (.in(decoder_3_out5));
  LED t1_2 (.in(decoder_3_out6));
  LED t2_2 (.in(decoder_3_out7));
  LED s0_2 (.in(decoder_3_out8));
  LED s1_2 (.in(decoder_3_out9));
  LED a0_2 (.in(decoder_3_out10));
  LED a1_2 (.in(decoder_3_out11));
  LED a2_2 (.in(decoder_3_out12));
  LED a3_2 (.in(decoder_3_out13));
  LED a4_2 (.in(decoder_3_out14));
  LED a5_2 (.in(decoder_3_out15));
  LED a6_2 (.in(decoder_3_out16));
  LED a7_2 (.in(decoder_3_out17));
  LED s2_2 (.in(decoder_3_out18));
  LED s3_2 (.in(decoder_3_out19));
  LED s4_2 (.in(decoder_3_out20));
  LED s5_2 (.in(decoder_3_out21));
  LED s6_2 (.in(decoder_3_out22));
  LED s7_2 (.in(decoder_3_out23));
  LED s8_2 (.in(decoder_3_out24));
  LED s9_2 (.in(decoder_3_out25));
  LED s10_2 (.in(decoder_3_out26));
  LED s11_2 (.in(decoder_3_out27));
  LED t3_2 (.in(decoder_3_out28));
  LED t4_2 (.in(decoder_3_out29));
  LED t5_2 (.in(decoder_3_out30));
  LED t6_2 (.in(decoder_3_out31));
  Decoder #(.select(5)) decoder_4 (
    .out0(decoder_4_out0), .out1(decoder_4_out1), .out2(decoder_4_out2), .out3(decoder_4_out3),
    .out4(decoder_4_out4), .out5(decoder_4_out5), .out6(decoder_4_out6), .out7(decoder_4_out7),
    .out8(decoder_4_out8), .out9(decoder_4_out9), .out10(decoder_4_out10), .out11(decoder_4_out11),
    .out12(decoder_4_out12), .out13(decoder_4_out13), .out14(decoder_4_out14), .out15(decoder_4_out15),
    .out16(decoder_4_out16), .out17(decoder_4_out17), .out18(decoder_4_out18), .out19(decoder_4_out19),
    .out20(decoder_4_out20), .out21(decoder_4_out21), .out22(decoder_4_out22), .out23(decoder_4_out23),
    .out24(decoder_4_out24), .out25(decoder_4_out25), .out26(decoder_4_out26), .out27(decoder_4_out27),
    .out28(decoder_4_out28), .out29(decoder_4_out29), .out30(decoder_4_out30), .out31(decoder_4_out31),
    .sel(in_4));  // open: en
  LED zero_3 (.in(decoder_4_out0));
  LED ra_3 (.in(decoder_4_out1));
  LED sp_3 (.in(decoder_4_out2));
  LED gp_3 (.in(decoder_4_out3));
  LED tp_3 (.in(decoder_4_out4));
  LED t0_3 (.in(decoder_4_out5));
  LED t1_3 (.in(decoder_4_out6));
  LED t2_3 (.in(decoder_4_out7));
  LED s0_3 (.in(decoder_4_out8));
  LED s1_3 (.in(decoder_4_out9));
  LED a0_3 (.in(decoder_4_out10));
  LED a1_3 (.in(decoder_4_out11));
  LED a2_3 (.in(decoder_4_out12));
  LED a3_3 (.in(decoder_4_out13));
  LED a4_3 (.in(decoder_4_out14));
  LED a5_3 (.in(decoder_4_out15));
  LED a6_3 (.in(decoder_4_out16));
  LED a7_3 (.in(decoder_4_out17));
  LED s2_3 (.in(decoder_4_out18));
  LED s3_3 (.in(decoder_4_out19));
  LED s4_3 (.in(decoder_4_out20));
  LED s5_3 (.in(decoder_4_out21));
  LED s6_3 (.in(decoder_4_out22));
  LED s7_3 (.in(decoder_4_out23));
  LED s8_3 (.in(decoder_4_out24));
  LED s9_3 (.in(decoder_4_out25));
  LED s10_3 (.in(decoder_4_out26));
  LED s11_3 (.in(decoder_4_out27));
  LED t3_3 (.in(decoder_4_out28));
  LED t4_3 (.in(decoder_4_out29));
  LED t5_3 (.in(decoder_4_out30));
  LED t6_3 (.in(decoder_4_out31));

  assign out_5 = in_1[0];

  // Other names for the same wires on the sheet: Inter = in_1[0]; Rd[4:0] = in_2; Rs1[4:0] = in_3; Rs2[4:0] = in_4
endmodule

module SR_LATCH (
  input  S,
  input  R,
  output Q,
  output nQ
);

  nor nor_1 (Q, S, nQ);
  nor nor_2 (nQ, Q, R);
endmodule

module Control_unit_v20 (
  input  CLK,
  input  CPU_BUSY,
  input  RST,
  input  [6:0] OP_CODE,
  output [23:0] INS,
  output [2:0] out_6
);

  wire d_ff_1_q, nor_1_out, or_1_out, or_2_out;

  ROM #(.addrWidth(10)) E0 (.addr({OP_CODE, out_6}), .data(INS[7:0]));
  ROM #(.addrWidth(10)) E1 (.addr({OP_CODE, out_6}), .data(INS[15:8]));
  ROM #(.addrWidth(10)) E2 (.addr({OP_CODE, out_6}), .data(INS[23:16]));
  or or_1 (or_1_out, CLK, RST);
  nor nor_1 (nor_1_out, or_1_out, CPU_BUSY);
  D_Flip_Flop d_ff_1 (.clk(or_1_out), .D(INS[12]), .Q(d_ff_1_q), .reset(RST));  // open: Qn, preset
  Counter #(.max('h7), .width(3)) counter_1 (
    .Q(out_6), .clk(nor_1_out), .clr(or_2_out));  // open: load, D, count, carry
  or or_2 (or_2_out, RST, d_ff_1_q);

  // Other names for the same wires on the sheet: OPCODE[6:0] = OP_CODE; Program_counter_enable = INS[12];
  //   Master_Reset = RST

  // Notes on the sheet:
  //   Inputs
  //   Circuit
  //   contents of E0 (hex, n*v repeats v):
  //   24*0 1 127*0 21 21 21 29*0 18 18 94*0 3 159*0 4 4 350*0 8 48 48 29*0 10 10 20 a0 a0 59*0 10 10 8 8
  //   contents of E1 (hex, n*v repeats v):
  //   24*0 40 4 10 125*0 40 48 44 10 28*0 3 7 10 93*0 41 10 126*0 8 8 4 10 10 27*0 3 7 10 349*0 2 12 2
  //   30*0 4 48 48 58 60*0 4 10
  //   contents of E2 (hex, n*v repeats v):
  //   7*0 80 7*0 80 7*0 80 c 14*0 80 7*0 80 7*0 80 7*0 80 7*0 80 7*0 80 7*0 80 7*0 80 7*0 80 7*0 80 7*0 80
  //   7*0 80 7*0 80 7*0 80 7*0 80 6 5 13*0 80 7*0 80 7*0 80 15*0 80 7*0 80 7*0 80 7*0 80 7*0 80 7*0 80 7*0
  //   80 7*0 80 7*0 80 7*0 80 7*0 80 4 14*0 80 7*0 80 7*0 80 7*0 80 7*0 80 7*0 80 7*0 80 7*0 80 7*0 80 7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
  //   Control Unit
  //   Outputs
endmodule
